// Logisim project 小车吃金币.circ as structural Verilog: 16 circuits, main circuit 玩家交互电路
// Kirin-990
module \单周期MIPS_单级中断  (
  input  IR4,
  input  IR5,
  input  IR6,
  input  CLK,
  input  RST,
  input  IR1,
  input  IR2,
  input  IR3,
  output [31:0] \行1 ,
  output [31:0] \行2 ,
  output [31:0] \行3 ,
  output [31:0] \行4 ,
  output [31:0] \行5 ,
  output [31:0] \行6 ,
  output [31:0] \行7 ,
  output [31:0] \行8 ,
  output [31:0] \行9 ,
  output [31:0] \行10 ,
  output [31:0] \行11 ,
  output [31:0] \行12 ,
  output [31:0] \行13 ,
  output [31:0] \行14 ,
  output [31:0] \行15 ,
  output [31:0] \行16 ,
  output Success,
  output [31:0] \行17 ,
  output [31:0] \行18 ,
  output [31:0] \行19 ,
  output [31:0] \行20 ,
  output [31:0] \行21 ,
  output [31:0] \行22 ,
  output [31:0] \行23 ,
  output \警报铃声 ,
  output [31:0] \行24 ,
  output [31:0] \行25 ,
  output [31:0] \行26 ,
  output [31:0] \行27 ,
  output [31:0] \行28 ,
  output [31:0] \行29 ,
  output [31:0] \行30 ,
  output [31:0] \行31 ,
  output [31:0] \行32 
);

  wire and_1_out, and_3_out, and_4_out, and_5_out, and_6_out, and_7_out, and_8_out, and_9_out, and_10_out,
       and_11_out, and_12_out, and_13_out, Beq, BLTZ, Bne, branch, Clear_IR, comparator_1_eq,
       comparator_2_eq, comparator_3_eq, comparator_4_eq, comparator_5_eq, comparator_6_eq, comparator_7_eq,
       comparator_8_lt, comparator_9_eq, comparator_10_eq, comparator_11_eq, comparator_12_lt,
       comparator_13_eq, controlled_buffer_6_out, \CPU中断 , Go, Halt, IE_q, IR1_t, IR2_t, IR3_t, IR4_t, IR5_t,
       IR6_t, IRA, IRB, IRC, J, JAL, JR, LH, LUI, MemWrite, mips_alu_1_equal, multiplexer_1_out, not_1_out,
       not_2_out, not_3_out, not_4_out, not_5_out, not_6_out, or_1_out, or_2_out, or_9_out, or_10_out,
       register_2_q, register_3_q, register_4_q, register_5_q, register_6_q, register_7_q, register_8_q,
       register_9_q, register_10_q, register_11_q, register_12_q, register_13_q, register_14_q,
       register_15_q, register_16_q, register_17_q, RegWrite, SET_IE, SignedExt, SRLV, Syscall, W1, W2, W3,
       W4, W5, W6, \中断按键信号产生电路_1_ir , \单周期硬布线控制器_1_alu_src , \单周期硬布线控制器_1_memtoreg , \单周期硬布线控制器_1_regdst ;
  wire [2:0] register_1_q, \中断号 ;
  wire [3:0] \单周期硬布线控制器_1_alu_op ;
  wire [4:0] multiplexer_3_out, multiplexer_8_out, R1_num, R2_num, W_num;
  wire [9:0] ADDR;
  wire [15:0] controlled_buffer_10_out, \总周期数 ;
  wire [31:0] bit_extender_4_out, BranchAddr, controlled_buffer_1_out, controlled_buffer_8_out,
       controlled_buffer_18_out, Data, EPC, Half, IR, JumpAddr, LedData, MAddr, MDin, multiplexer_6_out,
       multiplexer_7_out, multiplexer_10_out, multiplexer_11_out, multiplexer_12_out, PC, PC_4, R_rs, RDin,
       shifter_1_out, shifter_2_out, shifter_3_out, SignExt, ZeroExt, \入口地址 , \地图备份寄存器堆_32_1_行1 ,
       \地图备份寄存器堆_32_1_行2 , \地图备份寄存器堆_32_1_行3 , \地图备份寄存器堆_32_1_行4 , \地图备份寄存器堆_32_1_行5 , \地图备份寄存器堆_32_1_行6 ,
       \地图备份寄存器堆_32_1_行7 , \地图备份寄存器堆_32_1_行8 , \地图备份寄存器堆_32_1_行9 , \地图备份寄存器堆_32_1_行10 , \地图备份寄存器堆_32_1_行11 ,
       \地图备份寄存器堆_32_1_行12 , \地图备份寄存器堆_32_1_行13 , \地图备份寄存器堆_32_1_行14 , \地图备份寄存器堆_32_1_行15 ,
       \地图备份寄存器堆_32_1_行16 , \地图备份寄存器堆_32_1_行17 , \地图备份寄存器堆_32_1_行18 , \地图备份寄存器堆_32_1_行19 ,
       \地图备份寄存器堆_32_1_行20 , \地图备份寄存器堆_32_1_行21 , \地图备份寄存器堆_32_1_行22 , \地图备份寄存器堆_32_1_行23 ,
       \地图备份寄存器堆_32_1_行24 , \地图备份寄存器堆_32_1_行25 , \地图备份寄存器堆_32_1_行26 , \地图备份寄存器堆_32_1_行27 ,
       \地图备份寄存器堆_32_1_行28 , \地图备份寄存器堆_32_1_行29 , \地图备份寄存器堆_32_1_行30 , \地图备份寄存器堆_32_1_行31 ,
       \地图备份寄存器堆_32_1_行32 ;
  wire [31:1] s3_q;

  Button _1 (.out(IRA));
  Button _2 (.out(IRB));
  Button _3 (.out(IRC));
  Button \u_继续运行  (.out(Go));
  LED #(.active("true")) led_1 (.in(W1));
  LED #(.active("true")) led_2 (.in(W2));
  LED #(.active("true")) led_3 (.in(W3));
  assign controlled_buffer_1_out = branch ? BranchAddr : 32'bz;  // Controlled_Buffer controlled_buffer_1
  assign controlled_buffer_1_out = JR ? R_rs : 32'bz;  // Controlled_Buffer controlled_buffer_2
  or or_1 (or_1_out, J, JAL);
  assign controlled_buffer_1_out = or_1_out ? JumpAddr : 32'bz;  // Controlled_Buffer controlled_buffer_3
  assign controlled_buffer_1_out = and_1_out ? PC_4 : 32'bz;  // Controlled_Buffer controlled_buffer_4
  and and_1 (and_1_out, ~branch, ~JR, ~J, ~JAL, ~Clear_IR);  // AND_Gate
  assign controlled_buffer_1_out = Clear_IR ? EPC : 32'bz;  // Controlled_Buffer controlled_buffer_5
  assign controlled_buffer_6_out = not_5_out ? SET_IE : 1'bz;  // Controlled_Buffer controlled_buffer_6
  assign controlled_buffer_6_out = \CPU中断  ? 1'b0 : 1'bz;  // Controlled_Buffer controlled_buffer_7
  Hex_Digit_Display hex_digit_display_1 (.value(LedData[31:28]));  // open: dp
  Counter #(.width(16), .max('hffff), .ongoal("wrap"), .trigger("rising"), .behavior("old")) counter_1 (
    .count(Halt), .Q(\总周期数 ), .clk(CLK), .clr(RST));  // open: load, D, carry, preset
  assign controlled_buffer_8_out = \CPU中断  ? \入口地址  : 32'bz;  // Controlled_Buffer controlled_buffer_8
  assign controlled_buffer_8_out = not_1_out ? controlled_buffer_1_out : 32'bz;  // Controlled_Buffer controlled_buffer_9
  not not_1 (not_1_out, \CPU中断 );
  Multiplexer #(.select(1), .width(1), .disabled("Z"), .enable("false")) multiplexer_1 (
    .in0(1'b0), .in1(1'b1), .out(multiplexer_1_out), .sel(controlled_buffer_6_out));
  Hex_Digit_Display hex_digit_display_2 (.value(LedData[23:20]));  // open: dp
  Hex_Digit_Display hex_digit_display_3 (.value(LedData[27:24]));  // open: dp
  not not_2 (not_2_out, MAddr[1]);
  Register #(.width(32), .trigger("rising"), .Select("low")) u_PC (
    .D(controlled_buffer_8_out), .en(Halt), .Q(PC), .clk(CLK), .clr(RST));
  not not_3 (not_3_out, multiplexer_1_out);
  or or_2 (or_2_out, Clear_IR, \CPU中断 );
  Hex_Digit_Display hex_digit_display_4 (.value(LedData[19:16]));  // open: dp
  Hex_Digit_Display hex_digit_display_5 (.value(LedData[15:12]));  // open: dp
  assign controlled_buffer_10_out = not_2_out ? Data[15:0] : 16'bz;  // Controlled_Buffer controlled_buffer_10
  assign controlled_buffer_10_out = MAddr[1] ? Data[31:16] : 16'bz;  // Controlled_Buffer controlled_buffer_11
  Adder #(.width(32)) adder_1 (.a(PC), .b(32'h4), .out(PC_4));  // open: cin, cout
  // Probe on W_num
  \中断按键信号产生电路  \u_中断按键信号产生电路_1  (
    .CLK(CLK), .\_1号中断 (IR1_t), .\_1号中断等待指示灯 (W1), .\_2号中断 (IR2_t), .\_2号中断等待指示灯 (W2), .\_3号中断 (IR3_t),
    .\_3号中断等待指示灯 (W3), .\中断号 (\中断号 ), .Clear_IR(Clear_IR), .IR(\中断按键信号产生电路_1_ir ), .RST(RST),
    .target(register_1_q), .\_4号中断 (IR4_t), .\_4号中断等待指示灯 (W4), .\_5号中断等待指示灯 (W5), .\_5号中断 (IR5_t),
    .\_6号中断等待指示灯 (W6), .\_6号中断 (IR6_t));
  and and_2 (\CPU中断 , \中断按键信号产生电路_1_ir , not_4_out);
  not not_4 (not_4_out, IE_q);
  Register #(.width(1), .trigger("rising"), .Select("low")) IE (
    .D(not_3_out), .en(or_2_out), .Q(IE_q), .clk(CLK), .clr(RST));
  not not_5 (not_5_out, \CPU中断 );
  Hex_Digit_Display hex_digit_display_6 (.value(LedData[7:4]));  // open: dp
  Hex_Digit_Display hex_digit_display_7 (.value(LedData[11:8]));  // open: dp
  // Probe on \总周期数 
  assign Half = {{16{controlled_buffer_10_out[15]}}, controlled_buffer_10_out};  // Bit_Extender bit_extender_1
  // Probe on R2_num
  // Probe on R1_num
  Hex_Digit_Display hex_digit_display_8 (.value(LedData[3:0]));  // open: dp
  ROM #(.addrWidth(10), .dataWidth(32), .Select("high")) rom_1 (.addr(PC[11:2]), .data(IR));
  Register #(.width(3), .trigger("rising"), .Select("low")) register_1 (
    .D(\中断号 ), .en(\CPU中断 ), .Q(register_1_q), .clk(CLK), .clr(RST));
  Comparator #(.width(32), .mode("twosComplement")) comparator_1 (
    .a(MDin), .b(32'h64), .eq(comparator_1_eq));  // open: gt, lt
  and and_3 (and_3_out, comparator_1_eq, Syscall);
  or or_3 (IR4_t, IR4, IRC);
  or or_4 (IR1_t, IR1, IRA);
  \单周期硬布线控制器  \u_单周期硬布线控制器_1  (
    .Func(IR[5:0]), .OP(IR[31:26]), .ALU_OP(\单周期硬布线控制器_1_alu_op ), .MemToReg(\单周期硬布线控制器_1_memtoreg ),
    .MemWrite(MemWrite), .ALU_SRC(\单周期硬布线控制器_1_alu_src ), .RegWrite(RegWrite), .SysCALL(Syscall),
    .SignedExt(SignedExt), .RegDst(\单周期硬布线控制器_1_regdst ), .JR(JR), .JMP(J), .Beq(Beq), .JAL(JAL), .Bne(Bne),
    .BLTZ(BLTZ), .LH(LH), .SRLV(SRLV), .SET_IE(SET_IE), .Clear_IR(Clear_IR), .LUI(LUI));
  Multiplexer #(.select(1), .width(5), .disabled("Z"), .enable("false")) multiplexer_2 (
    .in0(IR[25:21]), .in1(5'b00100), .out(R1_num), .sel(Syscall));
  Multiplexer #(.select(1), .width(5), .disabled("Z"), .enable("false")) multiplexer_3 (
    .in0(IR[20:16]), .in1(IR[15:11]), .out(multiplexer_3_out), .sel(\单周期硬布线控制器_1_regdst ));
  assign SignExt = {{16{IR[15]}}, IR[15:0]};  // Bit_Extender bit_extender_2
  assign ZeroExt = {{16{1'b0}}, IR[15:0]};  // Bit_Extender bit_extender_3
  assign bit_extender_4_out = {{6{1'b0}}, IR[25:0]};  // Bit_Extender bit_extender_4
  Register #(.width(1), .trigger("rising"), .Select("low")) register_2 (
    .D(and_3_out), .Q(register_2_q), .clk(CLK), .clr(RST));  // open: en
  Register #(.width(1), .trigger("rising"), .Select("low")) register_3 (
    .D(register_2_q), .Q(register_3_q), .clk(CLK), .clr(RST));  // open: en
  or or_5 (IR5_t, IR5, IRC);
  or or_6 (IR2_t, IR2, IRB);
  Multiplexer #(.select(1), .width(5), .disabled("Z"), .enable("false")) multiplexer_4 (
    .in0(IR[20:16]), .in1(5'b00010), .out(R2_num), .sel(Syscall));
  Multiplexer #(.select(1), .width(5), .disabled("Z"), .enable("false")) multiplexer_5 (
    .in0(multiplexer_3_out), .in1({5{1'b1}}), .out(W_num), .sel(JAL));
  Shifter #(.width(32), .shift("ll")) shifter_1 (.in(SignExt), .\dist (5'b00010), .out(shifter_1_out));
  Shifter #(.width(32), .shift("ll")) shifter_2 (.in(bit_extender_4_out), .\dist (5'b00010), .out(shifter_2_out));
  Comparator #(.width(3), .mode("unsigned")) comparator_2 (
    .a(\中断号 ), .b(3'b001), .eq(comparator_2_eq));  // open: gt, lt
  Comparator #(.width(3), .mode("unsigned")) comparator_3 (
    .a(\中断号 ), .b(3'b010), .eq(comparator_3_eq));  // open: gt, lt
  Comparator #(.width(3), .mode("unsigned")) comparator_4 (
    .a(\中断号 ), .b(3'b011), .eq(comparator_4_eq));  // open: gt, lt
  Comparator #(.width(3), .mode("unsigned")) comparator_5 (
    .a(\中断号 ), .b(3'b100), .eq(comparator_5_eq));  // open: gt, lt
  Comparator #(.width(3), .mode("unsigned")) comparator_6 (
    .a(\中断号 ), .b(3'b101), .eq(comparator_6_eq));  // open: gt, lt
  Comparator #(.width(3), .mode("unsigned")) comparator_7 (
    .a(\中断号 ), .b(3'b110), .eq(comparator_7_eq));  // open: gt, lt
  Register #(.width(1), .trigger("rising"), .Select("low")) register_4 (
    .D(register_3_q), .Q(register_4_q), .clk(CLK), .clr(RST));  // open: en
  Adder #(.width(32)) adder_2 (.a(shifter_1_out), .b(PC_4), .out(BranchAddr));  // open: cin, cout
  Adder #(.width(32)) adder_3 (.a(shifter_2_out), .b({PC_4[31:28], {28{1'b0}}}), .out(JumpAddr));  // open: cin, cout
  assign \入口地址  = comparator_2_eq ? 32'h3450 : 32'bz;  // Controlled_Buffer controlled_buffer_12
  assign \入口地址  = comparator_3_eq ? 32'h33d4 : 32'bz;  // Controlled_Buffer controlled_buffer_13
  assign \入口地址  = comparator_4_eq ? 32'h32f4 : 32'bz;  // Controlled_Buffer controlled_buffer_14
  assign \入口地址  = comparator_5_eq ? 32'h3364 : 32'bz;  // Controlled_Buffer controlled_buffer_15
  assign \入口地址  = comparator_6_eq ? 32'h3004 : 32'bz;  // Controlled_Buffer controlled_buffer_16
  assign \入口地址  = comparator_7_eq ? 32'h3230 : 32'bz;  // Controlled_Buffer controlled_buffer_17
  Register #(.width(1), .trigger("rising"), .Select("low")) register_5 (
    .D(register_4_q), .Q(register_5_q), .clk(CLK), .clr(RST));  // open: en
  or or_7 (IR6_t, IR6, IRC);
  or or_8 (IR3_t, IR3, IRC);
  MIPS_Regifile mips_regifile_1 (
    .Din(RDin), .Clk(CLK), .R1(R_rs), .R2(MDin), .WE(RegWrite), .W_num(W_num), .R1_num(R1_num),
    .R2_num(R2_num));
  Register #(.width(1), .trigger("rising"), .Select("low")) register_6 (
    .D(register_5_q), .Q(register_6_q), .clk(CLK), .clr(RST));  // open: en
  Multiplexer #(.select(1), .width(32), .disabled("Z"), .enable("false")) multiplexer_6 (
    .in0(ZeroExt), .in1(SignExt), .out(multiplexer_6_out), .sel(SignedExt));
  // Probe on RDin
  Pull_Resistor #(.pull(0)) pull_resistor_1 (.node(\入口地址 ));
  Register #(.width(1), .trigger("rising"), .Select("low")) register_7 (
    .D(register_6_q), .Q(register_7_q), .clk(CLK), .clr(RST));  // open: en
  Register #(.width(1), .trigger("rising"), .Select("low")) register_8 (
    .D(register_7_q), .Q(register_8_q), .clk(CLK), .clr(RST));  // open: en
  // Probe on R_rs
  Multiplexer #(.select(1), .width(32), .disabled("Z"), .enable("false")) multiplexer_7 (
    .in0(MDin), .in1(multiplexer_6_out), .out(multiplexer_7_out), .sel(\单周期硬布线控制器_1_alu_src ));
  // Probe on multiplexer_7_out
  Register #(.width(1), .trigger("rising"), .Select("low")) register_9 (
    .D(register_8_q), .Q(register_9_q), .clk(CLK), .clr(RST));  // open: en
  Comparator #(.width(32), .mode("twosComplement")) comparator_8 (
    .a(R_rs), .b({32{1'b0}}), .lt(comparator_8_lt));  // open: gt, eq
  MIPS_ALU mips_alu_1 (
    .X(R_rs), .Y(multiplexer_7_out), .AluOP(\单周期硬布线控制器_1_alu_op ), .Equal(mips_alu_1_equal),
    .Result({MAddr[31:12], ADDR, MAddr[1:0]}), .shamt(multiplexer_8_out));  // open: Result_2
  Multiplexer #(.select(1), .width(5), .disabled("Z"), .enable("false")) multiplexer_8 (
    .in0(IR[10:6]), .in1(R_rs[4:0]), .out(multiplexer_8_out), .sel(SRLV));
  // Probe on multiplexer_8_out
  or or_9 (or_9_out, J, JAL);
  Register #(.width(1), .trigger("rising"), .Select("low")) register_10 (
    .D(register_9_q), .Q(register_10_q), .clk(CLK), .clr(RST));  // open: en
  and and_4 (and_4_out, BLTZ, comparator_8_lt);
  and and_5 (and_5_out, Beq, mips_alu_1_equal);
  and and_6 (and_6_out, Bne, ~mips_alu_1_equal);  // AND_Gate
  // Probe on {MAddr[31:12], ADDR, MAddr[1:0]}
  // Probe on MDin
  or or_10 (or_10_out, J, JAL);
  and and_7 (and_7_out, ~branch, ~JR, ~or_9_out);  // AND_Gate
  Register #(.width(1), .trigger("rising"), .Select("low")) register_11 (
    .D(register_10_q), .Q(register_11_q), .clk(CLK), .clr(RST));  // open: en
  Register #(.width(1), .trigger("rising"), .Select("low")) register_12 (
    .D(register_11_q), .Q(register_12_q), .clk(CLK), .clr(RST));  // open: en
  // Probe on ADDR
  Multiplexer #(.select(1), .width(32), .disabled("Z"), .enable("false")) multiplexer_9 (
    .in0(multiplexer_10_out), .in1(shifter_3_out), .out(RDin), .sel(LUI));
  Shifter #(.width(32), .shift("ll")) shifter_3 (.in(ZeroExt), .\dist (5'b10000), .out(shifter_3_out));
  assign controlled_buffer_18_out = branch ? BranchAddr : 32'bz;  // Controlled_Buffer controlled_buffer_18
  assign controlled_buffer_18_out = JR ? R_rs : 32'bz;  // Controlled_Buffer controlled_buffer_19
  assign controlled_buffer_18_out = or_10_out ? JumpAddr : 32'bz;  // Controlled_Buffer controlled_buffer_20
  assign controlled_buffer_18_out = and_7_out ? PC_4 : 32'bz;  // Controlled_Buffer controlled_buffer_21
  Register #(.width(1), .trigger("rising"), .Select("low")) register_13 (
    .D(register_12_q), .Q(register_13_q), .clk(CLK), .clr(RST));  // open: en
  or or_11 (branch, and_4_out, and_5_out, and_6_out);
  Multiplexer #(.select(1), .width(32), .disabled("Z"), .enable("false")) multiplexer_10 (
    .in0(multiplexer_12_out), .in1(PC_4), .out(multiplexer_10_out), .sel(JAL));
  Register #(.width(32), .trigger("rising"), .Select("low")) u_EPC (
    .D(controlled_buffer_18_out), .en(\CPU中断 ), .Q(EPC), .clk(CLK), .clr(RST));
  Register #(.width(1), .trigger("rising"), .Select("low")) register_14 (
    .D(register_13_q), .Q(register_14_q), .clk(CLK), .clr(RST));  // open: en
  RAM #(.addrWidth(10), .dataWidth(32), .bus("separate"), .Select("high")) ram_1 (
    .addr(ADDR), .din(MDin), .data(Data), .str(MemWrite), .clk(CLK), .clr(RST));  // open: sel, ld
  Register #(.width(1), .trigger("rising"), .Select("low")) register_15 (
    .D(register_14_q), .Q(register_15_q), .clk(CLK), .clr(RST));  // open: en
  Register #(.width(1), .trigger("rising"), .Select("low")) register_16 (
    .D(register_15_q), .Q(register_16_q), .clk(CLK), .clr(RST));  // open: en
  Multiplexer #(.select(1), .width(32), .disabled("Z"), .enable("false")) multiplexer_11 (
    .in0({MAddr[31:12], ADDR, MAddr[1:0]}), .in1(Data), .out(multiplexer_11_out), .sel(\单周期硬布线控制器_1_memtoreg ));
  Register #(.width(1), .trigger("rising"), .Select("low")) register_17 (
    .D(register_16_q), .Q(register_17_q), .clk(CLK), .clr(RST));  // open: en
  Comparator #(.width(32), .mode("twosComplement")) comparator_9 (
    .a(32'h64), .b(MDin), .eq(comparator_9_eq));  // open: gt, lt
  Comparator #(.width(32), .mode("twosComplement")) comparator_10 (
    .a(MDin), .b(32'h22), .eq(comparator_10_eq));  // open: gt, lt
  Multiplexer #(.select(1), .width(32), .disabled("Z"), .enable("false")) multiplexer_12 (
    .in0(multiplexer_11_out), .in1(Half), .out(multiplexer_12_out), .sel(LH));
  or or_12 (\警报铃声 , register_2_q, register_3_q, register_4_q, register_5_q, register_6_q, register_7_q, register_8_q, register_9_q, register_10_q, register_11_q, register_12_q, register_13_q, register_14_q, register_15_q, register_16_q, register_17_q);
  and and_8 (and_8_out, ~comparator_9_eq, ~comparator_10_eq);  // AND_Gate
  and and_9 (and_9_out, comparator_10_eq, Syscall);
  Comparator #(.width(5), .mode("unsigned")) comparator_11 (
    .a(W_num), .b(5'b10011), .eq(comparator_11_eq));  // open: gt, lt
  and and_10 (and_10_out, Syscall, and_8_out);
  not not_6 (not_6_out, and_10_out);
  Register #(.width(32), .trigger("rising"), .Select("low")) register_18 (
    .D(R_rs), .en(and_9_out), .Q(LedData), .clk(CLK), .clr(RST));
  and and_11 (and_11_out, comparator_11_eq, RegWrite);
  or or_13 (Halt, Go, not_6_out);
  Register #(.width(32), .trigger("rising"), .Select("low")) s3 (
    .D(RDin), .en(and_11_out), .Q({s3_q, Success}), .clk(CLK), .clr(RST));
  Comparator #(.width(10), .mode("unsigned")) comparator_12 (
    .a(ADDR), .b(10'h20), .lt(comparator_12_lt));  // open: gt, eq
  and and_12 (and_12_out, MemWrite, comparator_12_lt);
  Comparator #(.width(32), .mode("twosComplement")) comparator_13 (
    .a(MDin), .b(32'h22), .eq(comparator_13_eq));  // open: gt, lt
  \地图备份寄存器堆_32  \u_地图备份寄存器堆_32_1  (
    .\写使能 (and_12_out), .Addr(ADDR), .CLK(CLK), .Data(MDin), .\行1 (\地图备份寄存器堆_32_1_行1 ),
    .\行9 (\地图备份寄存器堆_32_1_行9 ), .\行17 (\地图备份寄存器堆_32_1_行17 ), .\行25 (\地图备份寄存器堆_32_1_行25 ),
    .\行2 (\地图备份寄存器堆_32_1_行2 ), .\行10 (\地图备份寄存器堆_32_1_行10 ), .\行18 (\地图备份寄存器堆_32_1_行18 ),
    .\行26 (\地图备份寄存器堆_32_1_行26 ), .\行3 (\地图备份寄存器堆_32_1_行3 ), .\行11 (\地图备份寄存器堆_32_1_行11 ),
    .\行19 (\地图备份寄存器堆_32_1_行19 ), .\行27 (\地图备份寄存器堆_32_1_行27 ), .\行4 (\地图备份寄存器堆_32_1_行4 ),
    .\行12 (\地图备份寄存器堆_32_1_行12 ), .\行20 (\地图备份寄存器堆_32_1_行20 ), .\行28 (\地图备份寄存器堆_32_1_行28 ),
    .\行5 (\地图备份寄存器堆_32_1_行5 ), .\行13 (\地图备份寄存器堆_32_1_行13 ), .\行21 (\地图备份寄存器堆_32_1_行21 ),
    .\行29 (\地图备份寄存器堆_32_1_行29 ), .\行6 (\地图备份寄存器堆_32_1_行6 ), .\行14 (\地图备份寄存器堆_32_1_行14 ),
    .\行22 (\地图备份寄存器堆_32_1_行22 ), .\行30 (\地图备份寄存器堆_32_1_行30 ), .\行7 (\地图备份寄存器堆_32_1_行7 ),
    .\行15 (\地图备份寄存器堆_32_1_行15 ), .\行23 (\地图备份寄存器堆_32_1_行23 ), .\行31 (\地图备份寄存器堆_32_1_行31 ),
    .\行8 (\地图备份寄存器堆_32_1_行8 ), .\行16 (\地图备份寄存器堆_32_1_行16 ), .\行24 (\地图备份寄存器堆_32_1_行24 ),
    .\行32 (\地图备份寄存器堆_32_1_行32 ), .RST(RST));
  and and_13 (and_13_out, comparator_13_eq, Syscall);
  \点阵显示寄存器堆_32  \u_点阵显示寄存器堆_32_1  (
    .\写使能 (and_13_out), ._1(\地图备份寄存器堆_32_1_行1 ), ._2(\地图备份寄存器堆_32_1_行2 ), ._3(\地图备份寄存器堆_32_1_行3 ),
    ._4(\地图备份寄存器堆_32_1_行4 ), ._5(\地图备份寄存器堆_32_1_行5 ), ._6(\地图备份寄存器堆_32_1_行6 ), ._7(\地图备份寄存器堆_32_1_行7 ),
    ._8(\地图备份寄存器堆_32_1_行8 ), ._9(\地图备份寄存器堆_32_1_行9 ), ._10(\地图备份寄存器堆_32_1_行10 ), ._11(\地图备份寄存器堆_32_1_行11 ),
    ._12(\地图备份寄存器堆_32_1_行12 ), ._13(\地图备份寄存器堆_32_1_行13 ), ._14(\地图备份寄存器堆_32_1_行14 ),
    ._15(\地图备份寄存器堆_32_1_行15 ), ._16(\地图备份寄存器堆_32_1_行16 ), ._17(\地图备份寄存器堆_32_1_行17 ),
    ._18(\地图备份寄存器堆_32_1_行18 ), ._19(\地图备份寄存器堆_32_1_行19 ), ._20(\地图备份寄存器堆_32_1_行20 ),
    ._21(\地图备份寄存器堆_32_1_行21 ), ._22(\地图备份寄存器堆_32_1_行22 ), ._23(\地图备份寄存器堆_32_1_行23 ),
    ._24(\地图备份寄存器堆_32_1_行24 ), ._25(\地图备份寄存器堆_32_1_行25 ), ._26(\地图备份寄存器堆_32_1_行26 ),
    ._27(\地图备份寄存器堆_32_1_行27 ), ._28(\地图备份寄存器堆_32_1_行28 ), ._29(\地图备份寄存器堆_32_1_行29 ),
    ._30(\地图备份寄存器堆_32_1_行30 ), ._31(\地图备份寄存器堆_32_1_行31 ), ._32(\地图备份寄存器堆_32_1_行32 ), .CLK(CLK), ._1_2(\行1 ),
    ._2_2(\行2 ), ._3_2(\行3 ), ._4_2(\行4 ), ._5_2(\行5 ), ._6_2(\行6 ), ._7_2(\行7 ), ._8_2(\行8 ), ._9_2(\行9 ),
    ._10_2(\行10 ), ._11_2(\行11 ), ._12_2(\行12 ), ._13_2(\行13 ), ._14_2(\行14 ), ._15_2(\行15 ), ._16_2(\行16 ),
    ._17_2(\行17 ), ._18_2(\行18 ), ._19_2(\行19 ), ._20_2(\行20 ), ._21_2(\行21 ), ._22_2(\行22 ), ._23_2(\行23 ),
    ._24_2(\行24 ), ._25_2(\行25 ), ._26_2(\行26 ), ._27_2(\行27 ), ._28_2(\行28 ), ._29_2(\行29 ), ._30_2(\行30 ),
    ._31_2(\行31 ), ._32_2(\行32 ), .RST(RST));

  // Other names for the same wires on the sheet: Low[15:0] = Data[15:0]; High[15:0] = Data[31:16]; MAddr[11:2] = ADDR;
  //   v0[31:0] = MDin

  // Notes on the sheet:
  //   中断源
  //   中断等待指示
  //   总复位信号应将除ROM以外所有存储组件全部清零
  //   数码管输出
  //   数码管输出应该用寄存器锁存，否则显示数据只能一闪而过
  //   指令存储器
  //   指令字
  //   contents of rom_1 (hex, n*v repeats v):
  //   8000d36 1640002d 3c010000 3421ffff 1c020 18c400 3718ffff ac180000 ac180004 ac180078 ac18007c
  //   20180000 ac180008 ac18000c ac180010 ac180014 ac180018 ac18001c ac180020 ac180024 ac180028 ac18002c
  //   ac180030 ac180034 ac180038 ac18003c ac180044 ac180048 ac18004c ac180050 ac180054 ac180058 ac18005c
  //   ac180060 ac180064 ac180068 ac18006c ac180070 ac180074 3c010000 34218000 1c020 18c400 ac180040
  //   20020022 c 20120001 42000018 1640008b 20180000 18c400 37180001 ac180000 20186efd 18c400 37187ffc
  //   ac180004 20181100 18c400 37188002 ac180008 3c010000 3421d35f 1c020 18c400 37181fda ac18000c 20181480
  //   18c400 37182022 ac180010 2018527f 18c400 3718c72a ac180014 20184880 18c400 371808aa ac180018
  //   2018447d 18c400 3718f28c ac18001c 20185280 18c400 37180252 ac180020 2018249f 18c400 3718dc2a
  //   ac180024 201850a0 18c400 371822a2 ac180028 20183c99 18c400 37182aac ac18002c 20184282 18c400
  //   3718aaa0 ac180030 2018527a 18c400 3718a91a ac180034 3c010000 3421a884 1c020 18c400 37180822 ac180038
  //   2018072d 18c400 3718d4a4 ac18003c 20184022 18c400 3718224a ac180040 2018535a 18c400 3718498a
  //   ac180044 20185484 18c400 37189022 ac180048 20185562 18c400 3718abdc ac18004c 20185548 18c400
  //   37180402 ac180050 20185152 18c400 3718a972 ac180054 20182e25 18c400 37181484 ac180058 20184092
  //   18c400 371822b8 ac18005c 20183929 18c400 37184484 ac180060 201804a2 18c400 37185112 ac180064
  //   3c010000 3421d698 1c020 18c400 371892aa ac180068 20181283 18c400 37181442 ac18006c 2018727c 18c400
  //   3718695c ac180070 20180a00 18c400 37188110 ac180074 3c010000 3421e9ff 1c020 18c400 37181ee4 ac180078
  //   20180800 18c400 37186002 ac18007c 20020022 c 20120001 42000018 1240001a 3c018000 34210000 10300072
  //   108040 ae300000 20020022 c 42000018 20090001 2095020 1495804 116080 8d8d0000 1ab7024 15c00066
  //   2098020 1ab6825 b5842 1ab6826 ad8d0000 20020022 c 200f001f 120f0001 42000018 122f0095 42000018
  //   1240001a 20010001 10300057 108042 ae300000 20020022 c 42000018 20090001 2098022 1ab6825 b5840
  //   1ab6826 ad8d0000 20020022 c 2098022 1ab6825 b5840 1ab6826 ad8d0000 20020022 c 200f001f 120f0001
  //   42000018 122f0079 42000018 1240001d 20010074 1031003b ae200000 22310004 ae300000 20020022 c 42000018
  //   20090001 1495804 2297820 f6080 8d8d0000 1ab7024 15c0002e 2298820 1ab6825 ad8d0000 20010004 1816022
  //   8d8d0000 1ab6826 ad8d0000 20020022 c 200f001f 120f0001 42000018 122f005a 42000018 1240001d 20010008
  //   1031001c ae200000 20090004 2298822 ae300000 20020022 c 42000018 20090001 1495804 2297822 f6080
  //   8d8d0000 1ab7024 15c0000e 2298822 1ab6825 ad8d0000 218c0004 8d8d0000 1ab6826 ad8d0000 20020022 c
  //   200f001f 120f0001 42000018 122f003b 42000018 20020064 c 42000018 3c010000 34218000 18020 108400
  //   20110040 3c010000 3421ffff 1c020 18c400 3718ffff ac180000 ac180004 ac180078 ac18007c 20180000
  //   ac180008 ac18000c ac180010 ac180014 ac180018 ac18001c ac180020 ac180024 ac180028 ac18002c ac180030
  //   ac180034 ac180038 ac18003c ac180044 ac180048 ac18004c ac180050 ac180054 ac180058 ac18005c ac180060
  //   ac180064 ac180068 ac18006c ac180070 ac180074 3c010000 34218000 1c020 18c400 ac180040 20020022 c 5*0
  //   8000d67 20130001 20187577 18c400 37187772 ac180034 20184544 18c400 37185442 ac180038 20187544 18c400
  //   37187772 ac18003c 20181544 18c400 37184110 ac180040 20187777 18c400 37187772 ac180044 20020022 c
  //   8000d67
  //   JMP
  //   JR
  //   OP
  //   OP
  //   Func
  //   Func
  //   rs
  //   rt
  //   rd
  //   shamt
  //   Beq
  //   Bne
  //   MemToReg
  //   MemWrite
  //   AluOP
  //   AluSrcB
  //   RegWrite
  //   JAL
  //   RegDst
  //   Syscall
  //   为方便自动评测，需要输出PC，IR，寄存器堆写如数据RDin
  //   RAM写使能MemWrite、RAM写入数据MDin等信号
endmodule

module \金币移动  (
  input  IR4,
  input  [15:0] \金币速度 ,
  input  IR5,
  input  IR6,
  input  RST,
  input  CLK,
  input  IR1,
  input  IR2,
  input  IR3,
  output [31:0] \行1 ,
  output [31:0] \行2 ,
  output [31:0] \行3 ,
  output [31:0] \行4 ,
  output [31:0] \行5 ,
  output [31:0] \行6 ,
  output [31:0] \行7 ,
  output [31:0] \行8 ,
  output [31:0] \行9 ,
  output [31:0] \行10 ,
  output [31:0] \行11 ,
  output [31:0] \行12 ,
  output [31:0] \行13 ,
  output [31:0] \行14 ,
  output [31:0] \行15 ,
  output [31:0] \行16 ,
  output Success,
  output [31:0] \行17 ,
  output [31:0] \行18 ,
  output [31:0] \行19 ,
  output [31:0] \行20 ,
  output [31:0] \行21 ,
  output [31:0] \行22 ,
  output [31:0] \行23 ,
  output \警报铃声 ,
  output [31:0] \行24 ,
  output [31:0] \行25 ,
  output [31:0] \行26 ,
  output [31:0] \行27 ,
  output [31:0] \行28 ,
  output [31:0] \行29 ,
  output [31:0] \行30 ,
  output [31:0] \行31 ,
  output [31:0] \行32 
);

  wire and_1_out, and_3_out, and_4_out, and_5_out, and_6_out, and_7_out, and_8_out, and_9_out, and_10_out,
       and_11_out, and_12_out, and_13_out, Beq, BLTZ, Bne, branch, Clear_IR, CLK_t, comparator_1_eq,
       comparator_2_eq, comparator_3_eq, comparator_4_eq, comparator_5_eq, comparator_6_eq, comparator_7_eq,
       comparator_8_lt, comparator_9_eq, comparator_10_eq, comparator_11_eq, comparator_12_lt,
       comparator_13_eq, controlled_buffer_6_out, \CPU中断 , Go, Halt, IE_q, IR1_t, IR2_t, IR3_t, IR4_t, IR5_t,
       IR6_t, IRA, IRB, IRC, J, JAL, JR, LH, LUI, MemWrite, mips_alu_1_equal, multiplexer_1_out, not_1_out,
       not_2_out, not_3_out, not_4_out, not_5_out, not_6_out, or_1_out, or_2_out, or_9_out, or_10_out,
       register_2_q, register_3_q, register_4_q, register_5_q, register_6_q, register_7_q, register_8_q,
       register_9_q, register_10_q, register_11_q, register_12_q, register_13_q, register_14_q,
       register_15_q, register_16_q, register_17_q, RegWrite, SET_IE, SignedExt, SRLV, Syscall, W1, W2, W3,
       W4, W5, W6, \中断按键信号产生电路_1_ir , \单周期硬布线控制器_1_alu_src , \单周期硬布线控制器_1_memtoreg , \单周期硬布线控制器_1_regdst ;
  wire [2:0] register_1_q, \中断号 ;
  wire [3:0] \单周期硬布线控制器_1_alu_op ;
  wire [4:0] multiplexer_3_out, multiplexer_8_out, R1_num, R2_num, W_num;
  wire [9:0] ADDR;
  wire [15:0] controlled_buffer_10_out, \总周期数 ;
  wire [31:0] bit_extender_4_out, BranchAddr, controlled_buffer_1_out, controlled_buffer_8_out,
       controlled_buffer_18_out, Data, EPC, Half, IR, JumpAddr, LedData, MAddr, MDin, multiplexer_6_out,
       multiplexer_7_out, multiplexer_10_out, multiplexer_11_out, multiplexer_12_out, PC, PC_4, R_rs, RDin,
       shifter_1_out, shifter_2_out, shifter_3_out, SignExt, ZeroExt, \入口地址 , \地图备份寄存器堆_32_1_行1 ,
       \地图备份寄存器堆_32_1_行2 , \地图备份寄存器堆_32_1_行3 , \地图备份寄存器堆_32_1_行4 , \地图备份寄存器堆_32_1_行5 , \地图备份寄存器堆_32_1_行6 ,
       \地图备份寄存器堆_32_1_行7 , \地图备份寄存器堆_32_1_行8 , \地图备份寄存器堆_32_1_行9 , \地图备份寄存器堆_32_1_行10 , \地图备份寄存器堆_32_1_行11 ,
       \地图备份寄存器堆_32_1_行12 , \地图备份寄存器堆_32_1_行13 , \地图备份寄存器堆_32_1_行14 , \地图备份寄存器堆_32_1_行15 ,
       \地图备份寄存器堆_32_1_行16 , \地图备份寄存器堆_32_1_行17 , \地图备份寄存器堆_32_1_行18 , \地图备份寄存器堆_32_1_行19 ,
       \地图备份寄存器堆_32_1_行20 , \地图备份寄存器堆_32_1_行21 , \地图备份寄存器堆_32_1_行22 , \地图备份寄存器堆_32_1_行23 ,
       \地图备份寄存器堆_32_1_行24 , \地图备份寄存器堆_32_1_行25 , \地图备份寄存器堆_32_1_行26 , \地图备份寄存器堆_32_1_行27 ,
       \地图备份寄存器堆_32_1_行28 , \地图备份寄存器堆_32_1_行29 , \地图备份寄存器堆_32_1_行30 , \地图备份寄存器堆_32_1_行31 ,
       \地图备份寄存器堆_32_1_行32 ;
  wire [31:1] s3_q;

  Button _1 (.out(IRA));
  Button _2 (.out(IRB));
  Button _3 (.out(IRC));
  Button \u_继续运行  (.out(Go));
  LED #(.active("true")) led_1 (.in(W1));
  LED #(.active("true")) led_2 (.in(W2));
  LED #(.active("true")) led_3 (.in(W3));
  assign controlled_buffer_1_out = branch ? BranchAddr : 32'bz;  // Controlled_Buffer controlled_buffer_1
  assign controlled_buffer_1_out = JR ? R_rs : 32'bz;  // Controlled_Buffer controlled_buffer_2
  or or_1 (or_1_out, J, JAL);
  assign controlled_buffer_1_out = or_1_out ? JumpAddr : 32'bz;  // Controlled_Buffer controlled_buffer_3
  assign controlled_buffer_1_out = and_1_out ? PC_4 : 32'bz;  // Controlled_Buffer controlled_buffer_4
  and and_1 (and_1_out, ~branch, ~JR, ~J, ~JAL, ~Clear_IR);  // AND_Gate
  assign controlled_buffer_1_out = Clear_IR ? EPC : 32'bz;  // Controlled_Buffer controlled_buffer_5
  assign controlled_buffer_6_out = not_5_out ? SET_IE : 1'bz;  // Controlled_Buffer controlled_buffer_6
  assign controlled_buffer_6_out = \CPU中断  ? 1'b0 : 1'bz;  // Controlled_Buffer controlled_buffer_7
  Hex_Digit_Display hex_digit_display_1 (.value(LedData[31:28]));  // open: dp
  Counter #(.width(16), .max('hffff), .ongoal("wrap"), .trigger("rising"), .behavior("old")) counter_1 (
    .count(Halt), .Q(\总周期数 ), .clk(CLK_t), .clr(RST));  // open: load, D, carry, preset
  assign controlled_buffer_8_out = \CPU中断  ? \入口地址  : 32'bz;  // Controlled_Buffer controlled_buffer_8
  assign controlled_buffer_8_out = not_1_out ? controlled_buffer_1_out : 32'bz;  // Controlled_Buffer controlled_buffer_9
  not not_1 (not_1_out, \CPU中断 );
  Hex_Digit_Display hex_digit_display_2 (.value(LedData[27:24]));  // open: dp
  Hex_Digit_Display hex_digit_display_3 (.value(LedData[23:20]));  // open: dp
  Register #(.width(32), .trigger("rising"), .Select("low")) u_PC (
    .D(controlled_buffer_8_out), .en(Halt), .Q(PC), .clk(CLK_t), .clr(RST));
  Multiplexer #(.select(1), .width(1), .disabled("Z"), .enable("false")) multiplexer_1 (
    .in0(1'b0), .in1(1'b1), .out(multiplexer_1_out), .sel(controlled_buffer_6_out));
  not not_2 (not_2_out, multiplexer_1_out);
  or or_2 (or_2_out, Clear_IR, \CPU中断 );
  Hex_Digit_Display hex_digit_display_4 (.value(LedData[15:12]));  // open: dp
  Hex_Digit_Display hex_digit_display_5 (.value(LedData[19:16]));  // open: dp
  not not_3 (not_3_out, MAddr[1]);
  assign controlled_buffer_10_out = not_3_out ? Data[15:0] : 16'bz;  // Controlled_Buffer controlled_buffer_10
  assign controlled_buffer_10_out = MAddr[1] ? Data[31:16] : 16'bz;  // Controlled_Buffer controlled_buffer_11
  Adder #(.width(32)) adder_1 (.a(PC), .b(32'h4), .out(PC_4));  // open: cin, cout
  // Probe on W_num
  \中断按键信号产生电路  \u_中断按键信号产生电路_1  (
    .CLK(CLK_t), .\_1号中断 (IR1_t), .\_1号中断等待指示灯 (W1), .\_2号中断 (IR2_t), .\_2号中断等待指示灯 (W2), .\_3号中断 (IR3_t),
    .\_3号中断等待指示灯 (W3), .\中断号 (\中断号 ), .Clear_IR(Clear_IR), .IR(\中断按键信号产生电路_1_ir ), .RST(RST),
    .target(register_1_q), .\_4号中断 (IR4_t), .\_4号中断等待指示灯 (W4), .\_5号中断等待指示灯 (W5), .\_5号中断 (IR5_t),
    .\_6号中断等待指示灯 (W6), .\_6号中断 (IR6_t));
  not not_4 (not_4_out, IE_q);
  Register #(.width(1), .trigger("rising"), .Select("low")) IE (
    .D(not_2_out), .en(or_2_out), .Q(IE_q), .clk(CLK_t), .clr(RST));
  not not_5 (not_5_out, \CPU中断 );
  Hex_Digit_Display hex_digit_display_6 (.value(LedData[11:8]));  // open: dp
  Hex_Digit_Display hex_digit_display_7 (.value(LedData[7:4]));  // open: dp
  assign Half = {{16{controlled_buffer_10_out[15]}}, controlled_buffer_10_out};  // Bit_Extender bit_extender_1
  // Probe on R1_num
  // Probe on R2_num
  and and_2 (\CPU中断 , \中断按键信号产生电路_1_ir , not_4_out);
  Hex_Digit_Display hex_digit_display_8 (.value(LedData[3:0]));  // open: dp
  // Probe on \总周期数 
  ROM #(.addrWidth(10), .dataWidth(32), .Select("high")) rom_1 (.addr(PC[11:2]), .data(IR));
  Register #(.width(3), .trigger("rising"), .Select("low")) register_1 (
    .D(\中断号 ), .en(\CPU中断 ), .Q(register_1_q), .clk(CLK_t), .clr(RST));
  Comparator #(.width(32), .mode("twosComplement")) comparator_1 (
    .a(MDin), .b(32'h64), .eq(comparator_1_eq));  // open: gt, lt
  and and_3 (and_3_out, comparator_1_eq, Syscall);
  or or_3 (IR4_t, IR4, IRC);
  or or_4 (IR1_t, IR1, IRA);
  \单周期硬布线控制器  \u_单周期硬布线控制器_1  (
    .Func(IR[5:0]), .OP(IR[31:26]), .ALU_OP(\单周期硬布线控制器_1_alu_op ), .MemToReg(\单周期硬布线控制器_1_memtoreg ),
    .MemWrite(MemWrite), .ALU_SRC(\单周期硬布线控制器_1_alu_src ), .RegWrite(RegWrite), .SysCALL(Syscall),
    .SignedExt(SignedExt), .RegDst(\单周期硬布线控制器_1_regdst ), .JR(JR), .JMP(J), .Beq(Beq), .JAL(JAL), .Bne(Bne),
    .BLTZ(BLTZ), .LH(LH), .SRLV(SRLV), .SET_IE(SET_IE), .Clear_IR(Clear_IR), .LUI(LUI));
  Multiplexer #(.select(1), .width(5), .disabled("Z"), .enable("false")) multiplexer_2 (
    .in0(IR[25:21]), .in1(5'b00100), .out(R1_num), .sel(Syscall));
  Multiplexer #(.select(1), .width(5), .disabled("Z"), .enable("false")) multiplexer_3 (
    .in0(IR[20:16]), .in1(IR[15:11]), .out(multiplexer_3_out), .sel(\单周期硬布线控制器_1_regdst ));
  assign SignExt = {{16{IR[15]}}, IR[15:0]};  // Bit_Extender bit_extender_2
  assign ZeroExt = {{16{1'b0}}, IR[15:0]};  // Bit_Extender bit_extender_3
  assign bit_extender_4_out = {{6{1'b0}}, IR[25:0]};  // Bit_Extender bit_extender_4
  Register #(.width(1), .trigger("rising"), .Select("low")) register_2 (
    .D(and_3_out), .Q(register_2_q), .clk(CLK_t), .clr(RST));  // open: en
  or or_5 (IR5_t, IR5, IRC);
  or or_6 (IR2_t, IR2, IRB);
  Multiplexer #(.select(1), .width(5), .disabled("Z"), .enable("false")) multiplexer_4 (
    .in0(IR[20:16]), .in1(5'b00010), .out(R2_num), .sel(Syscall));
  Multiplexer #(.select(1), .width(5), .disabled("Z"), .enable("false")) multiplexer_5 (
    .in0(multiplexer_3_out), .in1({5{1'b1}}), .out(W_num), .sel(JAL));
  Shifter #(.width(32), .shift("ll")) shifter_1 (.in(SignExt), .\dist (5'b00010), .out(shifter_1_out));
  Shifter #(.width(32), .shift("ll")) shifter_2 (.in(bit_extender_4_out), .\dist (5'b00010), .out(shifter_2_out));
  Register #(.width(1), .trigger("rising"), .Select("low")) register_3 (
    .D(register_4_q), .Q(register_3_q), .clk(CLK_t), .clr(RST));  // open: en
  Register #(.width(1), .trigger("rising"), .Select("low")) register_4 (
    .D(register_2_q), .Q(register_4_q), .clk(CLK_t), .clr(RST));  // open: en
  Adder #(.width(32)) adder_2 (.a(shifter_1_out), .b(PC_4), .out(BranchAddr));  // open: cin, cout
  Adder #(.width(32)) adder_3 (.a(shifter_2_out), .b({PC_4[31:28], {28{1'b0}}}), .out(JumpAddr));  // open: cin, cout
  Comparator #(.width(3), .mode("unsigned")) comparator_2 (
    .a(\中断号 ), .b(3'b001), .eq(comparator_2_eq));  // open: gt, lt
  assign \入口地址  = comparator_2_eq ? 32'h3450 : 32'bz;  // Controlled_Buffer controlled_buffer_12
  Comparator #(.width(3), .mode("unsigned")) comparator_3 (
    .a(\中断号 ), .b(3'b010), .eq(comparator_3_eq));  // open: gt, lt
  assign \入口地址  = comparator_3_eq ? 32'h33d4 : 32'bz;  // Controlled_Buffer controlled_buffer_13
  Comparator #(.width(3), .mode("unsigned")) comparator_4 (
    .a(\中断号 ), .b(3'b011), .eq(comparator_4_eq));  // open: gt, lt
  assign \入口地址  = comparator_4_eq ? 32'h32f4 : 32'bz;  // Controlled_Buffer controlled_buffer_14
  Comparator #(.width(3), .mode("unsigned")) comparator_5 (
    .a(\中断号 ), .b(3'b100), .eq(comparator_5_eq));  // open: gt, lt
  assign \入口地址  = comparator_5_eq ? 32'h3364 : 32'bz;  // Controlled_Buffer controlled_buffer_15
  Comparator #(.width(3), .mode("unsigned")) comparator_6 (
    .a(\中断号 ), .b(3'b101), .eq(comparator_6_eq));  // open: gt, lt
  assign \入口地址  = comparator_6_eq ? 32'h3004 : 32'bz;  // Controlled_Buffer controlled_buffer_16
  Comparator #(.width(3), .mode("unsigned")) comparator_7 (
    .a(\中断号 ), .b(3'b110), .eq(comparator_7_eq));  // open: gt, lt
  assign \入口地址  = comparator_7_eq ? 32'h3230 : 32'bz;  // Controlled_Buffer controlled_buffer_17
  Register #(.width(1), .trigger("rising"), .Select("low")) register_5 (
    .D(register_3_q), .Q(register_5_q), .clk(CLK_t), .clr(RST));  // open: en
  or or_7 (IR6_t, IR6, IRC);
  or or_8 (IR3_t, IR3, IRC);
  MIPS_Regifile mips_regifile_1 (
    .Din(RDin), .Clk(CLK_t), .R1(R_rs), .R2(MDin), .WE(RegWrite), .W_num(W_num), .R1_num(R1_num),
    .R2_num(R2_num));
  Register #(.width(1), .trigger("rising"), .Select("low")) register_6 (
    .D(register_5_q), .Q(register_6_q), .clk(CLK_t), .clr(RST));  // open: en
  Multiplexer #(.select(1), .width(32), .disabled("Z"), .enable("false")) multiplexer_6 (
    .in0(ZeroExt), .in1(SignExt), .out(multiplexer_6_out), .sel(SignedExt));
  // Probe on RDin
  Pull_Resistor #(.pull(0)) pull_resistor_1 (.node(\入口地址 ));
  Register #(.width(1), .trigger("rising"), .Select("low")) register_7 (
    .D(register_6_q), .Q(register_7_q), .clk(CLK_t), .clr(RST));  // open: en
  Register #(.width(1), .trigger("rising"), .Select("low")) register_8 (
    .D(register_7_q), .Q(register_8_q), .clk(CLK_t), .clr(RST));  // open: en
  \频率转换  \u_频率转换_1  (.\延缓倍数 (\金币速度 ), .\原CLK (CLK), .RST(RST), .\后CLK (CLK_t));
  // Probe on R_rs
  Multiplexer #(.select(1), .width(32), .disabled("Z"), .enable("false")) multiplexer_7 (
    .in0(MDin), .in1(multiplexer_6_out), .out(multiplexer_7_out), .sel(\单周期硬布线控制器_1_alu_src ));
  // Probe on multiplexer_7_out
  Register #(.width(1), .trigger("rising"), .Select("low")) register_9 (
    .D(register_8_q), .Q(register_9_q), .clk(CLK_t), .clr(RST));  // open: en
  Comparator #(.width(32), .mode("twosComplement")) comparator_8 (
    .a(R_rs), .b({32{1'b0}}), .lt(comparator_8_lt));  // open: gt, eq
  Multiplexer #(.select(1), .width(5), .disabled("Z"), .enable("false")) multiplexer_8 (
    .in0(IR[10:6]), .in1(R_rs[4:0]), .out(multiplexer_8_out), .sel(SRLV));
  // Probe on multiplexer_8_out
  Register #(.width(1), .trigger("rising"), .Select("low")) register_10 (
    .D(register_9_q), .Q(register_10_q), .clk(CLK_t), .clr(RST));  // open: en
  and and_4 (and_4_out, BLTZ, comparator_8_lt);
  and and_5 (and_5_out, Beq, mips_alu_1_equal);
  and and_6 (and_6_out, Bne, ~mips_alu_1_equal);  // AND_Gate
  // Probe on {MAddr[31:12], ADDR, MAddr[1:0]}
  MIPS_ALU mips_alu_1 (
    .X(R_rs), .Y(multiplexer_7_out), .AluOP(\单周期硬布线控制器_1_alu_op ), .Equal(mips_alu_1_equal),
    .Result({MAddr[31:12], ADDR, MAddr[1:0]}), .shamt(multiplexer_8_out));  // open: Result_2
  // Probe on MDin
  or or_9 (or_9_out, J, JAL);
  and and_7 (and_7_out, ~branch, ~JR, ~or_10_out);  // AND_Gate
  or or_10 (or_10_out, J, JAL);
  Register #(.width(1), .trigger("rising"), .Select("low")) register_11 (
    .D(register_10_q), .Q(register_11_q), .clk(CLK_t), .clr(RST));  // open: en
  Register #(.width(1), .trigger("rising"), .Select("low")) register_12 (
    .D(register_11_q), .Q(register_12_q), .clk(CLK_t), .clr(RST));  // open: en
  // Probe on ADDR
  Multiplexer #(.select(1), .width(32), .disabled("Z"), .enable("false")) multiplexer_9 (
    .in0(multiplexer_10_out), .in1(shifter_3_out), .out(RDin), .sel(LUI));
  Shifter #(.width(32), .shift("ll")) shifter_3 (.in(ZeroExt), .\dist (5'b10000), .out(shifter_3_out));
  assign controlled_buffer_18_out = branch ? BranchAddr : 32'bz;  // Controlled_Buffer controlled_buffer_18
  assign controlled_buffer_18_out = JR ? R_rs : 32'bz;  // Controlled_Buffer controlled_buffer_19
  assign controlled_buffer_18_out = or_9_out ? JumpAddr : 32'bz;  // Controlled_Buffer controlled_buffer_20
  assign controlled_buffer_18_out = and_7_out ? PC_4 : 32'bz;  // Controlled_Buffer controlled_buffer_21
  Register #(.width(1), .trigger("rising"), .Select("low")) register_13 (
    .D(register_12_q), .Q(register_13_q), .clk(CLK_t), .clr(RST));  // open: en
  or or_11 (branch, and_4_out, and_5_out, and_6_out);
  Multiplexer #(.select(1), .width(32), .disabled("Z"), .enable("false")) multiplexer_10 (
    .in0(multiplexer_12_out), .in1(PC_4), .out(multiplexer_10_out), .sel(JAL));
  Register #(.width(1), .trigger("rising"), .Select("low")) register_14 (
    .D(register_13_q), .Q(register_14_q), .clk(CLK_t), .clr(RST));  // open: en
  RAM #(.addrWidth(10), .dataWidth(32), .bus("separate"), .Select("high")) ram_1 (
    .addr(ADDR), .din(MDin), .data(Data), .str(MemWrite), .clk(CLK_t), .clr(RST));  // open: sel, ld
  Register #(.width(32), .trigger("rising"), .Select("low")) u_EPC (
    .D(controlled_buffer_18_out), .en(\CPU中断 ), .Q(EPC), .clk(CLK_t), .clr(RST));
  Register #(.width(1), .trigger("rising"), .Select("low")) register_15 (
    .D(register_14_q), .Q(register_15_q), .clk(CLK_t), .clr(RST));  // open: en
  Multiplexer #(.select(1), .width(32), .disabled("Z"), .enable("false")) multiplexer_11 (
    .in0({MAddr[31:12], ADDR, MAddr[1:0]}), .in1(Data), .out(multiplexer_11_out), .sel(\单周期硬布线控制器_1_memtoreg ));
  Register #(.width(1), .trigger("rising"), .Select("low")) register_16 (
    .D(register_15_q), .Q(register_16_q), .clk(CLK_t), .clr(RST));  // open: en
  Register #(.width(1), .trigger("rising"), .Select("low")) register_17 (
    .D(register_16_q), .Q(register_17_q), .clk(CLK_t), .clr(RST));  // open: en
  Comparator #(.width(32), .mode("twosComplement")) comparator_9 (
    .a(32'h64), .b(MDin), .eq(comparator_9_eq));  // open: gt, lt
  Comparator #(.width(32), .mode("twosComplement")) comparator_10 (
    .a(MDin), .b(32'h22), .eq(comparator_10_eq));  // open: gt, lt
  Multiplexer #(.select(1), .width(32), .disabled("Z"), .enable("false")) multiplexer_12 (
    .in0(multiplexer_11_out), .in1(Half), .out(multiplexer_12_out), .sel(LH));
  or or_12 (\警报铃声 , register_2_q, register_4_q, register_3_q, register_5_q, register_6_q, register_7_q, register_8_q, register_9_q, register_10_q, register_11_q, register_12_q, register_13_q, register_14_q, register_15_q, register_16_q, register_17_q);
  and and_8 (and_8_out, ~comparator_9_eq, ~comparator_10_eq);  // AND_Gate
  and and_9 (and_9_out, comparator_10_eq, Syscall);
  Comparator #(.width(5), .mode("unsigned")) comparator_11 (
    .a(W_num), .b(5'b10011), .eq(comparator_11_eq));  // open: gt, lt
  and and_10 (and_10_out, Syscall, and_8_out);
  not not_6 (not_6_out, and_10_out);
  Register #(.width(32), .trigger("rising"), .Select("low")) register_18 (
    .D(R_rs), .en(and_9_out), .Q(LedData), .clk(CLK_t), .clr(RST));
  and and_11 (and_11_out, comparator_11_eq, RegWrite);
  or or_13 (Halt, Go, not_6_out);
  Register #(.width(32), .trigger("rising"), .Select("low")) s3 (
    .D(RDin), .en(and_11_out), .Q({s3_q, Success}), .clk(CLK_t), .clr(RST));
  Comparator #(.width(10), .mode("unsigned")) comparator_12 (
    .a(ADDR), .b(10'h20), .lt(comparator_12_lt));  // open: gt, eq
  and and_12 (and_12_out, MemWrite, comparator_12_lt);
  Comparator #(.width(32), .mode("twosComplement")) comparator_13 (
    .a(MDin), .b(32'h22), .eq(comparator_13_eq));  // open: gt, lt
  and and_13 (and_13_out, comparator_13_eq, Syscall);
  \地图备份寄存器堆_32  \u_地图备份寄存器堆_32_1  (
    .\写使能 (and_12_out), .Addr(ADDR), .CLK(CLK_t), .Data(MDin), .\行1 (\地图备份寄存器堆_32_1_行1 ),
    .\行9 (\地图备份寄存器堆_32_1_行9 ), .\行17 (\地图备份寄存器堆_32_1_行17 ), .\行25 (\地图备份寄存器堆_32_1_行25 ),
    .\行2 (\地图备份寄存器堆_32_1_行2 ), .\行10 (\地图备份寄存器堆_32_1_行10 ), .\行18 (\地图备份寄存器堆_32_1_行18 ),
    .\行26 (\地图备份寄存器堆_32_1_行26 ), .\行3 (\地图备份寄存器堆_32_1_行3 ), .\行11 (\地图备份寄存器堆_32_1_行11 ),
    .\行19 (\地图备份寄存器堆_32_1_行19 ), .\行27 (\地图备份寄存器堆_32_1_行27 ), .\行4 (\地图备份寄存器堆_32_1_行4 ),
    .\行12 (\地图备份寄存器堆_32_1_行12 ), .\行20 (\地图备份寄存器堆_32_1_行20 ), .\行28 (\地图备份寄存器堆_32_1_行28 ),
    .\行5 (\地图备份寄存器堆_32_1_行5 ), .\行13 (\地图备份寄存器堆_32_1_行13 ), .\行21 (\地图备份寄存器堆_32_1_行21 ),
    .\行29 (\地图备份寄存器堆_32_1_行29 ), .\行6 (\地图备份寄存器堆_32_1_行6 ), .\行14 (\地图备份寄存器堆_32_1_行14 ),
    .\行22 (\地图备份寄存器堆_32_1_行22 ), .\行30 (\地图备份寄存器堆_32_1_行30 ), .\行7 (\地图备份寄存器堆_32_1_行7 ),
    .\行15 (\地图备份寄存器堆_32_1_行15 ), .\行23 (\地图备份寄存器堆_32_1_行23 ), .\行31 (\地图备份寄存器堆_32_1_行31 ),
    .\行8 (\地图备份寄存器堆_32_1_行8 ), .\行16 (\地图备份寄存器堆_32_1_行16 ), .\行24 (\地图备份寄存器堆_32_1_行24 ),
    .\行32 (\地图备份寄存器堆_32_1_行32 ), .RST(RST));
  \点阵显示寄存器堆_32  \u_点阵显示寄存器堆_32_1  (
    .\写使能 (and_13_out), ._1(\地图备份寄存器堆_32_1_行1 ), ._2(\地图备份寄存器堆_32_1_行2 ), ._3(\地图备份寄存器堆_32_1_行3 ),
    ._4(\地图备份寄存器堆_32_1_行4 ), ._5(\地图备份寄存器堆_32_1_行5 ), ._6(\地图备份寄存器堆_32_1_行6 ), ._7(\地图备份寄存器堆_32_1_行7 ),
    ._8(\地图备份寄存器堆_32_1_行8 ), ._9(\地图备份寄存器堆_32_1_行9 ), ._10(\地图备份寄存器堆_32_1_行10 ), ._11(\地图备份寄存器堆_32_1_行11 ),
    ._12(\地图备份寄存器堆_32_1_行12 ), ._13(\地图备份寄存器堆_32_1_行13 ), ._14(\地图备份寄存器堆_32_1_行14 ),
    ._15(\地图备份寄存器堆_32_1_行15 ), ._16(\地图备份寄存器堆_32_1_行16 ), ._17(\地图备份寄存器堆_32_1_行17 ),
    ._18(\地图备份寄存器堆_32_1_行18 ), ._19(\地图备份寄存器堆_32_1_行19 ), ._20(\地图备份寄存器堆_32_1_行20 ),
    ._21(\地图备份寄存器堆_32_1_行21 ), ._22(\地图备份寄存器堆_32_1_行22 ), ._23(\地图备份寄存器堆_32_1_行23 ),
    ._24(\地图备份寄存器堆_32_1_行24 ), ._25(\地图备份寄存器堆_32_1_行25 ), ._26(\地图备份寄存器堆_32_1_行26 ),
    ._27(\地图备份寄存器堆_32_1_行27 ), ._28(\地图备份寄存器堆_32_1_行28 ), ._29(\地图备份寄存器堆_32_1_行29 ),
    ._30(\地图备份寄存器堆_32_1_行30 ), ._31(\地图备份寄存器堆_32_1_行31 ), ._32(\地图备份寄存器堆_32_1_行32 ), .CLK(CLK_t),
    ._1_2(\行1 ), ._2_2(\行2 ), ._3_2(\行3 ), ._4_2(\行4 ), ._5_2(\行5 ), ._6_2(\行6 ), ._7_2(\行7 ), ._8_2(\行8 ),
    ._9_2(\行9 ), ._10_2(\行10 ), ._11_2(\行11 ), ._12_2(\行12 ), ._13_2(\行13 ), ._14_2(\行14 ), ._15_2(\行15 ),
    ._16_2(\行16 ), ._17_2(\行17 ), ._18_2(\行18 ), ._19_2(\行19 ), ._20_2(\行20 ), ._21_2(\行21 ), ._22_2(\行22 ),
    ._23_2(\行23 ), ._24_2(\行24 ), ._25_2(\行25 ), ._26_2(\行26 ), ._27_2(\行27 ), ._28_2(\行28 ), ._29_2(\行29 ),
    ._30_2(\行30 ), ._31_2(\行31 ), ._32_2(\行32 ), .RST(RST));

  // Other names for the same wires on the sheet: Low[15:0] = Data[15:0]; High[15:0] = Data[31:16]; MAddr[11:2] = ADDR;
  //   v0[31:0] = MDin

  // Notes on the sheet:
  //   中断源
  //   中断等待指示
  //   总复位信号应将除ROM以外所有存储组件全部清零
  //   数码管输出
  //   数码管输出应该用寄存器锁存，否则显示数据只能一闪而过
  //   指令存储器
  //   指令字
  //   contents of rom_1 (hex, n*v repeats v):
  //   8000c66 20130001 20150008 20100001 20110001 20120001 20140000 ac100020 ac10003c ac100050 20020022 c
  //   108040 22940001 1695fff8 20140000 ac100020 ac10003c ac100050 ac110010 ac110030 ac110080 20020022 c
  //   108040 118840 22940001 1695fff4 20140000 ac100020 ac10003c ac100050 ac110010 ac110030 ac110060
  //   ac120008 ac120028 ac120040 20020022 c 108040 118840 129040 22940001 1695fff0 20140000 22100001
  //   ac100020 ac10003c ac100050 ac110010 ac110030 ac110060 ac120008 ac120028 ac120040 20020022 c 108040
  //   118840 129040 22940001 1695fff0 20140000 22310001 ac100020 ac10003c ac100050 ac110010 ac110030
  //   ac110060 ac120008 ac120028 ac120040 20020022 c 108040 118840 129040 22940001 1695fff0 20140000
  //   22520001 ac100020 ac10003c ac100050 ac110010 ac110030 ac110060 ac120008 ac120028 ac120040 20020022 c
  //   108040 118840 129040 22940001 1695fff0 20140000 22100001 8000c2f 5*0 8000c66
  //   JMP
  //   JR
  //   OP
  //   OP
  //   Func
  //   Func
  //   rs
  //   rt
  //   rd
  //   shamt
  //   Beq
  //   Bne
  //   MemToReg
  //   MemWrite
  //   AluOP
  //   AluSrcB
  //   RegWrite
  //   JAL
  //   RegDst
  //   Syscall
  //   为方便自动评测，需要输出PC，IR，寄存器堆写如数据RDin
  //   RAM写使能MemWrite、RAM写入数据MDin等信号
endmodule

module \点阵显示  (
  input  \开始 ,
  input  CLK,
  input  RST,
  input  [15:0] \金币速度 ,
  input  \上 ,
  input  \下 ,
  output [31:0] _1,
  output [31:0] _2,
  output [31:0] _3,
  output [31:0] _4,
  output [31:0] _5,
  output [31:0] _6,
  output [31:0] _7,
  output [31:0] _8,
  output [31:0] _9,
  output [31:0] _10,
  output [31:0] _11,
  output [31:0] _12,
  output [31:0] _13,
  output [31:0] _14,
  output [31:0] _15,
  output [31:0] _16,
  output [31:0] _17,
  output [31:0] _18,
  output [31:0] _19,
  output [31:0] _20,
  output [31:0] _21,
  output success,
  output \警报 ,
  output [31:0] _22,
  output [31:0] _23,
  output [31:0] _24,
  output [31:0] _25,
  output [31:0] _26,
  output [31:0] _27,
  output [31:0] _28,
  output [31:0] _29,
  output [31:0] _30,
  output [31:0] _31,
  output [31:0] _32,
  output \得分 
);

  wire [31:0] and_1_out, and_2_out, and_3_out, and_4_out, and_5_out, and_6_out, and_7_out, and_8_out,
       and_9_out, and_10_out, and_11_out, and_12_out, and_13_out, and_14_out, and_15_out, and_16_out,
       and_17_out, and_18_out, and_19_out, and_20_out, and_21_out, and_22_out, and_23_out, and_24_out,
       and_25_out, and_26_out, and_27_out, and_28_out, or_1_out, \单周期mips_单级中断_1_行1 , \单周期mips_单级中断_1_行2 ,
       \单周期mips_单级中断_1_行3 , \单周期mips_单级中断_1_行4 , \单周期mips_单级中断_1_行5 , \单周期mips_单级中断_1_行6 ,
       \单周期mips_单级中断_1_行7 , \单周期mips_单级中断_1_行8 , \单周期mips_单级中断_1_行9 , \单周期mips_单级中断_1_行10 ,
       \单周期mips_单级中断_1_行11 , \单周期mips_单级中断_1_行12 , \单周期mips_单级中断_1_行13 , \单周期mips_单级中断_1_行14 ,
       \单周期mips_单级中断_1_行15 , \单周期mips_单级中断_1_行16 , \单周期mips_单级中断_1_行17 , \单周期mips_单级中断_1_行18 ,
       \单周期mips_单级中断_1_行19 , \单周期mips_单级中断_1_行20 , \单周期mips_单级中断_1_行21 , \单周期mips_单级中断_1_行22 ,
       \单周期mips_单级中断_1_行23 , \单周期mips_单级中断_1_行24 , \单周期mips_单级中断_1_行25 , \单周期mips_单级中断_1_行26 ,
       \单周期mips_单级中断_1_行27 , \单周期mips_单级中断_1_行28 , \单周期mips_单级中断_1_行29 , \单周期mips_单级中断_1_行30 ,
       \单周期mips_单级中断_1_行31 , \单周期mips_单级中断_1_行32 , \金币移动_1_行1 , \金币移动_1_行2 , \金币移动_1_行3 , \金币移动_1_行4 ,
       \金币移动_1_行5 , \金币移动_1_行6 , \金币移动_1_行7 , \金币移动_1_行8 , \金币移动_1_行9 , \金币移动_1_行10 , \金币移动_1_行11 ,
       \金币移动_1_行12 , \金币移动_1_行13 , \金币移动_1_行14 , \金币移动_1_行15 , \金币移动_1_行16 , \金币移动_1_行17 , \金币移动_1_行18 ,
       \金币移动_1_行19 , \金币移动_1_行20 , \金币移动_1_行21 , \金币移动_1_行22 , \金币移动_1_行23 , \金币移动_1_行24 , \金币移动_1_行25 ,
       \金币移动_1_行26 , \金币移动_1_行27 , \金币移动_1_行28 , \金币移动_1_行29 , \金币移动_1_行30 , \金币移动_1_行31 , \金币移动_1_行32 ;

  \金币移动  \u_金币移动_1  (
    .IR5(\开始 ), .CLK(CLK), .RST(RST), .\行1 (\金币移动_1_行1 ), .\行2 (\金币移动_1_行2 ), .\行3 (\金币移动_1_行3 ),
    .\行4 (\金币移动_1_行4 ), .\行5 (\金币移动_1_行5 ), .\行6 (\金币移动_1_行6 ), .\行7 (\金币移动_1_行7 ), .\行8 (\金币移动_1_行8 ),
    .\行9 (\金币移动_1_行9 ), .\行10 (\金币移动_1_行10 ), .\行11 (\金币移动_1_行11 ), .\行12 (\金币移动_1_行12 ),
    .\行13 (\金币移动_1_行13 ), .\行14 (\金币移动_1_行14 ), .\行15 (\金币移动_1_行15 ), .\行16 (\金币移动_1_行16 ),
    .\行17 (\金币移动_1_行17 ), .\行18 (\金币移动_1_行18 ), .\行19 (\金币移动_1_行19 ), .\行20 (\金币移动_1_行20 ),
    .\行21 (\金币移动_1_行21 ), .\行22 (\金币移动_1_行22 ), .\行23 (\金币移动_1_行23 ), .\行24 (\金币移动_1_行24 ),
    .\行25 (\金币移动_1_行25 ), .\行26 (\金币移动_1_行26 ), .\行27 (\金币移动_1_行27 ), .\行28 (\金币移动_1_行28 ),
    .\行29 (\金币移动_1_行29 ), .\行30 (\金币移动_1_行30 ), .\行31 (\金币移动_1_行31 ), .\行32 (\金币移动_1_行32 ), .\金币速度 (\金币速度 ));  // open: IR4, IR6, IR1, IR2, IR3, Success, 警报铃声
  \单周期MIPS_单级中断  \u_单周期mips_单级中断_1  (
    .IR1(\上 ), .IR2(\下 ), .\行1 (\单周期mips_单级中断_1_行1 ), .\行2 (\单周期mips_单级中断_1_行2 ), .\行3 (\单周期mips_单级中断_1_行3 ),
    .\行4 (\单周期mips_单级中断_1_行4 ), .\行5 (\单周期mips_单级中断_1_行5 ), .\行6 (\单周期mips_单级中断_1_行6 ),
    .\行7 (\单周期mips_单级中断_1_行7 ), .\行8 (\单周期mips_单级中断_1_行8 ), .\行9 (\单周期mips_单级中断_1_行9 ),
    .\行10 (\单周期mips_单级中断_1_行10 ), .\行11 (\单周期mips_单级中断_1_行11 ), .Success(success),
    .\行12 (\单周期mips_单级中断_1_行12 ), .\行13 (\单周期mips_单级中断_1_行13 ), .\行14 (\单周期mips_单级中断_1_行14 ),
    .\行15 (\单周期mips_单级中断_1_行15 ), .\行16 (\单周期mips_单级中断_1_行16 ), .\行17 (\单周期mips_单级中断_1_行17 ),
    .\行18 (\单周期mips_单级中断_1_行18 ), .\行19 (\单周期mips_单级中断_1_行19 ), .\行20 (\单周期mips_单级中断_1_行20 ),
    .\行21 (\单周期mips_单级中断_1_行21 ), .\行22 (\单周期mips_单级中断_1_行22 ), .\行23 (\单周期mips_单级中断_1_行23 ),
    .\行24 (\单周期mips_单级中断_1_行24 ), .\行25 (\单周期mips_单级中断_1_行25 ), .\行26 (\单周期mips_单级中断_1_行26 ),
    .\行27 (\单周期mips_单级中断_1_行27 ), .\行28 (\单周期mips_单级中断_1_行28 ), .\行29 (\单周期mips_单级中断_1_行29 ),
    .\行30 (\单周期mips_单级中断_1_行30 ), .\行31 (\单周期mips_单级中断_1_行31 ), .\行32 (\单周期mips_单级中断_1_行32 ), .RST(RST),
    .IR5(\开始 ), .CLK(CLK), .\警报铃声 (\警报 ));  // open: IR3, IR4, IR6
  assign and_1_out = \金币移动_1_行3  & \单周期mips_单级中断_1_行3 ;  // AND_Gate and_1, 32 bits wide
  assign and_2_out = \金币移动_1_行4  & \单周期mips_单级中断_1_行4 ;  // AND_Gate and_2, 32 bits wide
  assign and_3_out = \金币移动_1_行5  & \单周期mips_单级中断_1_行5 ;  // AND_Gate and_3, 32 bits wide
  assign and_4_out = \金币移动_1_行7  & \单周期mips_单级中断_1_行7 ;  // AND_Gate and_4, 32 bits wide
  assign and_5_out = \金币移动_1_行6  & \单周期mips_单级中断_1_行6 ;  // AND_Gate and_5, 32 bits wide
  assign and_6_out = \金币移动_1_行8  & \单周期mips_单级中断_1_行8 ;  // AND_Gate and_6, 32 bits wide
  assign and_7_out = \金币移动_1_行9  & \单周期mips_单级中断_1_行9 ;  // AND_Gate and_7, 32 bits wide
  assign and_8_out = \金币移动_1_行10  & \单周期mips_单级中断_1_行10 ;  // AND_Gate and_8, 32 bits wide
  assign and_9_out = \金币移动_1_行12  & \单周期mips_单级中断_1_行12 ;  // AND_Gate and_9, 32 bits wide
  assign and_10_out = \金币移动_1_行11  & \单周期mips_单级中断_1_行11 ;  // AND_Gate and_10, 32 bits wide
  assign and_11_out = \金币移动_1_行14  & \单周期mips_单级中断_1_行14 ;  // AND_Gate and_11, 32 bits wide
  assign and_12_out = \金币移动_1_行15  & \单周期mips_单级中断_1_行15 ;  // AND_Gate and_12, 32 bits wide
  assign and_13_out = \金币移动_1_行13  & \单周期mips_单级中断_1_行13 ;  // AND_Gate and_13, 32 bits wide
  assign and_14_out = \金币移动_1_行17  & \单周期mips_单级中断_1_行17 ;  // AND_Gate and_14, 32 bits wide
  assign and_15_out = \金币移动_1_行18  & \单周期mips_单级中断_1_行18 ;  // AND_Gate and_15, 32 bits wide
  assign and_16_out = \金币移动_1_行16  & \单周期mips_单级中断_1_行16 ;  // AND_Gate and_16, 32 bits wide
  assign or_1_out = and_1_out | and_2_out | and_3_out | and_5_out | and_4_out | and_6_out | and_7_out | and_8_out | and_10_out | and_9_out | and_13_out | and_11_out | and_12_out | and_16_out | and_14_out | and_15_out | and_18_out | and_17_out | and_20_out | and_19_out | and_21_out | and_23_out | and_24_out | and_22_out | and_25_out | and_26_out | and_27_out | and_28_out;  // OR_Gate or_1, 32 bits wide
  Comparator #(.width(32), .mode("unsigned")) comparator_1 (.a(or_1_out), .b({32{1'b0}}), .gt(\得分 ));  // open: eq, lt
  assign and_17_out = \金币移动_1_行29  & \单周期mips_单级中断_1_行29 ;  // AND_Gate and_17, 32 bits wide
  assign and_18_out = \金币移动_1_行30  & \单周期mips_单级中断_1_行30 ;  // AND_Gate and_18, 32 bits wide
  assign and_19_out = \金币移动_1_行27  & \单周期mips_单级中断_1_行27 ;  // AND_Gate and_19, 32 bits wide
  assign and_20_out = \金币移动_1_行28  & \单周期mips_单级中断_1_行28 ;  // AND_Gate and_20, 32 bits wide
  assign and_21_out = \金币移动_1_行26  & \单周期mips_单级中断_1_行26 ;  // AND_Gate and_21, 32 bits wide
  assign and_22_out = \金币移动_1_行23  & \单周期mips_单级中断_1_行23 ;  // AND_Gate and_22, 32 bits wide
  assign and_23_out = \金币移动_1_行25  & \单周期mips_单级中断_1_行25 ;  // AND_Gate and_23, 32 bits wide
  assign and_24_out = \金币移动_1_行24  & \单周期mips_单级中断_1_行24 ;  // AND_Gate and_24, 32 bits wide
  assign _1 = \金币移动_1_行1  | \单周期mips_单级中断_1_行1 ;  // OR_Gate or_2, 32 bits wide
  assign _2 = \金币移动_1_行2  | \单周期mips_单级中断_1_行2 ;  // OR_Gate or_3, 32 bits wide
  assign _3 = \金币移动_1_行3  | \单周期mips_单级中断_1_行3 ;  // OR_Gate or_4, 32 bits wide
  assign _4 = \金币移动_1_行4  | \单周期mips_单级中断_1_行4 ;  // OR_Gate or_5, 32 bits wide
  assign _5 = \金币移动_1_行5  | \单周期mips_单级中断_1_行5 ;  // OR_Gate or_6, 32 bits wide
  assign _6 = \金币移动_1_行6  | \单周期mips_单级中断_1_行6 ;  // OR_Gate or_7, 32 bits wide
  assign _7 = \金币移动_1_行7  | \单周期mips_单级中断_1_行7 ;  // OR_Gate or_8, 32 bits wide
  assign _8 = \金币移动_1_行8  | \单周期mips_单级中断_1_行8 ;  // OR_Gate or_9, 32 bits wide
  assign _9 = \金币移动_1_行9  | \单周期mips_单级中断_1_行9 ;  // OR_Gate or_10, 32 bits wide
  assign _10 = \金币移动_1_行10  | \单周期mips_单级中断_1_行10 ;  // OR_Gate or_11, 32 bits wide
  assign _11 = \金币移动_1_行11  | \单周期mips_单级中断_1_行11 ;  // OR_Gate or_12, 32 bits wide
  assign _12 = \金币移动_1_行12  | \单周期mips_单级中断_1_行12 ;  // OR_Gate or_13, 32 bits wide
  assign _13 = \金币移动_1_行13  | \单周期mips_单级中断_1_行13 ;  // OR_Gate or_14, 32 bits wide
  assign _14 = \金币移动_1_行14  | \单周期mips_单级中断_1_行14 ;  // OR_Gate or_15, 32 bits wide
  assign _15 = \金币移动_1_行15  | \单周期mips_单级中断_1_行15 ;  // OR_Gate or_16, 32 bits wide
  assign _16 = \金币移动_1_行16  | \单周期mips_单级中断_1_行16 ;  // OR_Gate or_17, 32 bits wide
  assign and_25_out = \金币移动_1_行22  & \单周期mips_单级中断_1_行22 ;  // AND_Gate and_25, 32 bits wide
  assign and_26_out = \金币移动_1_行21  & \单周期mips_单级中断_1_行21 ;  // AND_Gate and_26, 32 bits wide
  assign and_27_out = \金币移动_1_行20  & \单周期mips_单级中断_1_行20 ;  // AND_Gate and_27, 32 bits wide
  assign and_28_out = \金币移动_1_行19  & \单周期mips_单级中断_1_行19 ;  // AND_Gate and_28, 32 bits wide
  assign _17 = \单周期mips_单级中断_1_行17  | \金币移动_1_行17 ;  // OR_Gate or_18, 32 bits wide
  assign _18 = \单周期mips_单级中断_1_行18  | \金币移动_1_行18 ;  // OR_Gate or_19, 32 bits wide
  assign _19 = \单周期mips_单级中断_1_行19  | \金币移动_1_行19 ;  // OR_Gate or_20, 32 bits wide
  assign _20 = \单周期mips_单级中断_1_行20  | \金币移动_1_行20 ;  // OR_Gate or_21, 32 bits wide
  assign _21 = \单周期mips_单级中断_1_行21  | \金币移动_1_行21 ;  // OR_Gate or_22, 32 bits wide
  assign _22 = \单周期mips_单级中断_1_行22  | \金币移动_1_行22 ;  // OR_Gate or_23, 32 bits wide
  assign _23 = \单周期mips_单级中断_1_行23  | \金币移动_1_行23 ;  // OR_Gate or_24, 32 bits wide
  assign _24 = \单周期mips_单级中断_1_行24  | \金币移动_1_行24 ;  // OR_Gate or_25, 32 bits wide
  assign _25 = \单周期mips_单级中断_1_行25  | \金币移动_1_行25 ;  // OR_Gate or_26, 32 bits wide
  assign _26 = \单周期mips_单级中断_1_行26  | \金币移动_1_行26 ;  // OR_Gate or_27, 32 bits wide
  assign _27 = \单周期mips_单级中断_1_行27  | \金币移动_1_行27 ;  // OR_Gate or_28, 32 bits wide
  assign _28 = \单周期mips_单级中断_1_行28  | \金币移动_1_行28 ;  // OR_Gate or_29, 32 bits wide
  assign _29 = \单周期mips_单级中断_1_行29  | \金币移动_1_行29 ;  // OR_Gate or_30, 32 bits wide
  assign _30 = \单周期mips_单级中断_1_行30  | \金币移动_1_行30 ;  // OR_Gate or_31, 32 bits wide
  assign _31 = \单周期mips_单级中断_1_行31  | \金币移动_1_行31 ;  // OR_Gate or_32, 32 bits wide
  assign _32 = \单周期mips_单级中断_1_行32  | \金币移动_1_行32 ;  // OR_Gate or_33, 32 bits wide
endmodule

// 单周期硬布线控制器
module \单周期硬布线控制器  (
  input  [5:0] OP,
  input  [5:0] Func,
  output [3:0] ALU_OP,
  output MemToReg,
  output MemWrite,
  output ALU_SRC,
  output RegWrite,
  output SysCALL,
  output SignedExt,
  output RegDst,
  output Beq,
  output Bne,
  output JR,
  output JMP,
  output JAL,
  output BLTZ,
  output LH,
  output SRLV,
  output SET_IE,
  output Clear_IR,
  output LUI
);

  \运算控制器自动生成  \u_运算控制器自动生成_1  (
    .OP0(OP[0]), .OP1(OP[1]), .OP2(OP[2]), .OP3(OP[3]), .OP4(OP[4]), .OP5(OP[5]), .F0(Func[0]), .F1(Func[1]),
    .F2(Func[2]), .F3(Func[3]), .F4(Func[4]), .F5(Func[5]), .S0(ALU_OP[0]), .S1(ALU_OP[1]), .S2(ALU_OP[2]),
    .S3(ALU_OP[3]));
  \控制信号自动生成  \u_控制信号自动生成_1  (
    .OP0(OP[0]), .OP1(OP[1]), .OP2(OP[2]), .OP3(OP[3]), .OP4(OP[4]), .OP5(OP[5]), .F0(Func[0]), .F1(Func[1]),
    .F2(Func[2]), .F3(Func[3]), .F4(Func[4]), .F5(Func[5]), .MemToReg(MemToReg), .MemWrite(MemWrite),
    .ALU_SRC(ALU_SRC), .RegWrite(RegWrite), .SysCALL(SysCALL), .SignedExt(SignedExt), .RegDst(RegDst),
    .BEQ(Beq), .BNE(Bne), .JR(JR), .JUMP(JMP), .JAL(JAL));
  \新增控制信号生成电路  \u_新增控制信号生成电路_1  (
    .OP0(OP[0]), .OP1(OP[1]), .OP2(OP[2]), .OP3(OP[3]), .OP4(OP[4]), .OP5(OP[5]), .F0(Func[0]), .F1(Func[1]),
    .F2(Func[2]), .F3(Func[3]), .F4(Func[4]), .F5(Func[5]), .BLTZ(BLTZ), .LH(LH), .LUI(LUI), .SRLV(SRLV),
    .SET_IE(SET_IE), .Clear_IR(Clear_IR));

  // Other names for the same wires on the sheet: OP_CODE[5:0] = OP

  // Notes on the sheet:
  //   运算器控制器，根据指令生成运算器功能选择信号
  //   控制信号生成，产生数据通路需要的其他控制信号
endmodule

// 运算器控制器
module \运算控制器自动生成  (
  input  OP0,
  input  OP1,
  input  OP2,
  input  OP3,
  input  OP4,
  input  OP5,
  input  F0,
  input  F1,
  input  F2,
  input  F3,
  input  F4,
  input  F5,
  output S0,
  output S1,
  output S2,
  output S3
);

  wire and_1_out, and_2_out, and_3_out, and_4_out, and_5_out, and_6_out, and_7_out, and_8_out, and_9_out,
       and_10_out, and_11_out, and_12_out, and_13_out, and_14_out, and_15_out, and_16_out, and_17_out,
       and_18_out, and_19_out, and_20_out, and_21_out, and_22_out, and_23_out, and_24_out, and_25_out,
       and_26_out, and_27_out, and_28_out, and_29_out, and_30_out, and_31_out, and_32_out, and_33_out,
       and_34_out, and_35_out, and_36_out, and_37_out, and_38_out, and_39_out, and_40_out, and_41_out,
       not_1_out, not_2_out, not_3_out, not_4_out, not_5_out, not_6_out, not_7_out, not_8_out, not_9_out,
       not_10_out, not_11_out, not_12_out, not_13_out, not_14_out, not_15_out, not_16_out, not_17_out,
       not_18_out, not_19_out, not_20_out, not_21_out, not_22_out, not_23_out, not_24_out, not_25_out,
       not_26_out, not_27_out, not_28_out, not_29_out, not_30_out, not_31_out, not_32_out, not_33_out,
       not_34_out, not_35_out, not_36_out, not_37_out, not_38_out, not_39_out, not_40_out, not_41_out,
       not_42_out, not_43_out, not_44_out, not_45_out, not_46_out, not_47_out, not_48_out, not_49_out,
       not_50_out, not_51_out, not_52_out, not_53_out, not_54_out, not_55_out, not_56_out, not_57_out,
       not_58_out, not_59_out, not_60_out, not_61_out, not_62_out, not_63_out, not_64_out, not_65_out,
       not_66_out, not_67_out, not_68_out, not_69_out, not_70_out, not_71_out, not_72_out, not_73_out,
       not_74_out, not_75_out, not_76_out, not_77_out, not_78_out, not_79_out, not_80_out, not_81_out,
       not_82_out, not_83_out, not_84_out, not_85_out, not_86_out, not_87_out, not_88_out, not_89_out,
       not_90_out, not_91_out, not_92_out, not_93_out, not_94_out, not_95_out, not_96_out, not_97_out,
       not_98_out, not_99_out, not_100_out, not_101_out, not_102_out, not_103_out, not_104_out, not_105_out,
       not_106_out, not_107_out, not_108_out, not_109_out, not_110_out, not_111_out, not_112_out,
       not_113_out, not_114_out, not_115_out, not_116_out, not_117_out, not_118_out, not_119_out,
       not_120_out, not_121_out, not_122_out, not_123_out, not_124_out, not_125_out, not_126_out,
       not_127_out, not_128_out, not_129_out, not_130_out, not_131_out, not_132_out, not_133_out,
       not_134_out, not_135_out, not_136_out, not_137_out, not_138_out, not_139_out, not_140_out,
       not_141_out, not_142_out, not_143_out, not_144_out, not_145_out, not_146_out, not_147_out,
       not_148_out, not_149_out, not_150_out, not_151_out, not_152_out, not_153_out, not_154_out,
       not_155_out, not_156_out, not_157_out, not_158_out, not_159_out, not_160_out, not_161_out,
       not_162_out, not_163_out, not_164_out, not_165_out, not_166_out, not_167_out, not_168_out,
       not_169_out, not_170_out, not_171_out, not_172_out, not_173_out, not_174_out, not_175_out,
       not_176_out, not_177_out, not_178_out, not_179_out, not_180_out, not_181_out, not_182_out,
       not_183_out, not_184_out, not_185_out, not_186_out, not_187_out, not_188_out, not_189_out,
       not_190_out, not_191_out, not_192_out, not_193_out, not_194_out, not_195_out, not_196_out,
       not_197_out, not_198_out, not_199_out, not_200_out, not_201_out, not_202_out, not_203_out,
       not_204_out, not_205_out, not_206_out, not_207_out, not_208_out, not_209_out, not_210_out,
       not_211_out, not_212_out, not_213_out, not_214_out, not_215_out, not_216_out, not_217_out,
       not_218_out, not_219_out, not_220_out, not_221_out, not_222_out, not_223_out, not_224_out,
       not_225_out, not_226_out, not_227_out, not_228_out, not_229_out, not_230_out, not_231_out,
       not_232_out, not_233_out, not_234_out, not_235_out, not_236_out, not_237_out, not_238_out,
       not_239_out, not_240_out, not_241_out, not_242_out, not_243_out, not_244_out, not_245_out,
       not_246_out, not_247_out, not_248_out, not_249_out, not_250_out, not_251_out, not_252_out,
       not_253_out, not_254_out, not_255_out, not_256_out, not_257_out, not_258_out, not_259_out,
       not_260_out, not_261_out, not_262_out, not_263_out, not_264_out, not_265_out, not_266_out,
       not_267_out, not_268_out, not_269_out, not_270_out, not_271_out, not_272_out, not_273_out,
       not_274_out, not_275_out, not_276_out, not_277_out, not_278_out;

  not not_1 (not_1_out, OP5);
  not not_2 (not_2_out, OP4);
  not not_3 (not_3_out, OP3);
  not not_4 (not_4_out, OP2);
  not not_5 (not_5_out, OP1);
  not not_6 (not_6_out, OP0);
  not not_7 (not_7_out, F5);
  not not_8 (not_8_out, F4);
  not not_9 (not_9_out, F3);
  not not_10 (not_10_out, F2);
  not not_11 (not_11_out, OP5);
  not not_12 (not_12_out, OP4);
  not not_13 (not_13_out, OP3);
  not not_14 (not_14_out, OP2);
  not not_15 (not_15_out, OP1);
  not not_16 (not_16_out, OP0);
  not not_17 (not_17_out, F4);
  not not_18 (not_18_out, F3);
  not not_19 (not_19_out, F2);
  not not_20 (not_20_out, F1);
  not not_21 (not_21_out, F0);
  not not_22 (not_22_out, OP5);
  not not_23 (not_23_out, OP4);
  not not_24 (not_24_out, OP3);
  not not_25 (not_25_out, OP2);
  not not_26 (not_26_out, OP1);
  not not_27 (not_27_out, OP0);
  not not_28 (not_28_out, F4);
  not not_29 (not_29_out, F3);
  not not_30 (not_30_out, F2);
  not not_31 (not_31_out, F1);
  not not_32 (not_32_out, OP5);
  not not_33 (not_33_out, OP4);
  not not_34 (not_34_out, OP3);
  not not_35 (not_35_out, OP2);
  not not_36 (not_36_out, OP1);
  not not_37 (not_37_out, OP0);
  not not_38 (not_38_out, F4);
  not not_39 (not_39_out, F3);
  not not_40 (not_40_out, F1);
  not not_41 (not_41_out, F0);
  not not_42 (not_42_out, OP5);
  not not_43 (not_43_out, OP4);
  not not_44 (not_44_out, OP3);
  not not_45 (not_45_out, OP2);
  not not_46 (not_46_out, OP1);
  not not_47 (not_47_out, OP0);
  not not_48 (not_48_out, F4);
  not not_49 (not_49_out, F2);
  not not_50 (not_50_out, F0);
  not not_51 (not_51_out, OP5);
  not not_52 (not_52_out, OP4);
  not not_53 (not_53_out, OP2);
  not not_54 (not_54_out, OP1);
  not not_55 (not_55_out, OP0);
  not not_56 (not_56_out, OP5);
  not not_57 (not_57_out, OP4);
  not not_58 (not_58_out, OP1);
  not not_59 (not_59_out, OP0);
  not not_60 (not_60_out, OP5);
  not not_61 (not_61_out, OP4);
  not not_62 (not_62_out, OP2);
  not not_63 (not_63_out, OP1);
  not not_64 (not_64_out, OP5);
  not not_65 (not_65_out, OP4);
  not not_66 (not_66_out, OP2);
  not not_67 (not_67_out, OP0);
  not not_68 (not_68_out, OP4);
  not not_69 (not_69_out, OP3);
  not not_70 (not_70_out, OP2);
  not not_71 (not_71_out, OP4);
  not not_72 (not_72_out, OP2);
  not not_73 (not_73_out, OP4);
  not not_74 (not_74_out, OP3);
  not not_75 (not_75_out, OP2);
  not not_76 (not_76_out, OP1);
  not not_77 (not_77_out, OP5);
  not not_78 (not_78_out, OP4);
  not not_79 (not_79_out, OP3);
  not not_80 (not_80_out, OP2);
  not not_81 (not_81_out, OP1);
  not not_82 (not_82_out, OP0);
  not not_83 (not_83_out, F4);
  not not_84 (not_84_out, F3);
  not not_85 (not_85_out, F0);
  not not_86 (not_86_out, OP5);
  not not_87 (not_87_out, OP4);
  not not_88 (not_88_out, OP3);
  not not_89 (not_89_out, OP2);
  not not_90 (not_90_out, OP1);
  not not_91 (not_91_out, OP0);
  not not_92 (not_92_out, F5);
  not not_93 (not_93_out, F4);
  not not_94 (not_94_out, F3);
  not not_95 (not_95_out, F2);
  not not_96 (not_96_out, F0);
  not not_97 (not_97_out, OP5);
  not not_98 (not_98_out, OP4);
  not not_99 (not_99_out, OP3);
  not not_100 (not_100_out, OP2);
  not not_101 (not_101_out, OP1);
  not not_102 (not_102_out, OP0);
  not not_103 (not_103_out, F4);
  not not_104 (not_104_out, F3);
  not not_105 (not_105_out, F2);
  not not_106 (not_106_out, F0);
  not not_107 (not_107_out, OP5);
  not not_108 (not_108_out, OP4);
  not not_109 (not_109_out, OP3);
  not not_110 (not_110_out, OP2);
  not not_111 (not_111_out, OP1);
  not not_112 (not_112_out, OP0);
  not not_113 (not_113_out, F4);
  not not_114 (not_114_out, F3);
  not not_115 (not_115_out, F1);
  not not_116 (not_116_out, F0);
  not not_117 (not_117_out, OP5);
  not not_118 (not_118_out, OP4);
  not not_119 (not_119_out, OP3);
  not not_120 (not_120_out, OP2);
  not not_121 (not_121_out, OP1);
  not not_122 (not_122_out, OP0);
  not not_123 (not_123_out, F4);
  not not_124 (not_124_out, F3);
  not not_125 (not_125_out, OP5);
  not not_126 (not_126_out, OP4);
  not not_127 (not_127_out, OP3);
  not not_128 (not_128_out, OP2);
  not not_129 (not_129_out, OP1);
  not not_130 (not_130_out, OP0);
  not not_131 (not_131_out, F4);
  not not_132 (not_132_out, F2);
  not not_133 (not_133_out, F0);
  not not_134 (not_134_out, OP5);
  not not_135 (not_135_out, OP4);
  not not_136 (not_136_out, OP1);
  not not_137 (not_137_out, OP0);
  not not_138 (not_138_out, OP5);
  not not_139 (not_139_out, OP4);
  not not_140 (not_140_out, OP2);
  not not_141 (not_141_out, OP0);
  not not_142 (not_142_out, OP5);
  not not_143 (not_143_out, OP4);
  not not_144 (not_144_out, OP3);
  not not_145 (not_145_out, OP2);
  not not_146 (not_146_out, OP1);
  not not_147 (not_147_out, OP0);
  not not_148 (not_148_out, F5);
  not not_149 (not_149_out, F4);
  not not_150 (not_150_out, F3);
  not not_151 (not_151_out, F0);
  not not_152 (not_152_out, OP5);
  not not_153 (not_153_out, OP4);
  not not_154 (not_154_out, OP3);
  not not_155 (not_155_out, OP2);
  not not_156 (not_156_out, OP1);
  not not_157 (not_157_out, OP0);
  not not_158 (not_158_out, F4);
  not not_159 (not_159_out, F3);
  not not_160 (not_160_out, F2);
  not not_161 (not_161_out, F1);
  not not_162 (not_162_out, F0);
  not not_163 (not_163_out, OP5);
  not not_164 (not_164_out, OP4);
  not not_165 (not_165_out, OP3);
  not not_166 (not_166_out, OP2);
  not not_167 (not_167_out, OP1);
  not not_168 (not_168_out, OP0);
  not not_169 (not_169_out, F4);
  not not_170 (not_170_out, F3);
  not not_171 (not_171_out, F2);
  not not_172 (not_172_out, F1);
  not not_173 (not_173_out, OP5);
  not not_174 (not_174_out, OP4);
  not not_175 (not_175_out, OP3);
  not not_176 (not_176_out, OP2);
  not not_177 (not_177_out, OP1);
  not not_178 (not_178_out, OP0);
  not not_179 (not_179_out, F4);
  not not_180 (not_180_out, F3);
  not not_181 (not_181_out, F2);
  not not_182 (not_182_out, F0);
  not not_183 (not_183_out, OP5);
  not not_184 (not_184_out, OP4);
  not not_185 (not_185_out, OP3);
  not not_186 (not_186_out, OP2);
  not not_187 (not_187_out, OP1);
  not not_188 (not_188_out, OP0);
  not not_189 (not_189_out, F4);
  not not_190 (not_190_out, F3);
  not not_191 (not_191_out, F1);
  not not_192 (not_192_out, F0);
  not not_193 (not_193_out, OP5);
  not not_194 (not_194_out, OP4);
  not not_195 (not_195_out, OP3);
  not not_196 (not_196_out, OP2);
  not not_197 (not_197_out, OP1);
  not not_198 (not_198_out, OP0);
  not not_199 (not_199_out, F4);
  not not_200 (not_200_out, F2);
  not not_201 (not_201_out, OP5);
  not not_202 (not_202_out, OP4);
  not not_203 (not_203_out, OP2);
  not not_204 (not_204_out, OP1);
  not not_205 (not_205_out, OP0);
  not not_206 (not_206_out, OP5);
  not not_207 (not_207_out, OP4);
  not not_208 (not_208_out, OP1);
  not not_209 (not_209_out, OP0);
  not not_210 (not_210_out, OP5);
  not not_211 (not_211_out, OP4);
  not not_212 (not_212_out, OP2);
  not not_213 (not_213_out, OP1);
  not not_214 (not_214_out, OP4);
  not not_215 (not_215_out, OP3);
  not not_216 (not_216_out, OP2);
  not not_217 (not_217_out, OP4);
  not not_218 (not_218_out, OP2);
  not not_219 (not_219_out, OP5);
  not not_220 (not_220_out, OP4);
  not not_221 (not_221_out, OP2);
  not not_222 (not_222_out, OP4);
  not not_223 (not_223_out, OP3);
  not not_224 (not_224_out, OP2);
  not not_225 (not_225_out, OP1);
  not not_226 (not_226_out, OP5);
  not not_227 (not_227_out, OP4);
  not not_228 (not_228_out, OP3);
  not not_229 (not_229_out, OP2);
  not not_230 (not_230_out, OP1);
  not not_231 (not_231_out, OP0);
  not not_232 (not_232_out, F4);
  not not_233 (not_233_out, F3);
  not not_234 (not_234_out, F1);
  not not_235 (not_235_out, OP5);
  not not_236 (not_236_out, OP4);
  not not_237 (not_237_out, OP3);
  not not_238 (not_238_out, OP2);
  not not_239 (not_239_out, OP1);
  not not_240 (not_240_out, OP0);
  not not_241 (not_241_out, F4);
  not not_242 (not_242_out, F3);
  not not_243 (not_243_out, OP5);
  not not_244 (not_244_out, OP4);
  not not_245 (not_245_out, OP3);
  not not_246 (not_246_out, OP2);
  not not_247 (not_247_out, OP1);
  not not_248 (not_248_out, OP0);
  not not_249 (not_249_out, F4);
  not not_250 (not_250_out, F2);
  not not_251 (not_251_out, F0);
  not not_252 (not_252_out, OP5);
  not not_253 (not_253_out, OP4);
  not not_254 (not_254_out, OP3);
  not not_255 (not_255_out, OP2);
  not not_256 (not_256_out, OP1);
  not not_257 (not_257_out, OP0);
  not not_258 (not_258_out, F4);
  not not_259 (not_259_out, F2);
  not not_260 (not_260_out, OP5);
  not not_261 (not_261_out, OP4);
  not not_262 (not_262_out, OP2);
  not not_263 (not_263_out, OP0);
  not not_264 (not_264_out, OP5);
  not not_265 (not_265_out, OP4);
  not not_266 (not_266_out, OP1);
  not not_267 (not_267_out, OP5);
  not not_268 (not_268_out, OP4);
  not not_269 (not_269_out, OP2);
  not not_270 (not_270_out, OP5);
  not not_271 (not_271_out, OP4);
  not not_272 (not_272_out, OP3);
  not not_273 (not_273_out, OP2);
  not not_274 (not_274_out, OP1);
  not not_275 (not_275_out, OP0);
  not not_276 (not_276_out, F4);
  not not_277 (not_277_out, F3);
  not not_278 (not_278_out, F0);
  and and_1 (and_1_out, not_1_out, not_2_out, not_3_out, not_4_out, not_5_out, not_6_out, not_7_out, not_8_out, not_9_out, not_10_out, F1, F0);
  and and_2 (and_2_out, not_11_out, not_12_out, not_13_out, not_14_out, not_15_out, not_16_out, F5, not_17_out, not_18_out, not_19_out, not_20_out, not_21_out);
  and and_3 (and_3_out, not_22_out, not_23_out, not_24_out, not_25_out, not_26_out, not_27_out, F5, not_28_out, not_29_out, not_30_out, not_31_out, F0);
  and and_4 (and_4_out, not_32_out, not_33_out, not_34_out, not_35_out, not_36_out, not_37_out, F5, not_38_out, not_39_out, F2, not_40_out, not_41_out);
  and and_5 (and_5_out, not_42_out, not_43_out, not_44_out, not_45_out, not_46_out, not_47_out, F5, not_48_out, F3, not_49_out, F1, not_50_out);
  and and_6 (and_6_out, not_51_out, not_52_out, OP3, not_53_out, not_54_out, not_55_out);
  and and_7 (and_7_out, not_56_out, not_57_out, OP3, OP2, not_58_out, not_59_out);
  and and_8 (and_8_out, not_60_out, not_61_out, OP3, not_62_out, not_63_out, OP0);
  and and_9 (and_9_out, not_64_out, not_65_out, OP3, not_66_out, OP1, not_67_out);
  and and_10 (and_10_out, OP5, not_68_out, not_69_out, not_70_out, OP1, OP0);
  and and_11 (and_11_out, OP5, not_71_out, OP3, not_72_out, OP1, OP0);
  and and_12 (and_12_out, OP5, not_73_out, not_74_out, not_75_out, not_76_out, OP0);
  and and_13 (and_13_out, not_77_out, not_78_out, not_79_out, not_80_out, not_81_out, not_82_out, F5, not_83_out, not_84_out, F2, F1, not_85_out);
  and and_14 (and_14_out, not_86_out, not_87_out, not_88_out, not_89_out, not_90_out, not_91_out, not_92_out, not_93_out, not_94_out, not_95_out, F1, not_96_out);
  and and_15 (and_15_out, not_97_out, not_98_out, not_99_out, not_100_out, not_101_out, not_102_out, F5, not_103_out, not_104_out, not_105_out, F1, not_106_out);
  and and_16 (and_16_out, not_107_out, not_108_out, not_109_out, not_110_out, not_111_out, not_112_out, F5, not_113_out, not_114_out, F2, not_115_out, not_116_out);
  and and_17 (and_17_out, not_117_out, not_118_out, not_119_out, not_120_out, not_121_out, not_122_out, F5, not_123_out, not_124_out, F2, F1, F0);
  and and_18 (and_18_out, not_125_out, not_126_out, not_127_out, not_128_out, not_129_out, not_130_out, F5, not_131_out, F3, not_132_out, F1, not_133_out);
  and and_19 (and_19_out, not_134_out, not_135_out, OP3, OP2, not_136_out, not_137_out);
  and and_20 (and_20_out, not_138_out, not_139_out, OP3, not_140_out, OP1, not_141_out);
  and and_21 (and_21_out, not_142_out, not_143_out, not_144_out, not_145_out, not_146_out, not_147_out, not_148_out, not_149_out, not_150_out, F2, F1, not_151_out);
  and and_22 (and_22_out, not_152_out, not_153_out, not_154_out, not_155_out, not_156_out, not_157_out, F5, not_158_out, not_159_out, not_160_out, not_161_out, not_162_out);
  and and_23 (and_23_out, not_163_out, not_164_out, not_165_out, not_166_out, not_167_out, not_168_out, F5, not_169_out, not_170_out, not_171_out, not_172_out, F0);
  and and_24 (and_24_out, not_173_out, not_174_out, not_175_out, not_176_out, not_177_out, not_178_out, F5, not_179_out, not_180_out, not_181_out, F1, not_182_out);
  and and_25 (and_25_out, not_183_out, not_184_out, not_185_out, not_186_out, not_187_out, not_188_out, F5, not_189_out, not_190_out, F2, not_191_out, not_192_out);
  and and_26 (and_26_out, not_193_out, not_194_out, not_195_out, not_196_out, not_197_out, not_198_out, F5, not_199_out, F3, not_200_out, F1, F0);
  and and_27 (and_27_out, not_201_out, not_202_out, OP3, not_203_out, not_204_out, not_205_out);
  and and_28 (and_28_out, not_206_out, not_207_out, OP3, OP2, not_208_out, not_209_out);
  and and_29 (and_29_out, not_210_out, not_211_out, OP3, not_212_out, not_213_out, OP0);
  and and_30 (and_30_out, OP5, not_214_out, not_215_out, not_216_out, OP1, OP0);
  and and_31 (and_31_out, OP5, not_217_out, OP3, not_218_out, OP1, OP0);
  and and_32 (and_32_out, not_219_out, not_220_out, OP3, not_221_out, OP1, OP0);
  and and_33 (and_33_out, OP5, not_222_out, not_223_out, not_224_out, not_225_out, OP0);
  and and_34 (and_34_out, not_226_out, not_227_out, not_228_out, not_229_out, not_230_out, not_231_out, F5, not_232_out, not_233_out, F2, not_234_out, F0);
  and and_35 (and_35_out, not_235_out, not_236_out, not_237_out, not_238_out, not_239_out, not_240_out, F5, not_241_out, not_242_out, F2, F1, F0);
  and and_36 (and_36_out, not_243_out, not_244_out, not_245_out, not_246_out, not_247_out, not_248_out, F5, not_249_out, F3, not_250_out, F1, not_251_out);
  and and_37 (and_37_out, not_252_out, not_253_out, not_254_out, not_255_out, not_256_out, not_257_out, F5, not_258_out, F3, not_259_out, F1, F0);
  and and_38 (and_38_out, not_260_out, not_261_out, OP3, not_262_out, OP1, not_263_out);
  and and_39 (and_39_out, not_264_out, not_265_out, OP3, OP2, not_266_out, OP0);
  and and_40 (and_40_out, not_267_out, not_268_out, OP3, not_269_out, OP1, OP0);
  and and_41 (and_41_out, not_270_out, not_271_out, not_272_out, not_273_out, not_274_out, not_275_out, F5, not_276_out, not_277_out, F2, F1, not_278_out);
  or or_1 (S1, and_14_out, and_15_out, and_16_out, and_17_out, and_18_out, and_19_out, and_20_out, and_21_out);
  or or_2 (S3, and_34_out, and_35_out, and_36_out, and_37_out, and_38_out, and_39_out, and_40_out, and_41_out);
  or or_3 (S0, and_1_out, and_2_out, and_3_out, and_4_out, and_5_out, and_6_out, and_7_out, and_8_out, and_9_out, and_10_out, and_11_out, and_12_out, and_13_out);
  or or_4 (S2, and_22_out, and_23_out, and_24_out, and_25_out, and_26_out, and_27_out, and_28_out, and_29_out, and_30_out, and_31_out, and_32_out, and_33_out);
endmodule
// 控制信号生成
module \控制信号自动生成  (
  input  OP0,
  input  OP1,
  input  OP2,
  input  OP3,
  input  OP4,
  input  OP5,
  input  F0,
  input  F1,
  input  F2,
  input  F3,
  input  F4,
  input  F5,
  output MemToReg,
  output MemWrite,
  output ALU_SRC,
  output RegWrite,
  output SysCALL,
  output SignedExt,
  output RegDst,
  output BEQ,
  output BNE,
  output JR,
  output JUMP,
  output JAL
);

  wire and_3_out, and_4_out, and_5_out, and_6_out, and_7_out, and_8_out, and_9_out, and_10_out, and_11_out,
       and_12_out, and_13_out, and_14_out, and_15_out, and_16_out, and_17_out, and_18_out, and_19_out,
       and_20_out, and_21_out, and_22_out, and_23_out, and_24_out, and_25_out, and_26_out, and_27_out,
       and_28_out, and_29_out, and_30_out, and_32_out, and_33_out, and_34_out, and_35_out, and_36_out,
       and_37_out, and_38_out, and_39_out, and_40_out, and_41_out, and_42_out, and_43_out, and_44_out,
       and_45_out, and_46_out, and_47_out, and_48_out, not_1_out, not_2_out, not_3_out, not_4_out, not_5_out,
       not_6_out, not_7_out, not_8_out, not_9_out, not_10_out, not_11_out, not_12_out, not_13_out,
       not_14_out, not_15_out, not_16_out, not_17_out, not_18_out, not_19_out, not_20_out, not_21_out,
       not_22_out, not_23_out, not_24_out, not_25_out, not_26_out, not_27_out, not_28_out, not_29_out,
       not_30_out, not_31_out, not_32_out, not_33_out, not_34_out, not_35_out, not_36_out, not_37_out,
       not_38_out, not_39_out, not_40_out, not_41_out, not_42_out, not_43_out, not_44_out, not_45_out,
       not_46_out, not_47_out, not_48_out, not_49_out, not_50_out, not_51_out, not_52_out, not_53_out,
       not_54_out, not_55_out, not_56_out, not_57_out, not_58_out, not_59_out, not_60_out, not_61_out,
       not_62_out, not_63_out, not_64_out, not_65_out, not_66_out, not_67_out, not_68_out, not_69_out,
       not_70_out, not_71_out, not_72_out, not_73_out, not_74_out, not_75_out, not_76_out, not_77_out,
       not_78_out, not_79_out, not_80_out, not_81_out, not_82_out, not_83_out, not_84_out, not_85_out,
       not_86_out, not_87_out, not_88_out, not_89_out, not_90_out, not_91_out, not_92_out, not_93_out,
       not_94_out, not_95_out, not_96_out, not_97_out, not_98_out, not_99_out, not_100_out, not_101_out,
       not_102_out, not_103_out, not_104_out, not_105_out, not_106_out, not_107_out, not_108_out,
       not_109_out, not_110_out, not_111_out, not_112_out, not_113_out, not_114_out, not_115_out,
       not_116_out, not_117_out, not_118_out, not_119_out, not_120_out, not_121_out, not_122_out,
       not_123_out, not_124_out, not_125_out, not_126_out, not_127_out, not_128_out, not_129_out,
       not_130_out, not_131_out, not_132_out, not_133_out, not_134_out, not_135_out, not_136_out,
       not_137_out, not_138_out, not_139_out, not_140_out, not_141_out, not_142_out, not_143_out,
       not_144_out, not_145_out, not_146_out, not_147_out, not_148_out, not_149_out, not_150_out,
       not_151_out, not_152_out, not_153_out, not_154_out, not_155_out, not_156_out, not_157_out,
       not_158_out, not_159_out, not_160_out, not_161_out, not_162_out, not_163_out, not_164_out,
       not_165_out, not_166_out, not_167_out, not_168_out, not_169_out, not_170_out, not_171_out,
       not_172_out, not_173_out, not_174_out, not_175_out, not_176_out, not_177_out, not_178_out,
       not_179_out, not_180_out, not_181_out, not_182_out, not_183_out, not_184_out, not_185_out,
       not_186_out, not_187_out, not_188_out, not_189_out, not_190_out, not_191_out, not_192_out,
       not_193_out, not_194_out, not_195_out, not_196_out, not_197_out, not_198_out, not_199_out,
       not_200_out, not_201_out, not_202_out, not_203_out, not_204_out, not_205_out, not_206_out,
       not_207_out, not_208_out, not_209_out, not_210_out, not_211_out, not_212_out, not_213_out,
       not_214_out, not_215_out, not_216_out, not_217_out, not_218_out, not_219_out, not_220_out,
       not_221_out, not_222_out, not_223_out, not_224_out, not_225_out, not_226_out, not_227_out,
       not_228_out, not_229_out, not_230_out, not_231_out, not_232_out, not_233_out, not_234_out,
       not_235_out, not_236_out, not_237_out, not_238_out, not_239_out, not_240_out, not_241_out,
       not_242_out, not_243_out, not_244_out, not_245_out, not_246_out, not_247_out, not_248_out,
       not_249_out, not_250_out, not_251_out, not_252_out, not_253_out, not_254_out, not_255_out,
       not_256_out, not_257_out, not_258_out, not_259_out, not_260_out, not_261_out, not_262_out,
       not_263_out, not_264_out, not_265_out, not_266_out, not_267_out, not_268_out, not_269_out,
       not_270_out, not_271_out, not_272_out, not_273_out, not_274_out, not_275_out, not_276_out,
       not_277_out, not_278_out, not_279_out, not_280_out, not_281_out, not_282_out, not_283_out,
       not_284_out, not_285_out, not_286_out, not_287_out, not_288_out, not_289_out, not_290_out,
       not_291_out, not_292_out, not_293_out, not_294_out, not_295_out, not_296_out, not_297_out,
       not_298_out, not_299_out, not_300_out, not_301_out, not_302_out, not_303_out, not_304_out,
       not_305_out, not_306_out, not_307_out, not_308_out, not_309_out, not_310_out, not_311_out,
       not_312_out, not_313_out, not_314_out, not_315_out, not_316_out, not_317_out, not_318_out,
       not_319_out, not_320_out, not_321_out, not_322_out, not_323_out, not_324_out, not_325_out,
       not_326_out, not_327_out, not_328_out, not_329_out, not_330_out, not_331_out, not_332_out,
       not_333_out, not_334_out, not_335_out, not_336_out, not_337_out, not_338_out, not_339_out,
       not_340_out, not_341_out, not_342_out, not_343_out, not_344_out, not_345_out, not_346_out,
       not_347_out, not_348_out, not_349_out, not_350_out, not_351_out, not_352_out, not_353_out,
       not_354_out, not_355_out, not_356_out, not_357_out, not_358_out, not_359_out, not_360_out,
       not_361_out, not_362_out, not_363_out, not_364_out, not_365_out, not_366_out, not_367_out,
       not_368_out, not_369_out, not_370_out, not_371_out, not_372_out, not_373_out, not_374_out, not_375_out;

  not not_1 (not_1_out, OP2);
  not not_2 (not_2_out, OP3);
  not not_3 (not_3_out, OP4);
  not not_4 (not_4_out, OP2);
  not not_5 (not_5_out, OP4);
  not not_6 (not_6_out, OP1);
  not not_7 (not_7_out, OP4);
  not not_8 (not_8_out, OP5);
  not not_9 (not_9_out, OP2);
  not not_10 (not_10_out, OP4);
  not not_11 (not_11_out, OP5);
  not not_12 (not_12_out, OP2);
  not not_13 (not_13_out, OP3);
  not not_14 (not_14_out, OP4);
  not not_15 (not_15_out, OP2);
  not not_16 (not_16_out, OP4);
  not not_17 (not_17_out, OP5);
  not not_18 (not_18_out, OP4);
  not not_19 (not_19_out, OP3);
  not not_20 (not_20_out, OP2);
  not not_21 (not_21_out, OP1);
  not not_22 (not_22_out, OP0);
  not not_23 (not_23_out, F5);
  not not_24 (not_24_out, F4);
  not not_25 (not_25_out, F3);
  not not_26 (not_26_out, F2);
  not not_27 (not_27_out, F1);
  not not_28 (not_28_out, F0);
  not not_29 (not_29_out, OP5);
  not not_30 (not_30_out, OP4);
  not not_31 (not_31_out, OP3);
  not not_32 (not_32_out, OP2);
  not not_33 (not_33_out, OP1);
  not not_34 (not_34_out, OP0);
  not not_35 (not_35_out, F5);
  not not_36 (not_36_out, F4);
  not not_37 (not_37_out, F3);
  not not_38 (not_38_out, F2);
  not not_39 (not_39_out, OP5);
  not not_40 (not_40_out, OP4);
  not not_41 (not_41_out, OP3);
  not not_42 (not_42_out, OP2);
  not not_43 (not_43_out, OP1);
  not not_44 (not_44_out, OP0);
  not not_45 (not_45_out, F5);
  not not_46 (not_46_out, F4);
  not not_47 (not_47_out, F3);
  not not_48 (not_48_out, F2);
  not not_49 (not_49_out, F0);
  not not_50 (not_50_out, OP5);
  not not_51 (not_51_out, OP4);
  not not_52 (not_52_out, OP3);
  not not_53 (not_53_out, OP2);
  not not_54 (not_54_out, OP1);
  not not_55 (not_55_out, OP0);
  not not_56 (not_56_out, F4);
  not not_57 (not_57_out, F3);
  not not_58 (not_58_out, F2);
  not not_59 (not_59_out, F1);
  not not_60 (not_60_out, F0);
  not not_61 (not_61_out, OP5);
  not not_62 (not_62_out, OP4);
  not not_63 (not_63_out, OP3);
  not not_64 (not_64_out, OP2);
  not not_65 (not_65_out, OP1);
  not not_66 (not_66_out, OP0);
  not not_67 (not_67_out, F4);
  not not_68 (not_68_out, F3);
  not not_69 (not_69_out, F2);
  not not_70 (not_70_out, F1);
  not not_71 (not_71_out, OP5);
  not not_72 (not_72_out, OP4);
  not not_73 (not_73_out, OP3);
  not not_74 (not_74_out, OP2);
  not not_75 (not_75_out, OP1);
  not not_76 (not_76_out, OP0);
  not not_77 (not_77_out, F4);
  not not_78 (not_78_out, F3);
  not not_79 (not_79_out, F2);
  not not_80 (not_80_out, F0);
  not not_81 (not_81_out, OP5);
  not not_82 (not_82_out, OP4);
  not not_83 (not_83_out, OP3);
  not not_84 (not_84_out, OP2);
  not not_85 (not_85_out, OP1);
  not not_86 (not_86_out, OP0);
  not not_87 (not_87_out, F4);
  not not_88 (not_88_out, F3);
  not not_89 (not_89_out, F1);
  not not_90 (not_90_out, F0);
  not not_91 (not_91_out, OP5);
  not not_92 (not_92_out, OP4);
  not not_93 (not_93_out, OP3);
  not not_94 (not_94_out, OP2);
  not not_95 (not_95_out, OP1);
  not not_96 (not_96_out, OP0);
  not not_97 (not_97_out, F4);
  not not_98 (not_98_out, F3);
  not not_99 (not_99_out, F1);
  not not_100 (not_100_out, OP5);
  not not_101 (not_101_out, OP4);
  not not_102 (not_102_out, OP3);
  not not_103 (not_103_out, OP2);
  not not_104 (not_104_out, OP1);
  not not_105 (not_105_out, OP0);
  not not_106 (not_106_out, F4);
  not not_107 (not_107_out, F3);
  not not_108 (not_108_out, OP5);
  not not_109 (not_109_out, OP4);
  not not_110 (not_110_out, OP3);
  not not_111 (not_111_out, OP2);
  not not_112 (not_112_out, OP1);
  not not_113 (not_113_out, OP0);
  not not_114 (not_114_out, F4);
  not not_115 (not_115_out, F2);
  not not_116 (not_116_out, F0);
  not not_117 (not_117_out, OP5);
  not not_118 (not_118_out, OP4);
  not not_119 (not_119_out, OP3);
  not not_120 (not_120_out, OP2);
  not not_121 (not_121_out, OP1);
  not not_122 (not_122_out, OP0);
  not not_123 (not_123_out, F4);
  not not_124 (not_124_out, F2);
  not not_125 (not_125_out, OP5);
  not not_126 (not_126_out, OP4);
  not not_127 (not_127_out, OP3);
  not not_128 (not_128_out, OP2);
  not not_129 (not_129_out, OP5);
  not not_130 (not_130_out, OP4);
  not not_131 (not_131_out, OP2);
  not not_132 (not_132_out, OP1);
  not not_133 (not_133_out, OP0);
  not not_134 (not_134_out, OP5);
  not not_135 (not_135_out, OP4);
  not not_136 (not_136_out, OP1);
  not not_137 (not_137_out, OP0);
  not not_138 (not_138_out, OP5);
  not not_139 (not_139_out, OP4);
  not not_140 (not_140_out, OP2);
  not not_141 (not_141_out, OP1);
  not not_142 (not_142_out, OP5);
  not not_143 (not_143_out, OP4);
  not not_144 (not_144_out, OP2);
  not not_145 (not_145_out, OP0);
  not not_146 (not_146_out, OP5);
  not not_147 (not_147_out, OP4);
  not not_148 (not_148_out, OP1);
  not not_149 (not_149_out, OP4);
  not not_150 (not_150_out, OP3);
  not not_151 (not_151_out, OP2);
  not not_152 (not_152_out, OP5);
  not not_153 (not_153_out, OP4);
  not not_154 (not_154_out, OP3);
  not not_155 (not_155_out, OP2);
  not not_156 (not_156_out, OP1);
  not not_157 (not_157_out, OP0);
  not not_158 (not_158_out, F5);
  not not_159 (not_159_out, F4);
  not not_160 (not_160_out, F3);
  not not_161 (not_161_out, F0);
  not not_162 (not_162_out, OP5);
  not not_163 (not_163_out, OP4);
  not not_164 (not_164_out, OP2);
  not not_165 (not_165_out, OP4);
  not not_166 (not_166_out, OP3);
  not not_167 (not_167_out, OP2);
  not not_168 (not_168_out, OP1);
  not not_169 (not_169_out, OP5);
  not not_170 (not_170_out, OP4);
  not not_171 (not_171_out, OP3);
  not not_172 (not_172_out, OP2);
  not not_173 (not_173_out, OP1);
  not not_174 (not_174_out, OP0);
  not not_175 (not_175_out, F5);
  not not_176 (not_176_out, F4);
  not not_177 (not_177_out, F3);
  not not_178 (not_178_out, F1);
  not not_179 (not_179_out, F0);
  not not_180 (not_180_out, OP5);
  not not_181 (not_181_out, OP4);
  not not_182 (not_182_out, OP5);
  not not_183 (not_183_out, OP4);
  not not_184 (not_184_out, OP3);
  not not_185 (not_185_out, OP2);
  not not_186 (not_186_out, OP1);
  not not_187 (not_187_out, OP0);
  not not_188 (not_188_out, F4);
  not not_189 (not_189_out, F3);
  not not_190 (not_190_out, F0);
  not not_191 (not_191_out, OP0);
  not not_192 (not_192_out, OP1);
  not not_193 (not_193_out, OP2);
  not not_194 (not_194_out, OP3);
  not not_195 (not_195_out, OP4);
  not not_196 (not_196_out, OP5);
  not not_197 (not_197_out, F0);
  not not_198 (not_198_out, F1);
  not not_199 (not_199_out, F4);
  not not_200 (not_200_out, F5);
  not not_201 (not_201_out, OP2);
  not not_202 (not_202_out, OP4);
  not not_203 (not_203_out, OP5);
  not not_204 (not_204_out, OP2);
  not not_205 (not_205_out, OP3);
  not not_206 (not_206_out, OP4);
  not not_207 (not_207_out, OP2);
  not not_208 (not_208_out, OP4);
  not not_209 (not_209_out, OP5);
  not not_210 (not_210_out, OP4);
  not not_211 (not_211_out, OP3);
  not not_212 (not_212_out, OP2);
  not not_213 (not_213_out, OP1);
  not not_214 (not_214_out, OP0);
  not not_215 (not_215_out, F5);
  not not_216 (not_216_out, F4);
  not not_217 (not_217_out, F3);
  not not_218 (not_218_out, F2);
  not not_219 (not_219_out, F1);
  not not_220 (not_220_out, F0);
  not not_221 (not_221_out, OP5);
  not not_222 (not_222_out, OP4);
  not not_223 (not_223_out, OP3);
  not not_224 (not_224_out, OP2);
  not not_225 (not_225_out, OP1);
  not not_226 (not_226_out, OP0);
  not not_227 (not_227_out, F5);
  not not_228 (not_228_out, F4);
  not not_229 (not_229_out, F3);
  not not_230 (not_230_out, F2);
  not not_231 (not_231_out, OP5);
  not not_232 (not_232_out, OP4);
  not not_233 (not_233_out, OP3);
  not not_234 (not_234_out, OP2);
  not not_235 (not_235_out, OP1);
  not not_236 (not_236_out, OP0);
  not not_237 (not_237_out, F5);
  not not_238 (not_238_out, F4);
  not not_239 (not_239_out, F3);
  not not_240 (not_240_out, F2);
  not not_241 (not_241_out, F0);
  not not_242 (not_242_out, OP5);
  not not_243 (not_243_out, OP4);
  not not_244 (not_244_out, OP3);
  not not_245 (not_245_out, OP2);
  not not_246 (not_246_out, OP1);
  not not_247 (not_247_out, OP0);
  not not_248 (not_248_out, F4);
  not not_249 (not_249_out, F3);
  not not_250 (not_250_out, F2);
  not not_251 (not_251_out, F1);
  not not_252 (not_252_out, F0);
  not not_253 (not_253_out, OP5);
  not not_254 (not_254_out, OP4);
  not not_255 (not_255_out, OP3);
  not not_256 (not_256_out, OP2);
  not not_257 (not_257_out, OP1);
  not not_258 (not_258_out, OP0);
  not not_259 (not_259_out, F4);
  not not_260 (not_260_out, F3);
  not not_261 (not_261_out, F2);
  not not_262 (not_262_out, F1);
  not not_263 (not_263_out, OP5);
  not not_264 (not_264_out, OP4);
  not not_265 (not_265_out, OP3);
  not not_266 (not_266_out, OP2);
  not not_267 (not_267_out, OP1);
  not not_268 (not_268_out, OP0);
  not not_269 (not_269_out, F4);
  not not_270 (not_270_out, F3);
  not not_271 (not_271_out, F2);
  not not_272 (not_272_out, F0);
  not not_273 (not_273_out, OP5);
  not not_274 (not_274_out, OP4);
  not not_275 (not_275_out, OP3);
  not not_276 (not_276_out, OP2);
  not not_277 (not_277_out, OP1);
  not not_278 (not_278_out, OP0);
  not not_279 (not_279_out, F4);
  not not_280 (not_280_out, F3);
  not not_281 (not_281_out, F1);
  not not_282 (not_282_out, F0);
  not not_283 (not_283_out, OP5);
  not not_284 (not_284_out, OP4);
  not not_285 (not_285_out, OP3);
  not not_286 (not_286_out, OP2);
  not not_287 (not_287_out, OP1);
  not not_288 (not_288_out, OP0);
  not not_289 (not_289_out, F4);
  not not_290 (not_290_out, F3);
  not not_291 (not_291_out, F1);
  not not_292 (not_292_out, OP5);
  not not_293 (not_293_out, OP4);
  not not_294 (not_294_out, OP3);
  not not_295 (not_295_out, OP2);
  not not_296 (not_296_out, OP1);
  not not_297 (not_297_out, OP0);
  not not_298 (not_298_out, F4);
  not not_299 (not_299_out, F3);
  not not_300 (not_300_out, OP5);
  not not_301 (not_301_out, OP4);
  not not_302 (not_302_out, OP3);
  not not_303 (not_303_out, OP2);
  not not_304 (not_304_out, OP1);
  not not_305 (not_305_out, OP0);
  not not_306 (not_306_out, F4);
  not not_307 (not_307_out, F2);
  not not_308 (not_308_out, F0);
  not not_309 (not_309_out, OP5);
  not not_310 (not_310_out, OP4);
  not not_311 (not_311_out, OP3);
  not not_312 (not_312_out, OP2);
  not not_313 (not_313_out, OP1);
  not not_314 (not_314_out, OP0);
  not not_315 (not_315_out, F4);
  not not_316 (not_316_out, F2);
  not not_317 (not_317_out, OP5);
  not not_318 (not_318_out, OP4);
  not not_319 (not_319_out, OP3);
  not not_320 (not_320_out, OP2);
  not not_321 (not_321_out, OP1);
  not not_322 (not_322_out, OP0);
  not not_323 (not_323_out, F5);
  not not_324 (not_324_out, F4);
  not not_325 (not_325_out, F3);
  not not_326 (not_326_out, F0);
  not not_327 (not_327_out, OP5);
  not not_328 (not_328_out, OP4);
  not not_329 (not_329_out, OP3);
  not not_330 (not_330_out, OP2);
  not not_331 (not_331_out, OP1);
  not not_332 (not_332_out, OP0);
  not not_333 (not_333_out, F5);
  not not_334 (not_334_out, F4);
  not not_335 (not_335_out, F3);
  not not_336 (not_336_out, F1);
  not not_337 (not_337_out, F0);
  not not_338 (not_338_out, OP5);
  not not_339 (not_339_out, OP4);
  not not_340 (not_340_out, OP3);
  not not_341 (not_341_out, OP2);
  not not_342 (not_342_out, OP1);
  not not_343 (not_343_out, OP0);
  not not_344 (not_344_out, F4);
  not not_345 (not_345_out, F3);
  not not_346 (not_346_out, F0);
  not not_347 (not_347_out, OP0);
  not not_348 (not_348_out, OP1);
  not not_349 (not_349_out, OP3);
  not not_350 (not_350_out, OP4);
  not not_351 (not_351_out, OP5);
  not not_352 (not_352_out, OP1);
  not not_353 (not_353_out, OP3);
  not not_354 (not_354_out, OP4);
  not not_355 (not_355_out, OP5);
  not not_356 (not_356_out, OP0);
  not not_357 (not_357_out, OP1);
  not not_358 (not_358_out, OP2);
  not not_359 (not_359_out, OP3);
  not not_360 (not_360_out, OP4);
  not not_361 (not_361_out, OP5);
  not not_362 (not_362_out, F0);
  not not_363 (not_363_out, F1);
  not not_364 (not_364_out, F2);
  not not_365 (not_365_out, F4);
  not not_366 (not_366_out, F5);
  not not_367 (not_367_out, OP0);
  not not_368 (not_368_out, OP2);
  not not_369 (not_369_out, OP3);
  not not_370 (not_370_out, OP4);
  not not_371 (not_371_out, OP5);
  not not_372 (not_372_out, OP2);
  not not_373 (not_373_out, OP3);
  not not_374 (not_374_out, OP4);
  not not_375 (not_375_out, OP5);
  and and_1 (MemToReg, OP0, OP1, not_1_out, not_2_out, not_3_out, OP5);
  and and_2 (MemWrite, OP0, OP1, not_4_out, OP3, not_5_out, OP5);
  and and_3 (and_3_out, not_6_out, OP3, not_7_out, not_8_out);
  and and_4 (and_4_out, not_9_out, OP3, not_10_out, not_11_out);
  and and_5 (and_5_out, OP0, not_12_out, not_13_out, not_14_out, OP5);
  and and_6 (and_6_out, OP0, OP1, not_15_out, OP3, not_16_out);
  and and_7 (and_7_out, not_17_out, not_18_out, not_19_out, not_20_out, not_21_out, not_22_out, not_23_out, not_24_out, not_25_out, not_26_out, not_27_out, not_28_out);
  and and_8 (and_8_out, not_29_out, not_30_out, not_31_out, not_32_out, not_33_out, not_34_out, not_35_out, not_36_out, not_37_out, not_38_out, F1, F0);
  and and_9 (and_9_out, not_39_out, not_40_out, not_41_out, not_42_out, not_43_out, not_44_out, not_45_out, not_46_out, not_47_out, not_48_out, F1, not_49_out);
  and and_10 (and_10_out, not_50_out, not_51_out, not_52_out, not_53_out, not_54_out, not_55_out, F5, not_56_out, not_57_out, not_58_out, not_59_out, not_60_out);
  and and_11 (and_11_out, not_61_out, not_62_out, not_63_out, not_64_out, not_65_out, not_66_out, F5, not_67_out, not_68_out, not_69_out, not_70_out, F0);
  and and_12 (and_12_out, not_71_out, not_72_out, not_73_out, not_74_out, not_75_out, not_76_out, F5, not_77_out, not_78_out, not_79_out, F1, not_80_out);
  and and_13 (and_13_out, not_81_out, not_82_out, not_83_out, not_84_out, not_85_out, not_86_out, F5, not_87_out, not_88_out, F2, not_89_out, not_90_out);
  and and_14 (and_14_out, not_91_out, not_92_out, not_93_out, not_94_out, not_95_out, not_96_out, F5, not_97_out, not_98_out, F2, not_99_out, F0);
  and and_15 (and_15_out, not_100_out, not_101_out, not_102_out, not_103_out, not_104_out, not_105_out, F5, not_106_out, not_107_out, F2, F1, F0);
  and and_16 (and_16_out, not_108_out, not_109_out, not_110_out, not_111_out, not_112_out, not_113_out, F5, not_114_out, F3, not_115_out, F1, not_116_out);
  and and_17 (and_17_out, not_117_out, not_118_out, not_119_out, not_120_out, not_121_out, not_122_out, F5, not_123_out, F3, not_124_out, F1, F0);
  and and_18 (and_18_out, not_125_out, not_126_out, not_127_out, not_128_out, OP1, OP0);
  and and_19 (and_19_out, not_129_out, not_130_out, OP3, not_131_out, not_132_out, not_133_out);
  and and_20 (and_20_out, not_134_out, not_135_out, OP3, OP2, not_136_out, not_137_out);
  and and_21 (and_21_out, not_138_out, not_139_out, OP3, not_140_out, not_141_out, OP0);
  and and_22 (and_22_out, not_142_out, not_143_out, OP3, not_144_out, OP1, not_145_out);
  and and_23 (and_23_out, not_146_out, not_147_out, OP3, OP2, not_148_out, OP0);
  and and_24 (and_24_out, OP5, not_149_out, not_150_out, not_151_out, OP1, OP0);
  and and_25 (and_25_out, not_152_out, not_153_out, not_154_out, not_155_out, not_156_out, not_157_out, not_158_out, not_159_out, not_160_out, F2, F1, not_161_out);
  and and_26 (and_26_out, not_162_out, not_163_out, OP3, not_164_out, OP1, OP0);
  and and_27 (and_27_out, OP5, not_165_out, not_166_out, not_167_out, not_168_out, OP0);
  and and_28 (and_28_out, not_169_out, not_170_out, not_171_out, not_172_out, not_173_out, not_174_out, not_175_out, not_176_out, not_177_out, F2, not_178_out, not_179_out);
  and and_29 (and_29_out, not_180_out, not_181_out, OP3, OP2, OP1, OP0);
  and and_30 (and_30_out, not_182_out, not_183_out, not_184_out, not_185_out, not_186_out, not_187_out, F5, not_188_out, not_189_out, F2, F1, not_190_out);
  and and_31 (SysCALL, not_191_out, not_192_out, not_193_out, not_194_out, not_195_out, not_196_out, not_197_out, not_198_out, F2, F3, not_199_out, not_200_out);
  and and_32 (and_32_out, not_201_out, OP3, not_202_out, not_203_out);
  and and_33 (and_33_out, OP0, not_204_out, not_205_out, not_206_out, OP5);
  or or_1 (SignedExt, and_32_out, and_33_out, and_34_out);
  and and_34 (and_34_out, OP0, OP1, not_207_out, not_208_out, OP5);
  and and_35 (and_35_out, not_209_out, not_210_out, not_211_out, not_212_out, not_213_out, not_214_out, not_215_out, not_216_out, not_217_out, not_218_out, not_219_out, not_220_out);
  and and_36 (and_36_out, not_221_out, not_222_out, not_223_out, not_224_out, not_225_out, not_226_out, not_227_out, not_228_out, not_229_out, not_230_out, F1, F0);
  and and_37 (and_37_out, not_231_out, not_232_out, not_233_out, not_234_out, not_235_out, not_236_out, not_237_out, not_238_out, not_239_out, not_240_out, F1, not_241_out);
  and and_38 (and_38_out, not_242_out, not_243_out, not_244_out, not_245_out, not_246_out, not_247_out, F5, not_248_out, not_249_out, not_250_out, not_251_out, not_252_out);
  and and_39 (and_39_out, not_253_out, not_254_out, not_255_out, not_256_out, not_257_out, not_258_out, F5, not_259_out, not_260_out, not_261_out, not_262_out, F0);
  and and_40 (and_40_out, not_263_out, not_264_out, not_265_out, not_266_out, not_267_out, not_268_out, F5, not_269_out, not_270_out, not_271_out, F1, not_272_out);
  and and_41 (and_41_out, not_273_out, not_274_out, not_275_out, not_276_out, not_277_out, not_278_out, F5, not_279_out, not_280_out, F2, not_281_out, not_282_out);
  and and_42 (and_42_out, not_283_out, not_284_out, not_285_out, not_286_out, not_287_out, not_288_out, F5, not_289_out, not_290_out, F2, not_291_out, F0);
  and and_43 (and_43_out, not_292_out, not_293_out, not_294_out, not_295_out, not_296_out, not_297_out, F5, not_298_out, not_299_out, F2, F1, F0);
  and and_44 (and_44_out, not_300_out, not_301_out, not_302_out, not_303_out, not_304_out, not_305_out, F5, not_306_out, F3, not_307_out, F1, not_308_out);
  and and_45 (and_45_out, not_309_out, not_310_out, not_311_out, not_312_out, not_313_out, not_314_out, F5, not_315_out, F3, not_316_out, F1, F0);
  and and_46 (and_46_out, not_317_out, not_318_out, not_319_out, not_320_out, not_321_out, not_322_out, not_323_out, not_324_out, not_325_out, F2, F1, not_326_out);
  and and_47 (and_47_out, not_327_out, not_328_out, not_329_out, not_330_out, not_331_out, not_332_out, not_333_out, not_334_out, not_335_out, F2, not_336_out, not_337_out);
  and and_48 (and_48_out, not_338_out, not_339_out, not_340_out, not_341_out, not_342_out, not_343_out, F5, not_344_out, not_345_out, F2, F1, not_346_out);
  and and_49 (BEQ, not_347_out, not_348_out, OP2, not_349_out, not_350_out, not_351_out);
  and and_50 (BNE, OP0, not_352_out, OP2, not_353_out, not_354_out, not_355_out);
  and and_51 (JR, not_356_out, not_357_out, not_358_out, not_359_out, not_360_out, not_361_out, not_362_out, not_363_out, not_364_out, F3, not_365_out, not_366_out);
  and and_52 (JUMP, not_367_out, OP1, not_368_out, not_369_out, not_370_out, not_371_out);
  and and_53 (JAL, OP0, OP1, not_372_out, not_373_out, not_374_out, not_375_out);
  or or_2 (ALU_SRC, and_3_out, and_4_out, and_5_out, and_6_out);
  or or_3 (RegWrite, and_7_out, and_8_out, and_9_out, and_10_out, and_11_out, and_12_out, and_13_out, and_14_out, and_15_out, and_16_out, and_17_out, and_18_out, and_19_out, and_20_out, and_21_out, and_22_out, and_23_out, and_24_out, and_25_out, and_26_out, and_27_out, and_28_out, and_29_out, and_30_out);
  or or_4 (RegDst, and_35_out, and_36_out, and_37_out, and_38_out, and_39_out, and_40_out, and_41_out, and_42_out, and_43_out, and_44_out, and_45_out, and_46_out, and_47_out, and_48_out);
endmodule

// ALU
module MIPS_ALU (
  input  [4:0] shamt,
  input  [31:0] X,
  input  [31:0] Y,
  input  [3:0] AluOP,
  output Equal,
  output [31:0] Result,
  output [31:0] Result_2
);

  wire [0:0] comparator_1_lt, comparator_2_lt;
  wire [31:0] adder_1_out, AND_out, divider_1_out, divider_1_rem, multiplier_1_cout, multiplier_1_out,
       NOR_out, OR_out, shifter_1_out, shifter_2_out, shifter_3_out, subtractor_1_out, XOR_out;

  assign AND_out = X & Y;  // AND_Gate AND, 32 bits wide
  assign OR_out = X | Y;  // OR_Gate OR, 32 bits wide
  Shifter #(.width(32), .shift("ll")) shifter_1 (.in(Y), .\dist (shamt), .out(shifter_1_out));
  Shifter #(.width(32), .shift("ar")) shifter_2 (.in(Y), .\dist (shamt), .out(shifter_2_out));
  Shifter #(.width(32), .shift("lr")) shifter_3 (.in(Y), .\dist (shamt), .out(shifter_3_out));
  Multiplier #(.width(32)) multiplier_1 (.a(X), .b(Y), .out(multiplier_1_out), .cout(multiplier_1_cout));  // open: cin
  Divider #(.width(32)) divider_1 (.a(X), .b(Y), .out(divider_1_out), .rem(divider_1_rem));  // open: upper
  Adder #(.width(32)) adder_1 (.a(X), .b(Y), .out(adder_1_out));  // open: cin, cout
  Subtractor #(.width(32)) subtractor_1 (.a(X), .b(Y), .out(subtractor_1_out));  // open: bin, bout
  assign XOR_out = X ^ Y;  // XOR_Gate XOR, 32 bits wide
  assign NOR_out = ~(X | Y);  // NOR_Gate NOR, 32 bits wide
  Comparator #(.width(32), .mode("twosComplement")) comparator_1 (
    .a(X), .b(Y), .eq(Equal), .lt(comparator_1_lt[0]));  // open: gt
  Comparator #(.width(32), .mode("unsigned")) comparator_2 (.a(X), .b(Y), .lt(comparator_2_lt[0]));  // open: gt, eq
  Multiplexer #(.select(4), .width(32), .disabled("Z"), .enable("false")) multiplexer_1 (
    .in0(shifter_1_out), .in1(shifter_2_out), .in2(shifter_3_out), .in3(multiplier_1_out),
    .in4(divider_1_out), .in5(adder_1_out), .in6(subtractor_1_out), .in7(AND_out), .in8(OR_out),
    .in9(XOR_out), .in10(NOR_out), .in11({{31{1'b0}}, comparator_1_lt[0]}),
    .in12({{31{1'b0}}, comparator_2_lt[0]}), .in13({32{1'b0}}), .in14({32{1'b0}}), .in15({32{1'b0}}),
    .out(Result), .sel(AluOP));
  Multiplexer #(.select(4), .width(32), .disabled("Z"), .enable("false")) multiplexer_2 (
    .in0({32{1'b0}}), .in1({32{1'b0}}), .in2({32{1'b0}}), .in3(multiplier_1_cout), .in4(divider_1_rem),
    .in5({32{1'b0}}), .in6({32{1'b0}}), .in7({32{1'b0}}), .in8({32{1'b0}}), .in9({32{1'b0}}),
    .in10({32{1'b0}}), .in11({32{1'b0}}), .in12({32{1'b0}}), .in13({32{1'b0}}), .in14({32{1'b0}}),
    .in15({32{1'b0}}), .out(Result_2), .sel(AluOP));

  // Other names for the same wires on the sheet: Result2[31:0] = Result_2; S[3:0] = AluOP

  // Notes on the sheet:
  //   不要改变此引脚区域内容，也不要改变ALU封装形式
  //   输入引脚
  //   输出引脚
endmodule

module MIPS_Regifile (
  input  [31:0] Din,
  input  Clk,
  input  WE,
  input  [4:0] R1_num,
  input  [4:0] W_num,
  input  [4:0] R2_num,
  output [31:0] R1,
  output [31:0] R2
);

  // RegisterFile registerfile_1: pin names not known; wires that end beside it: Din, Clk, WE, W_num, R1_num, R2_num, R1, R2
endmodule

// 新增控制信号生成
module \新增控制信号生成电路  (
  input  OP0,
  input  OP1,
  input  OP2,
  input  OP3,
  input  OP4,
  input  OP5,
  input  F0,
  input  F1,
  input  F2,
  input  F3,
  input  F4,
  input  F5,
  output BLTZ,
  output LH,
  output LUI,
  output SRLV,
  output SET_IE,
  output Clear_IR
);

  wire not_1_out, not_2_out, not_3_out, not_4_out, not_5_out, not_6_out, not_7_out, not_8_out, not_9_out,
       not_10_out, not_11_out, not_12_out, not_13_out, not_14_out, not_15_out, not_16_out, not_17_out,
       not_18_out, not_19_out, not_20_out, not_21_out, not_22_out, not_23_out, not_24_out, not_25_out,
       not_26_out, not_27_out, not_28_out, not_29_out, not_30_out, not_31_out, not_32_out, not_33_out,
       not_34_out, not_35_out, not_36_out, not_37_out, not_38_out, not_39_out;

  not not_1 (not_1_out, OP1);
  not not_2 (not_2_out, OP2);
  not not_3 (not_3_out, OP3);
  not not_4 (not_4_out, OP4);
  not not_5 (not_5_out, OP5);
  not not_6 (not_6_out, OP1);
  not not_7 (not_7_out, OP2);
  not not_8 (not_8_out, OP3);
  not not_9 (not_9_out, OP4);
  not not_10 (not_10_out, OP5);
  not not_11 (not_11_out, OP4);
  not not_12 (not_12_out, OP0);
  not not_13 (not_13_out, OP1);
  not not_14 (not_14_out, OP2);
  not not_15 (not_15_out, OP3);
  not not_16 (not_16_out, OP4);
  not not_17 (not_17_out, OP5);
  not not_18 (not_18_out, F0);
  not not_19 (not_19_out, F3);
  not not_20 (not_20_out, F4);
  not not_21 (not_21_out, F5);
  not not_22 (not_22_out, OP0);
  not not_23 (not_23_out, OP1);
  not not_24 (not_24_out, OP2);
  not not_25 (not_25_out, OP3);
  not not_26 (not_26_out, OP5);
  not not_27 (not_27_out, F0);
  not not_28 (not_28_out, F1);
  not not_29 (not_29_out, F2);
  not not_30 (not_30_out, F5);
  not not_31 (not_31_out, OP0);
  not not_32 (not_32_out, OP1);
  not not_33 (not_33_out, OP2);
  not not_34 (not_34_out, OP3);
  not not_35 (not_35_out, OP5);
  not not_36 (not_36_out, F0);
  not not_37 (not_37_out, F1);
  not not_38 (not_38_out, F2);
  not not_39 (not_39_out, F5);
  and and_1 (BLTZ, OP0, not_1_out, not_2_out, not_3_out, not_4_out, not_5_out);
  and and_2 (LH, OP0, not_6_out, not_7_out, not_8_out, not_9_out, OP5);
  and and_3 (LUI, not_10_out, not_11_out, OP3, OP2, OP1, OP0);
  and and_4 (SRLV, not_12_out, not_13_out, not_14_out, not_15_out, not_16_out, not_17_out, not_18_out, F2, not_19_out, not_20_out, not_21_out);
  and and_5 (SET_IE, not_22_out, not_23_out, not_24_out, not_25_out, OP4, not_26_out, not_27_out, not_28_out, not_29_out, F3, F4, not_30_out);
  and and_6 (Clear_IR, not_31_out, not_32_out, not_33_out, not_34_out, OP4, not_35_out, not_36_out, not_37_out, not_38_out, F3, F4, not_39_out);
endmodule

// 按键信号产生电路
module \中断按键信号产生电路  (
  input  CLK,
  input  \_1号中断 ,
  input  [2:0] target,
  input  Clear_IR,
  input  \_2号中断 ,
  input  \_3号中断 ,
  input  \_4号中断 ,
  input  \_5号中断 ,
  input  \_6号中断 ,
  input  RST,
  output \_1号中断等待指示灯 ,
  output \_2号中断等待指示灯 ,
  output [2:0] \中断号 ,
  output \_3号中断等待指示灯 ,
  output IR,
  output \_4号中断等待指示灯 ,
  output \_5号中断等待指示灯 ,
  output \_6号中断等待指示灯 
);

  wire and_1_out, and_2_out, and_3_out, and_4_out, and_5_out, and_6_out, comparator_1_eq, comparator_2_eq,
       comparator_3_eq, comparator_4_eq, comparator_5_eq, comparator_6_eq, d_ff_1_q, d_ff_2_q, d_ff_3_q,
       d_ff_4_q, d_ff_5_q, d_ff_6_q, I1, I2, I3, I4, I5, I6, or_7_out, or_8_out, or_9_out, or_10_out,
       or_11_out, or_12_out, pull_resistor_1_node, pull_resistor_2_node, pull_resistor_3_node,
       pull_resistor_4_node, pull_resistor_5_node, pull_resistor_6_node;

  D_Flip_Flop #(.trigger("rising"), .Pre_Clr_Positions("LEGACY"), .NegatePresetClear("false"), .enable("true"), .NewFFLayout("false")) d_ff_1 (
    .clk(\_1号中断 ), .D(1'b1), .Q(d_ff_1_q), .reset(I1));  // open: Qn, preset, en
  or or_1 (\_1号中断等待指示灯 , I1, d_ff_1_q);
  D_Flip_Flop #(.trigger("rising"), .Pre_Clr_Positions("LEGACY"), .NegatePresetClear("false"), .enable("true"), .NewFFLayout("false")) d_ff_2 (
    .clk(\_2号中断 ), .D(1'b1), .Q(d_ff_2_q), .reset(I2));  // open: Qn, preset, en
  or or_2 (\_2号中断等待指示灯 , I2, d_ff_2_q);
  D_Flip_Flop #(.trigger("rising"), .Pre_Clr_Positions("LEGACY"), .NegatePresetClear("false"), .enable("true"), .NewFFLayout("false")) d_ff_3 (
    .clk(\_3号中断 ), .D(1'b1), .Q(d_ff_3_q), .reset(I3));  // open: Qn, preset, en
  or or_3 (\_3号中断等待指示灯 , I3, d_ff_3_q);
  D_Flip_Flop #(.trigger("rising"), .Pre_Clr_Positions("LEGACY"), .NegatePresetClear("false"), .enable("true"), .NewFFLayout("false")) d_ff_4 (
    .clk(\_4号中断 ), .D(1'b1), .Q(d_ff_4_q), .reset(I4));  // open: Qn, preset, en
  or or_4 (\_4号中断等待指示灯 , I4, d_ff_4_q);
  D_Flip_Flop #(.trigger("rising"), .Pre_Clr_Positions("LEGACY"), .NegatePresetClear("false"), .enable("true"), .NewFFLayout("false")) d_ff_5 (
    .clk(\_5号中断 ), .D(1'b1), .Q(d_ff_5_q), .reset(I5));  // open: Qn, preset, en
  or or_5 (\_5号中断等待指示灯 , I5, d_ff_5_q);
  D_Flip_Flop #(.trigger("rising"), .Pre_Clr_Positions("LEGACY"), .NegatePresetClear("false"), .enable("true"), .NewFFLayout("false")) d_ff_6 (
    .clk(\_6号中断 ), .D(1'b1), .Q(d_ff_6_q), .reset(I6));  // open: Qn, preset, en
  or or_6 (\_6号中断等待指示灯 , I6, d_ff_6_q);
  or or_7 (or_7_out, d_ff_1_q, I1);
  and and_1 (and_1_out, or_7_out, ~pull_resistor_1_node);  // AND_Gate
  or or_8 (or_8_out, d_ff_2_q, I2);
  and and_2 (and_2_out, or_8_out, ~pull_resistor_2_node);  // AND_Gate
  or or_9 (or_9_out, d_ff_3_q, I3);
  and and_3 (and_3_out, or_9_out, ~pull_resistor_3_node);  // AND_Gate
  or or_10 (or_10_out, d_ff_4_q, I4);
  and and_4 (and_4_out, or_10_out, ~pull_resistor_4_node);  // AND_Gate
  or or_11 (or_11_out, d_ff_5_q, I5);
  and and_5 (and_5_out, or_11_out, ~pull_resistor_5_node);  // AND_Gate
  or or_12 (or_12_out, d_ff_6_q, I6);
  and and_6 (and_6_out, or_12_out, ~pull_resistor_6_node);  // AND_Gate
  D_Flip_Flop #(.trigger("rising"), .Pre_Clr_Positions("LEGACY"), .NegatePresetClear("false"), .enable("true"), .NewFFLayout("false")) IR1 (
    .clk(CLK), .D(and_1_out), .Q(I1), .reset(RST));  // open: Qn, preset, en
  D_Flip_Flop #(.trigger("rising"), .Pre_Clr_Positions("LEGACY"), .NegatePresetClear("false"), .enable("true"), .NewFFLayout("false")) IR2 (
    .clk(CLK), .D(and_2_out), .Q(I2), .reset(RST));  // open: Qn, preset, en
  D_Flip_Flop #(.trigger("rising"), .Pre_Clr_Positions("LEGACY"), .NegatePresetClear("false"), .enable("true"), .NewFFLayout("false")) IR3 (
    .clk(CLK), .D(and_3_out), .Q(I3), .reset(RST));  // open: Qn, preset, en
  D_Flip_Flop #(.trigger("rising"), .Pre_Clr_Positions("LEGACY"), .NegatePresetClear("false"), .enable("true"), .NewFFLayout("false")) IR4 (
    .clk(CLK), .D(and_4_out), .Q(I4), .reset(RST));  // open: Qn, preset, en
  D_Flip_Flop #(.trigger("rising"), .Pre_Clr_Positions("LEGACY"), .NegatePresetClear("false"), .enable("true"), .NewFFLayout("false")) IR5 (
    .clk(CLK), .D(and_5_out), .Q(I5), .reset(RST));  // open: Qn, preset, en
  D_Flip_Flop #(.trigger("rising"), .Pre_Clr_Positions("LEGACY"), .NegatePresetClear("false"), .enable("true"), .NewFFLayout("false")) IR6 (
    .clk(CLK), .D(and_6_out), .Q(I6), .reset(RST));  // open: Qn, preset, en
  Pull_Resistor #(.pull(0)) pull_resistor_1 (.node(pull_resistor_1_node));
  Pull_Resistor #(.pull(0)) pull_resistor_2 (.node(pull_resistor_2_node));
  Pull_Resistor #(.pull(0)) pull_resistor_3 (.node(pull_resistor_3_node));
  Pull_Resistor #(.pull(0)) pull_resistor_4 (.node(pull_resistor_4_node));
  Pull_Resistor #(.pull(0)) pull_resistor_5 (.node(pull_resistor_5_node));
  Pull_Resistor #(.pull(0)) pull_resistor_6 (.node(pull_resistor_6_node));
  Comparator #(.width(3), .mode("unsigned")) comparator_1 (
    .a(target), .b(3'b001), .eq(comparator_1_eq));  // open: gt, lt
  Comparator #(.width(3), .mode("unsigned")) comparator_2 (
    .a(target), .b(3'b010), .eq(comparator_2_eq));  // open: gt, lt
  Comparator #(.width(3), .mode("unsigned")) comparator_3 (
    .a(target), .b(3'b011), .eq(comparator_3_eq));  // open: gt, lt
  Comparator #(.width(3), .mode("unsigned")) comparator_4 (
    .a(target), .b(3'b100), .eq(comparator_4_eq));  // open: gt, lt
  Comparator #(.width(3), .mode("unsigned")) comparator_5 (
    .a(target), .b(3'b101), .eq(comparator_5_eq));  // open: gt, lt
  Comparator #(.width(3), .mode("unsigned")) comparator_6 (
    .a(target), .b(3'b110), .eq(comparator_6_eq));  // open: gt, lt
  assign pull_resistor_1_node = comparator_1_eq ? Clear_IR : 1'bz;  // Controlled_Buffer controlled_buffer_1
  assign pull_resistor_2_node = comparator_2_eq ? Clear_IR : 1'bz;  // Controlled_Buffer controlled_buffer_2
  assign pull_resistor_3_node = comparator_3_eq ? Clear_IR : 1'bz;  // Controlled_Buffer controlled_buffer_3
  assign pull_resistor_4_node = comparator_4_eq ? Clear_IR : 1'bz;  // Controlled_Buffer controlled_buffer_4
  assign pull_resistor_5_node = comparator_5_eq ? Clear_IR : 1'bz;  // Controlled_Buffer controlled_buffer_5
  assign pull_resistor_6_node = comparator_6_eq ? Clear_IR : 1'bz;  // Controlled_Buffer controlled_buffer_6
  or or_13 (IR, I1, I2, I3, I4, I5, I6);
  Priority_Encoder #(.select(3), .disabled("Z")) priority_encoder_1 (
    .in0(1'b1), .in1(I1), .in2(I2), .in3(I3), .in4(I4), .in5(I5), .in6(I6), .out(\中断号 ), .en_in(1'b1));  // open: in7, gs, en_out

  // Notes on the sheet:
  //   Reset 
  //   Reset 
  //   Reset 
endmodule

module \地图备份寄存器堆_32  (
  input  \写使能 ,
  input  [9:0] Addr,
  input  CLK,
  input  RST,
  input  [31:0] Data,
  output [31:0] \行1 ,
  output [31:0] \行9 ,
  output [31:0] \行17 ,
  output [31:0] \行25 ,
  output [31:0] \行2 ,
  output [31:0] \行10 ,
  output [31:0] \行18 ,
  output [31:0] \行26 ,
  output [31:0] \行3 ,
  output [31:0] \行11 ,
  output [31:0] \行19 ,
  output [31:0] \行27 ,
  output [31:0] \行4 ,
  output [31:0] \行12 ,
  output [31:0] \行20 ,
  output [31:0] \行28 ,
  output [31:0] \行5 ,
  output [31:0] \行13 ,
  output [31:0] \行21 ,
  output [31:0] \行29 ,
  output [31:0] \行6 ,
  output [31:0] \行14 ,
  output [31:0] \行22 ,
  output [31:0] \行30 ,
  output [31:0] \行7 ,
  output [31:0] \行15 ,
  output [31:0] \行23 ,
  output [31:0] \行31 ,
  output [31:0] \行8 ,
  output [31:0] \行16 ,
  output [31:0] \行24 ,
  output [31:0] \行32 
);

  wire and_1_out, and_2_out, and_3_out, and_4_out, and_5_out, and_6_out, and_7_out, and_8_out, and_9_out,
       and_10_out, and_11_out, and_12_out, and_13_out, and_14_out, and_15_out, and_16_out, and_17_out,
       and_18_out, and_19_out, and_20_out, and_21_out, and_22_out, and_23_out, and_24_out, and_25_out,
       and_26_out, and_27_out, and_28_out, and_29_out, and_30_out, and_31_out, and_32_out, \行1_t , \行2_t ,
       \行3_t , \行4_t , \行5_t , \行6_t , \行7_t , \行8_t , \行9_t , \行10_t , \行11_t , \行12_t , \行13_t , \行14_t ,
       \行15_t , \行16_t , \行17_t , \行18_t , \行19_t , \行20_t , \行21_t , \行22_t , \行23_t , \行24_t , \行25_t ,
       \行26_t , \行27_t , \行28_t , \行29_t , \行30_t , \行31_t , \行32_t ;

  and and_1 (and_1_out, \写使能 , \行1_t );
  and and_2 (and_2_out, \写使能 , \行2_t );
  and and_3 (and_3_out, \写使能 , \行3_t );
  and and_4 (and_4_out, \写使能 , \行4_t );
  and and_5 (and_5_out, \写使能 , \行5_t );
  and and_6 (and_6_out, \写使能 , \行6_t );
  and and_7 (and_7_out, \写使能 , \行7_t );
  and and_8 (and_8_out, \写使能 , \行8_t );
  Register #(.width(32), .trigger("rising"), .Select("low")) register_1 (
    .D(Data), .en(and_1_out), .Q(\行1 ), .clk(CLK), .clr(RST));
  Register #(.width(32), .trigger("rising"), .Select("low")) register_2 (
    .D(Data), .en(and_2_out), .Q(\行2 ), .clk(CLK), .clr(RST));
  Register #(.width(32), .trigger("rising"), .Select("low")) register_3 (
    .D(Data), .en(and_3_out), .Q(\行3 ), .clk(CLK), .clr(RST));
  Register #(.width(32), .trigger("rising"), .Select("low")) register_4 (
    .D(Data), .en(and_4_out), .Q(\行4 ), .clk(CLK), .clr(RST));
  Register #(.width(32), .trigger("rising"), .Select("low")) register_5 (
    .D(Data), .en(and_5_out), .Q(\行5 ), .clk(CLK), .clr(RST));
  Register #(.width(32), .trigger("rising"), .Select("low")) register_6 (
    .D(Data), .en(and_6_out), .Q(\行6 ), .clk(CLK), .clr(RST));
  Register #(.width(32), .trigger("rising"), .Select("low")) register_7 (
    .D(Data), .en(and_7_out), .Q(\行7 ), .clk(CLK), .clr(RST));
  Register #(.width(32), .trigger("rising"), .Select("low")) register_8 (
    .D(Data), .en(and_8_out), .Q(\行8 ), .clk(CLK), .clr(RST));
  and and_9 (and_9_out, \写使能 , \行9_t );
  and and_10 (and_10_out, \写使能 , \行10_t );
  and and_11 (and_11_out, \写使能 , \行11_t );
  and and_12 (and_12_out, \写使能 , \行12_t );
  and and_13 (and_13_out, \写使能 , \行13_t );
  and and_14 (and_14_out, \写使能 , \行14_t );
  and and_15 (and_15_out, \写使能 , \行15_t );
  and and_16 (and_16_out, \写使能 , \行16_t );
  Register #(.width(32), .trigger("rising"), .Select("low")) register_9 (
    .D(Data), .en(and_9_out), .Q(\行9 ), .clk(CLK), .clr(RST));
  Register #(.width(32), .trigger("rising"), .Select("low")) register_10 (
    .D(Data), .en(and_10_out), .Q(\行10 ), .clk(CLK), .clr(RST));
  Register #(.width(32), .trigger("rising"), .Select("low")) register_11 (
    .D(Data), .en(and_11_out), .Q(\行11 ), .clk(CLK), .clr(RST));
  Register #(.width(32), .trigger("rising"), .Select("low")) register_12 (
    .D(Data), .en(and_12_out), .Q(\行12 ), .clk(CLK), .clr(RST));
  Register #(.width(32), .trigger("rising"), .Select("low")) register_13 (
    .D(Data), .en(and_13_out), .Q(\行13 ), .clk(CLK), .clr(RST));
  Register #(.width(32), .trigger("rising"), .Select("low")) register_14 (
    .D(Data), .en(and_14_out), .Q(\行14 ), .clk(CLK), .clr(RST));
  Register #(.width(32), .trigger("rising"), .Select("low")) register_15 (
    .D(Data), .en(and_15_out), .Q(\行15 ), .clk(CLK), .clr(RST));
  Register #(.width(32), .trigger("rising"), .Select("low")) register_16 (
    .D(Data), .en(and_16_out), .Q(\行16 ), .clk(CLK), .clr(RST));
  and and_17 (and_17_out, \写使能 , \行17_t );
  and and_18 (and_18_out, \写使能 , \行18_t );
  and and_19 (and_19_out, \写使能 , \行19_t );
  and and_20 (and_20_out, \写使能 , \行20_t );
  and and_21 (and_21_out, \写使能 , \行21_t );
  and and_22 (and_22_out, \写使能 , \行22_t );
  and and_23 (and_23_out, \写使能 , \行23_t );
  and and_24 (and_24_out, \写使能 , \行24_t );
  Register #(.width(32), .trigger("rising"), .Select("low")) register_17 (
    .D(Data), .en(and_17_out), .Q(\行17 ), .clk(CLK), .clr(RST));
  Register #(.width(32), .trigger("rising"), .Select("low")) register_18 (
    .D(Data), .en(and_18_out), .Q(\行18 ), .clk(CLK), .clr(RST));
  Register #(.width(32), .trigger("rising"), .Select("low")) register_19 (
    .D(Data), .en(and_19_out), .Q(\行19 ), .clk(CLK), .clr(RST));
  Register #(.width(32), .trigger("rising"), .Select("low")) register_20 (
    .D(Data), .en(and_20_out), .Q(\行20 ), .clk(CLK), .clr(RST));
  Register #(.width(32), .trigger("rising"), .Select("low")) register_21 (
    .D(Data), .en(and_21_out), .Q(\行21 ), .clk(CLK), .clr(RST));
  Register #(.width(32), .trigger("rising"), .Select("low")) register_22 (
    .D(Data), .en(and_22_out), .Q(\行22 ), .clk(CLK), .clr(RST));
  Register #(.width(32), .trigger("rising"), .Select("low")) register_23 (
    .D(Data), .en(and_23_out), .Q(\行23 ), .clk(CLK), .clr(RST));
  Register #(.width(32), .trigger("rising"), .Select("low")) register_24 (
    .D(Data), .en(and_24_out), .Q(\行24 ), .clk(CLK), .clr(RST));
  and and_25 (and_25_out, \写使能 , \行25_t );
  and and_26 (and_26_out, \写使能 , \行26_t );
  and and_27 (and_27_out, \写使能 , \行27_t );
  and and_28 (and_28_out, \写使能 , \行28_t );
  and and_29 (and_29_out, \写使能 , \行29_t );
  and and_30 (and_30_out, \写使能 , \行30_t );
  and and_31 (and_31_out, \写使能 , \行31_t );
  and and_32 (and_32_out, \写使能 , \行32_t );
  Register #(.width(32), .trigger("rising"), .Select("low")) register_25 (
    .D(Data), .en(and_25_out), .Q(\行25 ), .clk(CLK), .clr(RST));
  Register #(.width(32), .trigger("rising"), .Select("low")) register_26 (
    .D(Data), .en(and_26_out), .Q(\行26 ), .clk(CLK), .clr(RST));
  Register #(.width(32), .trigger("rising"), .Select("low")) register_27 (
    .D(Data), .en(and_27_out), .Q(\行27 ), .clk(CLK), .clr(RST));
  Register #(.width(32), .trigger("rising"), .Select("low")) register_28 (
    .D(Data), .en(and_28_out), .Q(\行28 ), .clk(CLK), .clr(RST));
  Register #(.width(32), .trigger("rising"), .Select("low")) register_29 (
    .D(Data), .en(and_29_out), .Q(\行29 ), .clk(CLK), .clr(RST));
  Register #(.width(32), .trigger("rising"), .Select("low")) register_30 (
    .D(Data), .en(and_30_out), .Q(\行30 ), .clk(CLK), .clr(RST));
  Register #(.width(32), .trigger("rising"), .Select("low")) register_31 (
    .D(Data), .en(and_31_out), .Q(\行31 ), .clk(CLK), .clr(RST));
  Register #(.width(32), .trigger("rising"), .Select("low")) register_32 (
    .D(Data), .en(and_32_out), .Q(\行32 ), .clk(CLK), .clr(RST));
  Demultiplexer #(.select(5), .width(1), .tristate("false"), .disabled("Z"), .enable("false")) demultiplexer_1 (
    .out0(\行1_t ), .out1(\行2_t ), .out2(\行3_t ), .out3(\行4_t ), .out4(\行5_t ), .out5(\行6_t ), .out6(\行7_t ),
    .out7(\行8_t ), .out8(\行9_t ), .out9(\行10_t ), .out10(\行11_t ), .out11(\行12_t ), .out12(\行13_t ),
    .out13(\行14_t ), .out14(\行15_t ), .out15(\行16_t ), .out16(\行17_t ), .out17(\行18_t ), .out18(\行19_t ),
    .out19(\行20_t ), .out20(\行21_t ), .out21(\行22_t ), .out22(\行23_t ), .out23(\行24_t ), .out24(\行25_t ),
    .out25(\行26_t ), .out26(\行27_t ), .out27(\行28_t ), .out28(\行29_t ), .out29(\行30_t ), .out30(\行31_t ),
    .out31(\行32_t ), .in(1'b1), .sel(Addr[4:0]));
endmodule

module \玩家交互电路  (
);

  wire and_1_out, CLK, comparator_1_eq, comparator_1_lt, not_1_out, or_1_out, RST, \上 , \下 , \关卡1 , \关卡2 ,
       \减速_out , \加速_out , \右 , \左 , \点阵显示_1_success , \点阵显示_1_得分 , \点阵显示_1_警报 , \音乐_1_enable , \音乐_1_音量 ;
  wire [6:0] keyboard_1_data;
  wire [7:0] counter_2_q;
  wire [13:0] \音乐_1_out_5 , \音乐_1_out_8 ;
  wire [15:0] \速度 , \速度初始 ;
  wire [31:0] \点阵显示_1__1 , \点阵显示_1__2 , \点阵显示_1__3 , \点阵显示_1__4 , \点阵显示_1__5 , \点阵显示_1__6 , \点阵显示_1__7 ,
       \点阵显示_1__8 , \点阵显示_1__9 , \点阵显示_1__10 , \点阵显示_1__11 , \点阵显示_1__12 , \点阵显示_1__13 , \点阵显示_1__14 ,
       \点阵显示_1__15 , \点阵显示_1__16 , \点阵显示_1__17 , \点阵显示_1__18 , \点阵显示_1__19 , \点阵显示_1__20 , \点阵显示_1__21 ,
       \点阵显示_1__22 , \点阵显示_1__23 , \点阵显示_1__24 , \点阵显示_1__25 , \点阵显示_1__26 , \点阵显示_1__27 , \点阵显示_1__28 ,
       \点阵显示_1__29 , \点阵显示_1__30 , \点阵显示_1__31 , \点阵显示_1__32 ;

  Comparator #(.width(16), .mode("twosComplement")) comparator_1 (
    .a(\速度初始 ), .b(16'h1), .eq(comparator_1_eq), .lt(comparator_1_lt));  // open: gt
  not not_1 (not_1_out, comparator_1_eq);
  and and_1 (and_1_out, not_1_out, \加速_out );
  Button \u_加速  (.out(\加速_out ));
  Multiplexer #(.select(1), .width(16), .disabled("Z"), .enable("false")) multiplexer_1 (
    .in0(\速度初始 ), .in1(16'h1), .out(\速度 ), .sel(comparator_1_lt));
  Counter #(.width(16), .max('hffff), .ongoal("wrap"), .trigger("rising"), .behavior("new")) counter_1 (
    .load(comparator_1_lt), .D(16'h1), .Q(\速度初始 ), .clk(or_1_out), .down(and_1_out));  // open: count, carry, clr, preset
  or or_1 (or_1_out, and_1_out, \减速_out );
  Button \u_减速  (.out(\减速_out ));
  \点阵显示  \u_点阵显示_1  (
    .\开始 (\关卡1 ), .CLK(CLK), .RST(RST), .\金币速度 (\速度 ), .\上 (\上 ), .\下 (\下 ), .success(\点阵显示_1_success ),
    .\警报 (\点阵显示_1_警报 ), ._1(\点阵显示_1__1 ), ._2(\点阵显示_1__2 ), ._3(\点阵显示_1__3 ), ._4(\点阵显示_1__4 ),
    ._5(\点阵显示_1__5 ), ._6(\点阵显示_1__6 ), ._7(\点阵显示_1__7 ), ._8(\点阵显示_1__8 ), ._9(\点阵显示_1__9 ),
    ._10(\点阵显示_1__10 ), ._11(\点阵显示_1__11 ), ._12(\点阵显示_1__12 ), ._13(\点阵显示_1__13 ), ._14(\点阵显示_1__14 ),
    ._15(\点阵显示_1__15 ), ._16(\点阵显示_1__16 ), ._17(\点阵显示_1__17 ), ._18(\点阵显示_1__18 ), ._19(\点阵显示_1__19 ),
    ._20(\点阵显示_1__20 ), ._21(\点阵显示_1__21 ), ._22(\点阵显示_1__22 ), ._23(\点阵显示_1__23 ), ._24(\点阵显示_1__24 ),
    ._25(\点阵显示_1__25 ), ._26(\点阵显示_1__26 ), ._27(\点阵显示_1__27 ), ._28(\点阵显示_1__28 ), ._29(\点阵显示_1__29 ),
    ._30(\点阵显示_1__30 ), ._31(\点阵显示_1__31 ), ._32(\点阵显示_1__32 ), .\得分 (\点阵显示_1_得分 ));
  Button button_1 (.out(\关卡1 ));
  Button button_2 (.out(\关卡2 ));
  Button button_3 (.out(RST));
  Clock #(.highDuration(1), .lowDuration(1)) clock_1 (.out(CLK));
  DotMatrix #(.inputtype("row"), .matrixcols(32), .matrixrows(32), .persist(0), .dotshape("square")) dotmatrix_1 (
    .row0(\点阵显示_1__1 ), .row1(\点阵显示_1__2 ), .row2(\点阵显示_1__3 ), .row3(\点阵显示_1__4 ), .row4(\点阵显示_1__5 ),
    .row5(\点阵显示_1__6 ), .row6(\点阵显示_1__7 ), .row7(\点阵显示_1__8 ), .row8(\点阵显示_1__9 ), .row9(\点阵显示_1__10 ),
    .row10(\点阵显示_1__11 ), .row11(\点阵显示_1__12 ), .row12(\点阵显示_1__13 ), .row13(\点阵显示_1__14 ),
    .row14(\点阵显示_1__15 ), .row15(\点阵显示_1__16 ), .row16(\点阵显示_1__17 ), .row17(\点阵显示_1__18 ),
    .row18(\点阵显示_1__19 ), .row19(\点阵显示_1__20 ), .row20(\点阵显示_1__21 ), .row21(\点阵显示_1__22 ),
    .row22(\点阵显示_1__23 ), .row23(\点阵显示_1__24 ), .row24(\点阵显示_1__25 ), .row25(\点阵显示_1__26 ),
    .row26(\点阵显示_1__27 ), .row27(\点阵显示_1__28 ), .row28(\点阵显示_1__29 ), .row29(\点阵显示_1__30 ),
    .row30(\点阵显示_1__31 ), .row31(\点阵显示_1__32 ));
  Keyboard #(.Char_bit_width(7), .buflen(32), .trigger("rising")) keyboard_1 (
    .clk(CLK), .clr(RST), .data(keyboard_1_data));  // open: re, avail
  \键盘逻辑  \u_键盘逻辑_1  (
    .CLK(CLK), .UP_W(\上 ), .Down_S(\下 ), .Left_A(\左 ), .Right_D(\右 ), .\键盘输入 (keyboard_1_data), .RST(RST));
  LED #(.active("true")) led_1 (.in(\点阵显示_1_得分 ));
  Counter #(.width(8), .max('hff), .ongoal("wrap"), .trigger("rising"), .behavior("old")) counter_2 (
    .count(1'b1), .Q(counter_2_q), .clk(\点阵显示_1_得分 ), .clr(RST));  // open: load, D, carry, preset
  Hex_Digit_Display hex_digit_display_1 (.value(counter_2_q[7:4]));  // open: dp
  \音乐  \u_音乐_1  (
    .\频率延缓倍数 (16'hfa), .play(\点阵显示_1_success ), .out_5(\音乐_1_out_5 ), .Enable(\音乐_1_enable ),
    .out_8(\音乐_1_out_8 ), .CLK(CLK), .RST(RST), .\音量 (\音乐_1_音量 ));
  LED #(.active("true")) led_2 (.in(\点阵显示_1_警报 ));
  Hex_Digit_Display hex_digit_display_2 (.value(counter_2_q[3:0]));  // open: dp
  // Buzzer #(.freq_measure("Hz"), .vol_width(1)) 主调: pin names not known; wires that end beside it: \音乐_1_out_5 , \音乐_1_enable , \音乐_1_音量 
  // Buzzer #(.freq_measure("Hz"), .vol_width(1)) 伴奏: pin names not known; wires that end beside it: \音乐_1_out_8 , \音乐_1_enable , \音乐_1_音量 
  // Buzzer #(.freq_measure("Hz"), .vol_width(1)) 警告: pin names not known; wires that end beside it: 14'hfff, \点阵显示_1_警报 , \点阵显示_1_警报 
endmodule

module \点阵显示寄存器堆_32  (
  input  \写使能 ,
  input  [31:0] _1,
  input  [31:0] _2,
  input  [31:0] _3,
  input  [31:0] _4,
  input  [31:0] _5,
  input  [31:0] _6,
  input  [31:0] _7,
  input  [31:0] _8,
  input  [31:0] _9,
  input  [31:0] _10,
  input  [31:0] _11,
  input  [31:0] _12,
  input  [31:0] _13,
  input  [31:0] _14,
  input  [31:0] _15,
  input  [31:0] _16,
  input  [31:0] _17,
  input  [31:0] _18,
  input  [31:0] _19,
  input  [31:0] _20,
  input  [31:0] _21,
  input  [31:0] _22,
  input  [31:0] _23,
  input  [31:0] _24,
  input  [31:0] _25,
  input  [31:0] _26,
  input  [31:0] _27,
  input  [31:0] _28,
  input  [31:0] _29,
  input  [31:0] _30,
  input  [31:0] _31,
  input  [31:0] _32,
  input  CLK,
  input  RST,
  output [31:0] _1_2,
  output [31:0] _2_2,
  output [31:0] _3_2,
  output [31:0] _4_2,
  output [31:0] _5_2,
  output [31:0] _6_2,
  output [31:0] _7_2,
  output [31:0] _8_2,
  output [31:0] _9_2,
  output [31:0] _10_2,
  output [31:0] _11_2,
  output [31:0] _12_2,
  output [31:0] _13_2,
  output [31:0] _14_2,
  output [31:0] _15_2,
  output [31:0] _16_2,
  output [31:0] _17_2,
  output [31:0] _18_2,
  output [31:0] _19_2,
  output [31:0] _20_2,
  output [31:0] _21_2,
  output [31:0] _22_2,
  output [31:0] _23_2,
  output [31:0] _24_2,
  output [31:0] _25_2,
  output [31:0] _26_2,
  output [31:0] _27_2,
  output [31:0] _28_2,
  output [31:0] _29_2,
  output [31:0] _30_2,
  output [31:0] _31_2,
  output [31:0] _32_2
);

  Register #(.width(32), .trigger("rising"), .Select("low")) register_1 (
    .D(_1), .en(\写使能 ), .Q(_1_2), .clk(CLK), .clr(RST));
  Register #(.width(32), .trigger("rising"), .Select("low")) register_2 (
    .D(_5), .en(\写使能 ), .Q(_5_2), .clk(CLK), .clr(RST));
  Register #(.width(32), .trigger("rising"), .Select("low")) register_3 (
    .D(_9), .en(\写使能 ), .Q(_9_2), .clk(CLK), .clr(RST));
  Register #(.width(32), .trigger("rising"), .Select("low")) register_4 (
    .D(_13), .en(\写使能 ), .Q(_13_2), .clk(CLK), .clr(RST));
  Register #(.width(32), .trigger("rising"), .Select("low")) register_5 (
    .D(_17), .en(\写使能 ), .Q(_17_2), .clk(CLK), .clr(RST));
  Register #(.width(32), .trigger("rising"), .Select("low")) register_6 (
    .D(_21), .en(\写使能 ), .Q(_21_2), .clk(CLK), .clr(RST));
  Register #(.width(32), .trigger("rising"), .Select("low")) register_7 (
    .D(_25), .en(\写使能 ), .Q(_25_2), .clk(CLK), .clr(RST));
  Register #(.width(32), .trigger("rising"), .Select("low")) register_8 (
    .D(_29), .en(\写使能 ), .Q(_29_2), .clk(CLK), .clr(RST));
  Register #(.width(32), .trigger("rising"), .Select("low")) register_9 (
    .D(_2), .en(\写使能 ), .Q(_2_2), .clk(CLK), .clr(RST));
  Register #(.width(32), .trigger("rising"), .Select("low")) register_10 (
    .D(_6), .en(\写使能 ), .Q(_6_2), .clk(CLK), .clr(RST));
  Register #(.width(32), .trigger("rising"), .Select("low")) register_11 (
    .D(_10), .en(\写使能 ), .Q(_10_2), .clk(CLK), .clr(RST));
  Register #(.width(32), .trigger("rising"), .Select("low")) register_12 (
    .D(_14), .en(\写使能 ), .Q(_14_2), .clk(CLK), .clr(RST));
  Register #(.width(32), .trigger("rising"), .Select("low")) register_13 (
    .D(_18), .en(\写使能 ), .Q(_18_2), .clk(CLK), .clr(RST));
  Register #(.width(32), .trigger("rising"), .Select("low")) register_14 (
    .D(_22), .en(\写使能 ), .Q(_22_2), .clk(CLK), .clr(RST));
  Register #(.width(32), .trigger("rising"), .Select("low")) register_15 (
    .D(_26), .en(\写使能 ), .Q(_26_2), .clk(CLK), .clr(RST));
  Register #(.width(32), .trigger("rising"), .Select("low")) register_16 (
    .D(_30), .en(\写使能 ), .Q(_30_2), .clk(CLK), .clr(RST));
  Register #(.width(32), .trigger("rising"), .Select("low")) register_17 (
    .D(_3), .en(\写使能 ), .Q(_3_2), .clk(CLK), .clr(RST));
  Register #(.width(32), .trigger("rising"), .Select("low")) register_18 (
    .D(_7), .en(\写使能 ), .Q(_7_2), .clk(CLK), .clr(RST));
  Register #(.width(32), .trigger("rising"), .Select("low")) register_19 (
    .D(_11), .en(\写使能 ), .Q(_11_2), .clk(CLK), .clr(RST));
  Register #(.width(32), .trigger("rising"), .Select("low")) register_20 (
    .D(_15), .en(\写使能 ), .Q(_15_2), .clk(CLK), .clr(RST));
  Register #(.width(32), .trigger("rising"), .Select("low")) register_21 (
    .D(_19), .en(\写使能 ), .Q(_19_2), .clk(CLK), .clr(RST));
  Register #(.width(32), .trigger("rising"), .Select("low")) register_22 (
    .D(_23), .en(\写使能 ), .Q(_23_2), .clk(CLK), .clr(RST));
  Register #(.width(32), .trigger("rising"), .Select("low")) register_23 (
    .D(_27), .en(\写使能 ), .Q(_27_2), .clk(CLK), .clr(RST));
  Register #(.width(32), .trigger("rising"), .Select("low")) register_24 (
    .D(_31), .en(\写使能 ), .Q(_31_2), .clk(CLK), .clr(RST));
  Register #(.width(32), .trigger("rising"), .Select("low")) register_25 (
    .D(_4), .en(\写使能 ), .Q(_4_2), .clk(CLK), .clr(RST));
  Register #(.width(32), .trigger("rising"), .Select("low")) register_26 (
    .D(_8), .en(\写使能 ), .Q(_8_2), .clk(CLK), .clr(RST));
  Register #(.width(32), .trigger("rising"), .Select("low")) register_27 (
    .D(_12), .en(\写使能 ), .Q(_12_2), .clk(CLK), .clr(RST));
  Register #(.width(32), .trigger("rising"), .Select("low")) register_28 (
    .D(_16), .en(\写使能 ), .Q(_16_2), .clk(CLK), .clr(RST));
  Register #(.width(32), .trigger("rising"), .Select("low")) register_29 (
    .D(_20), .en(\写使能 ), .Q(_20_2), .clk(CLK), .clr(RST));
  Register #(.width(32), .trigger("rising"), .Select("low")) register_30 (
    .D(_24), .en(\写使能 ), .Q(_24_2), .clk(CLK), .clr(RST));
  Register #(.width(32), .trigger("rising"), .Select("low")) register_31 (
    .D(_28), .en(\写使能 ), .Q(_28_2), .clk(CLK), .clr(RST));
  Register #(.width(32), .trigger("rising"), .Select("low")) register_32 (
    .D(_32), .en(\写使能 ), .Q(_32_2), .clk(CLK), .clr(RST));
endmodule

// 键盘解析
module \键盘逻辑  (
  input  [6:0] \键盘输入 ,
  input  CLK,
  input  RST,
  output UP_W,
  output Down_S,
  output Left_A,
  output Right_D
);

  wire comparator_1_eq, comparator_2_eq, comparator_3_eq, comparator_4_eq;

  Comparator #(.width(7), .mode("twosComplement")) comparator_1 (
    .a(\键盘输入 ), .b(7'b1110111), .eq(comparator_1_eq));  // open: gt, lt
  Comparator #(.width(7), .mode("twosComplement")) comparator_2 (
    .a(\键盘输入 ), .b(7'b1110011), .eq(comparator_2_eq));  // open: gt, lt
  Comparator #(.width(7), .mode("twosComplement")) comparator_3 (
    .a(\键盘输入 ), .b(7'b1100001), .eq(comparator_3_eq));  // open: gt, lt
  Comparator #(.width(7), .mode("twosComplement")) comparator_4 (
    .a(\键盘输入 ), .b(7'b1100100), .eq(comparator_4_eq));  // open: gt, lt
  Register #(.width(1), .trigger("rising"), .Select("low")) register_1 (
    .D(comparator_1_eq), .Q(UP_W), .clk(CLK), .clr(RST));  // open: en
  Register #(.width(1), .trigger("rising"), .Select("low")) register_2 (
    .D(comparator_2_eq), .Q(Down_S), .clk(CLK), .clr(RST));  // open: en
  Register #(.width(1), .trigger("rising"), .Select("low")) register_3 (
    .D(comparator_3_eq), .Q(Left_A), .clk(CLK), .clr(RST));  // open: en
  Register #(.width(1), .trigger("rising"), .Select("low")) register_4 (
    .D(comparator_4_eq), .Q(Right_D), .clk(CLK), .clr(RST));  // open: en
endmodule

// DMA
module \音乐  (
  input  [15:0] \频率延缓倍数 ,
  input  CLK,
  input  play,
  input  RST,
  output [13:0] out_5,
  output Enable,
  output \音量 ,
  output [13:0] out_8
);

  wire Now_CLK;
  wire [31:0] adder_1_out, PC_q;
  wire [31:14] \主_data , \伴奏_data ;

  Register #(.width(32), .trigger("rising"), .Select("low")) PC (
    .D(adder_1_out), .en(play), .Q(PC_q), .clk(Now_CLK), .clr(RST));
  \频率转换  \u_频率转换_1  (.\延缓倍数 (\频率延缓倍数 ), .\原CLK (CLK), .RST(RST), .\后CLK (Now_CLK));
  Adder #(.width(32)) adder_1 (.a(PC_q), .b(32'h4), .out(adder_1_out), .cout(RST));  // open: cin
  ROM #(.addrWidth(10), .dataWidth(32), .Select("high")) \u_主  (.addr(PC_q[11:2]), .data({\主_data , out_5}));
  ROM #(.addrWidth(10), .dataWidth(32), .Select("high")) \u_伴奏  (.addr(PC_q[11:2]), .data({\伴奏_data , out_8}));

  assign Enable = play;
  assign \音量  = play;

  // Notes on the sheet:
  //   建议频率:转换后：16Hz
  //   contents of 主 (hex, n*v repeats v):
  //   20b 20b 20b 0 20b 20b 20b 0 310 310 310 0 310 310 310 0 370 370 370 0 370 370 370 0 310 310 310 5*0
  //   2ba 2ba 2ba 0 2ba 2ba 2ba 0 293 293 293 0 293 293 293 0 24b 24b 24b 0 24b 24b 24b 0 20b 20b 20b 5*0
  //   310 310 310 0 310 310 310 0 2ba 2ba 2ba 0 2ba 2ba 2ba 0 293 293 293 0 293 293 293 0 24b 24b 24b 5*0
  //   310 310 310 0 310 310 310 0 2ba 2ba 2ba 0 2ba 2ba 2ba 0 293 293 293 0 293 293 293 0 24b 24b 24b 5*0
  //   20b 20b 20b 0 20b 20b 20b 0 310 310 310 0 310 310 310 0 370 370 370 0 370 370 370 0 310 310 310 5*0
  //   2ba 2ba 2ba 0 2ba 2ba 2ba 0 293 293 293 0 293 293 293 0 24b 24b 24b 0 24b 24b 24b 0 20b 20b 20b
  //   contents of 伴奏 (hex, n*v repeats v):
  //   106 106 188 188 14a 14a 188 188 106 106 188 188 14a 14a 188 188 106 106 1b8 1b8 15d 15d 1b8 1b8 106
  //   106 188 188 14a 14a 188 188 e9 e9 188 188 126 126 188 188 106 106 188 188 14a 14a 188 188 e9 e9 188
  //   188 126 126 188 188 106 106 188 188 14a 14a 188 188 106 106 188 188 14a 14a 188 188 e9 e9 188 188
  //   126 126 188 188 106 106 188 188 14a 14a 188 188 e9 e9 188 188 126 126 188 188 106 106 188 188 14a
  //   14a 188 188 e9 e9 188 188 126 126 188 188 106 106 188 188 14a 14a 188 188 e9 e9 188 188 126 126 188
  //   188 106 106 188 188 14a 14a 188 188 106 106 188 188 14a 14a 188 188 106 106 1b8 1b8 15d 15d 1b8 1b8
  //   106 106 188 188 14a 14a 188 188 e9 e9 188 188 126 126 188 188 106 106 188 188 14a 14a 188 188 e9 e9
  //   188 188 126 126 188 188 106 106 188 188 14a 14a 188 188
  //   小星星变奏曲-前奏
endmodule

module \频率转换  (
  input  [15:0] \延缓倍数 ,
  input  \原CLK ,
  input  RST,
  output \后CLK 
);

  wire comparator_1_eq, comparator_2_eq, comparator_2_gt, or_1_out;
  wire [15:0] counter_1_q, shifter_1_out;

  Shifter #(.width(16), .shift("lr")) shifter_1 (.in(\延缓倍数 ), .\dist (4'b0001), .out(shifter_1_out));
  Counter #(.width(16), .max('hffff), .ongoal("wrap"), .trigger("rising"), .behavior("new")) counter_1 (
    .load(comparator_1_eq), .D({16{1'b0}}), .Q(counter_1_q), .clk(\原CLK ), .clr(RST));  // open: count, carry, preset, down
  Comparator #(.width(16), .mode("unsigned")) comparator_1 (
    .a(\延缓倍数 ), .b(counter_1_q), .eq(comparator_1_eq));  // open: gt, lt
  Comparator #(.width(16), .mode("unsigned")) comparator_2 (
    .a(shifter_1_out), .b(counter_1_q), .gt(comparator_2_gt), .eq(comparator_2_eq));  // open: lt
  or or_1 (or_1_out, comparator_2_gt, comparator_2_eq);
  Multiplexer #(.select(1), .width(1), .disabled("Z"), .enable("false")) multiplexer_1 (
    .in0(1'b1), .in1(1'b0), .out(\后CLK ), .sel(or_1_out));
endmodule
