// Logisim project 重定向流水线ccab.circ as structural Verilog: 25 circuits, main circuit ◇单周期MIPS
module \单周期MIPS  (
  input  IR1,
  input  IR2,
  input  IR3,
  output RegWrite,
  output MemWrite,
  output [31:0] PC,
  output [31:0] IR,
  output [31:0] RDin,
  output [31:0] MDin,
  output [31:0] LedData
);

  wire Go, IR1_t, IR2_t, IR3_t, IRA, IRB, IRC, W1, W2, W3;
  wire [15:0] \总周期数 ;

  Clock #(.highDuration(1), .lowDuration(1)) clock_1 ();  // open: out
  Button _1 (.out(IRA));
  Button _2 (.out(IRB));
  Button _3 (.out(IRC));
  Button \u_继续运行  (.out(Go));
  LED #(.active("true")) led_1 (.in(W1));
  LED #(.active("true")) led_2 (.in(W2));
  LED #(.active("true")) led_3 (.in(W3));
  Hex_Digit_Display hex_digit_display_1 (.value(LedData[31:28]));  // open: dp
  Hex_Digit_Display hex_digit_display_2 (.value(LedData[27:24]));  // open: dp
  Hex_Digit_Display hex_digit_display_3 (.value(LedData[23:20]));  // open: dp
  Hex_Digit_Display hex_digit_display_4 (.value(LedData[15:12]));  // open: dp
  Hex_Digit_Display hex_digit_display_5 (.value(LedData[19:16]));  // open: dp
  Hex_Digit_Display hex_digit_display_6 (.value(LedData[11:8]));  // open: dp
  Hex_Digit_Display hex_digit_display_7 (.value(LedData[7:4]));  // open: dp
  // Probe on \总周期数 
  Hex_Digit_Display hex_digit_display_8 (.value(LedData[3:0]));  // open: dp
  or or_1 (IR1_t, IR1, IRA);
  or or_2 (IR2_t, IR2, IRB);
  or or_3 (IR3_t, IR3, IRC);

  // Notes on the sheet:
  //   中断源
  //   中断等待指示
  //   总复位信号应将除ROM以外所有存储组件全部清零
  //   数码管输出
  //   数码管输出应该用寄存器锁存，否则显示数据只能一闪而过
  //   为方便自动评测，需要输出PC，IR，寄存器堆写如数据RDin
  //   RAM写使能MemWrite、RAM写入数据MDin等信号
endmodule

// 单周期硬布线控制器
module \单周期硬布线控制器  (
  input  [5:0] OP,
  input  [5:0] Func,
  output [3:0] ALU_OP,
  output sllv,
  output lb,
  output bgtz,
  output MemToReg,
  output MemWrite,
  output ALU_SRC,
  output RegWrite,
  output SysCALL,
  output SignedExt,
  output RegDst,
  output Beq,
  output Bne,
  output JR,
  output JMP,
  output JAL
);

  \运算控制器自动生成  \u_运算控制器自动生成_1  (
    .OP0(OP[0]), .OP1(OP[1]), .OP2(OP[2]), .OP3(OP[3]), .OP4(OP[4]), .OP5(OP[5]), .F0(Func[0]), .F1(Func[1]),
    .F2(Func[2]), .F3(Func[3]), .F4(Func[4]), .F5(Func[5]), .S0(ALU_OP[0]), .S1(ALU_OP[1]), .S2(ALU_OP[2]),
    .S3(ALU_OP[3]));
  \控制信号自动生成  \u_控制信号自动生成_1  (
    .OP0(OP[0]), .OP1(OP[1]), .OP2(OP[2]), .OP3(OP[3]), .OP4(OP[4]), .OP5(OP[5]), .F0(Func[0]), .F1(Func[1]),
    .F2(Func[2]), .F3(Func[3]), .F4(Func[4]), .F5(Func[5]), .SLLV(sllv), .LB(lb), .BGTZ(bgtz),
    .MemToReg(MemToReg), .MemWrite(MemWrite), .ALU_SRC(ALU_SRC), .RegWrite(RegWrite), .SysCALL(SysCALL),
    .SignedExt(SignedExt), .RegDst(RegDst), .BEQ(Beq), .BNE(Bne), .JR(JR), .JUMP(JMP), .JAL(JAL));

  // Other names for the same wires on the sheet: OP_CODE[5:0] = OP

  // Notes on the sheet:
  //   运算器控制器，根据指令生成运算器功能选择信号
endmodule

// 运算器控制器
module \运算控制器自动生成  (
  input  OP0,
  input  OP1,
  input  OP2,
  input  OP3,
  input  OP4,
  input  OP5,
  input  F0,
  input  F1,
  input  F2,
  input  F3,
  input  F4,
  input  F5,
  output S0,
  output S1,
  output S2,
  output S3
);

  wire and_1_out, and_2_out, and_3_out, and_4_out, and_5_out, and_6_out, and_7_out, and_8_out, and_9_out,
       and_10_out, and_11_out, and_12_out, and_13_out, and_14_out, and_15_out, and_16_out, and_17_out,
       and_18_out, and_19_out, and_20_out, and_21_out, and_22_out, and_23_out, and_24_out, and_25_out,
       and_26_out, and_27_out, and_28_out, and_29_out, and_30_out, and_31_out, and_32_out, and_33_out,
       and_34_out, and_35_out, and_36_out, and_37_out, and_38_out, not_1_out, not_2_out, not_3_out,
       not_4_out, not_5_out, not_6_out, not_7_out, not_8_out, not_9_out, not_10_out, not_11_out, not_12_out,
       not_13_out, not_14_out, not_15_out, not_16_out, not_17_out, not_18_out, not_19_out, not_20_out,
       not_21_out, not_22_out, not_23_out, not_24_out, not_25_out, not_26_out, not_27_out, not_28_out,
       not_29_out, not_30_out, not_31_out, not_32_out, not_33_out, not_34_out, not_35_out, not_36_out,
       not_37_out, not_38_out, not_39_out, not_40_out, not_41_out, not_42_out, not_43_out, not_44_out,
       not_45_out, not_46_out, not_47_out, not_48_out, not_49_out, not_50_out, not_51_out, not_52_out,
       not_53_out, not_54_out, not_55_out, not_56_out, not_57_out, not_58_out, not_59_out, not_60_out,
       not_61_out, not_62_out, not_63_out, not_64_out, not_65_out, not_66_out, not_67_out, not_68_out,
       not_69_out, not_70_out, not_71_out, not_72_out, not_73_out, not_74_out, not_75_out, not_76_out,
       not_77_out, not_78_out, not_79_out, not_80_out, not_81_out, not_82_out, not_83_out, not_84_out,
       not_85_out, not_86_out, not_87_out, not_88_out, not_89_out, not_90_out, not_91_out, not_92_out,
       not_93_out, not_94_out, not_95_out, not_96_out, not_97_out, not_98_out, not_99_out, not_100_out,
       not_101_out, not_102_out, not_103_out, not_104_out, not_105_out, not_106_out, not_107_out,
       not_108_out, not_109_out, not_110_out, not_111_out, not_112_out, not_113_out, not_114_out,
       not_115_out, not_116_out, not_117_out, not_118_out, not_119_out, not_120_out, not_121_out,
       not_122_out, not_123_out, not_124_out, not_125_out, not_126_out, not_127_out, not_128_out,
       not_129_out, not_130_out, not_131_out, not_132_out, not_133_out, not_134_out, not_135_out,
       not_136_out, not_137_out, not_138_out, not_139_out, not_140_out, not_141_out, not_142_out,
       not_143_out, not_144_out, not_145_out, not_146_out, not_147_out, not_148_out, not_149_out,
       not_150_out, not_151_out, not_152_out, not_153_out, not_154_out, not_155_out, not_156_out,
       not_157_out, not_158_out, not_159_out, not_160_out, not_161_out, not_162_out, not_163_out,
       not_164_out, not_165_out, not_166_out, not_167_out, not_168_out, not_169_out, not_170_out,
       not_171_out, not_172_out, not_173_out, not_174_out, not_175_out, not_176_out, not_177_out,
       not_178_out, not_179_out, not_180_out, not_181_out, not_182_out, not_183_out, not_184_out,
       not_185_out, not_186_out, not_187_out, not_188_out, not_189_out, not_190_out, not_191_out,
       not_192_out, not_193_out, not_194_out, not_195_out, not_196_out, not_197_out, not_198_out,
       not_199_out, not_200_out, not_201_out, not_202_out, not_203_out, not_204_out, not_205_out,
       not_206_out, not_207_out, not_208_out, not_209_out, not_210_out, not_211_out, not_212_out,
       not_213_out, not_214_out, not_215_out, not_216_out, not_217_out, not_218_out, not_219_out,
       not_220_out, not_221_out, not_222_out, not_223_out, not_224_out, not_225_out, not_226_out,
       not_227_out, not_228_out, not_229_out, not_230_out, not_231_out, not_232_out, not_233_out,
       not_234_out, not_235_out, not_236_out, not_237_out, not_238_out, not_239_out, not_240_out,
       not_241_out, not_242_out, not_243_out, not_244_out, not_245_out, not_246_out, not_247_out,
       not_248_out, not_249_out, not_250_out, not_251_out, not_252_out;

  not not_1 (not_1_out, OP5);
  not not_2 (not_2_out, OP4);
  not not_3 (not_3_out, OP3);
  not not_4 (not_4_out, OP2);
  not not_5 (not_5_out, OP1);
  not not_6 (not_6_out, OP0);
  not not_7 (not_7_out, F5);
  not not_8 (not_8_out, F4);
  not not_9 (not_9_out, F3);
  not not_10 (not_10_out, F2);
  not not_11 (not_11_out, OP5);
  not not_12 (not_12_out, OP4);
  not not_13 (not_13_out, OP3);
  not not_14 (not_14_out, OP2);
  not not_15 (not_15_out, OP1);
  not not_16 (not_16_out, OP0);
  not not_17 (not_17_out, F4);
  not not_18 (not_18_out, F3);
  not not_19 (not_19_out, F2);
  not not_20 (not_20_out, F1);
  not not_21 (not_21_out, F0);
  not not_22 (not_22_out, OP5);
  not not_23 (not_23_out, OP4);
  not not_24 (not_24_out, OP3);
  not not_25 (not_25_out, OP2);
  not not_26 (not_26_out, OP1);
  not not_27 (not_27_out, OP0);
  not not_28 (not_28_out, F4);
  not not_29 (not_29_out, F3);
  not not_30 (not_30_out, F2);
  not not_31 (not_31_out, F1);
  not not_32 (not_32_out, OP5);
  not not_33 (not_33_out, OP4);
  not not_34 (not_34_out, OP3);
  not not_35 (not_35_out, OP2);
  not not_36 (not_36_out, OP1);
  not not_37 (not_37_out, OP0);
  not not_38 (not_38_out, F4);
  not not_39 (not_39_out, F3);
  not not_40 (not_40_out, F1);
  not not_41 (not_41_out, F0);
  not not_42 (not_42_out, OP5);
  not not_43 (not_43_out, OP4);
  not not_44 (not_44_out, OP3);
  not not_45 (not_45_out, OP2);
  not not_46 (not_46_out, OP1);
  not not_47 (not_47_out, OP0);
  not not_48 (not_48_out, F4);
  not not_49 (not_49_out, F2);
  not not_50 (not_50_out, F0);
  not not_51 (not_51_out, OP5);
  not not_52 (not_52_out, OP4);
  not not_53 (not_53_out, OP2);
  not not_54 (not_54_out, OP1);
  not not_55 (not_55_out, OP0);
  not not_56 (not_56_out, OP5);
  not not_57 (not_57_out, OP4);
  not not_58 (not_58_out, OP1);
  not not_59 (not_59_out, OP0);
  not not_60 (not_60_out, OP5);
  not not_61 (not_61_out, OP4);
  not not_62 (not_62_out, OP2);
  not not_63 (not_63_out, OP1);
  not not_64 (not_64_out, OP5);
  not not_65 (not_65_out, OP4);
  not not_66 (not_66_out, OP2);
  not not_67 (not_67_out, OP0);
  not not_68 (not_68_out, OP4);
  not not_69 (not_69_out, OP3);
  not not_70 (not_70_out, OP2);
  not not_71 (not_71_out, OP4);
  not not_72 (not_72_out, OP2);
  not not_73 (not_73_out, OP5);
  not not_74 (not_74_out, OP4);
  not not_75 (not_75_out, OP0);
  not not_76 (not_76_out, OP4);
  not not_77 (not_77_out, OP3);
  not not_78 (not_78_out, OP2);
  not not_79 (not_79_out, OP1);
  not not_80 (not_80_out, OP0);
  not not_81 (not_81_out, OP5);
  not not_82 (not_82_out, OP4);
  not not_83 (not_83_out, OP3);
  not not_84 (not_84_out, OP2);
  not not_85 (not_85_out, OP1);
  not not_86 (not_86_out, OP0);
  not not_87 (not_87_out, F5);
  not not_88 (not_88_out, F4);
  not not_89 (not_89_out, F3);
  not not_90 (not_90_out, F2);
  not not_91 (not_91_out, F0);
  not not_92 (not_92_out, OP5);
  not not_93 (not_93_out, OP4);
  not not_94 (not_94_out, OP3);
  not not_95 (not_95_out, OP2);
  not not_96 (not_96_out, OP1);
  not not_97 (not_97_out, OP0);
  not not_98 (not_98_out, F4);
  not not_99 (not_99_out, F3);
  not not_100 (not_100_out, F2);
  not not_101 (not_101_out, F0);
  not not_102 (not_102_out, OP5);
  not not_103 (not_103_out, OP4);
  not not_104 (not_104_out, OP3);
  not not_105 (not_105_out, OP2);
  not not_106 (not_106_out, OP1);
  not not_107 (not_107_out, OP0);
  not not_108 (not_108_out, F4);
  not not_109 (not_109_out, F3);
  not not_110 (not_110_out, F1);
  not not_111 (not_111_out, F0);
  not not_112 (not_112_out, OP5);
  not not_113 (not_113_out, OP4);
  not not_114 (not_114_out, OP3);
  not not_115 (not_115_out, OP2);
  not not_116 (not_116_out, OP1);
  not not_117 (not_117_out, OP0);
  not not_118 (not_118_out, F4);
  not not_119 (not_119_out, F3);
  not not_120 (not_120_out, OP5);
  not not_121 (not_121_out, OP4);
  not not_122 (not_122_out, OP3);
  not not_123 (not_123_out, OP2);
  not not_124 (not_124_out, OP1);
  not not_125 (not_125_out, OP0);
  not not_126 (not_126_out, F4);
  not not_127 (not_127_out, F2);
  not not_128 (not_128_out, F0);
  not not_129 (not_129_out, OP5);
  not not_130 (not_130_out, OP4);
  not not_131 (not_131_out, OP1);
  not not_132 (not_132_out, OP0);
  not not_133 (not_133_out, OP5);
  not not_134 (not_134_out, OP4);
  not not_135 (not_135_out, OP2);
  not not_136 (not_136_out, OP0);
  not not_137 (not_137_out, OP5);
  not not_138 (not_138_out, OP4);
  not not_139 (not_139_out, OP3);
  not not_140 (not_140_out, OP2);
  not not_141 (not_141_out, OP1);
  not not_142 (not_142_out, OP0);
  not not_143 (not_143_out, F4);
  not not_144 (not_144_out, F3);
  not not_145 (not_145_out, F2);
  not not_146 (not_146_out, F1);
  not not_147 (not_147_out, F0);
  not not_148 (not_148_out, OP5);
  not not_149 (not_149_out, OP4);
  not not_150 (not_150_out, OP3);
  not not_151 (not_151_out, OP2);
  not not_152 (not_152_out, OP1);
  not not_153 (not_153_out, OP0);
  not not_154 (not_154_out, F4);
  not not_155 (not_155_out, F3);
  not not_156 (not_156_out, F2);
  not not_157 (not_157_out, F1);
  not not_158 (not_158_out, OP5);
  not not_159 (not_159_out, OP4);
  not not_160 (not_160_out, OP3);
  not not_161 (not_161_out, OP2);
  not not_162 (not_162_out, OP1);
  not not_163 (not_163_out, OP0);
  not not_164 (not_164_out, F4);
  not not_165 (not_165_out, F3);
  not not_166 (not_166_out, F2);
  not not_167 (not_167_out, F0);
  not not_168 (not_168_out, OP5);
  not not_169 (not_169_out, OP4);
  not not_170 (not_170_out, OP3);
  not not_171 (not_171_out, OP2);
  not not_172 (not_172_out, OP1);
  not not_173 (not_173_out, OP0);
  not not_174 (not_174_out, F4);
  not not_175 (not_175_out, F3);
  not not_176 (not_176_out, F1);
  not not_177 (not_177_out, F0);
  not not_178 (not_178_out, OP5);
  not not_179 (not_179_out, OP4);
  not not_180 (not_180_out, OP3);
  not not_181 (not_181_out, OP2);
  not not_182 (not_182_out, OP1);
  not not_183 (not_183_out, OP0);
  not not_184 (not_184_out, F4);
  not not_185 (not_185_out, F2);
  not not_186 (not_186_out, OP5);
  not not_187 (not_187_out, OP4);
  not not_188 (not_188_out, OP2);
  not not_189 (not_189_out, OP1);
  not not_190 (not_190_out, OP0);
  not not_191 (not_191_out, OP5);
  not not_192 (not_192_out, OP4);
  not not_193 (not_193_out, OP1);
  not not_194 (not_194_out, OP0);
  not not_195 (not_195_out, OP5);
  not not_196 (not_196_out, OP4);
  not not_197 (not_197_out, OP2);
  not not_198 (not_198_out, OP1);
  not not_199 (not_199_out, OP4);
  not not_200 (not_200_out, OP3);
  not not_201 (not_201_out, OP2);
  not not_202 (not_202_out, OP4);
  not not_203 (not_203_out, OP2);
  not not_204 (not_204_out, OP4);
  not not_205 (not_205_out, OP3);
  not not_206 (not_206_out, OP2);
  not not_207 (not_207_out, OP1);
  not not_208 (not_208_out, OP0);
  not not_209 (not_209_out, OP5);
  not not_210 (not_210_out, OP4);
  not not_211 (not_211_out, OP3);
  not not_212 (not_212_out, OP2);
  not not_213 (not_213_out, OP1);
  not not_214 (not_214_out, OP0);
  not not_215 (not_215_out, F4);
  not not_216 (not_216_out, F3);
  not not_217 (not_217_out, F1);
  not not_218 (not_218_out, OP5);
  not not_219 (not_219_out, OP4);
  not not_220 (not_220_out, OP3);
  not not_221 (not_221_out, OP2);
  not not_222 (not_222_out, OP1);
  not not_223 (not_223_out, OP0);
  not not_224 (not_224_out, F4);
  not not_225 (not_225_out, F3);
  not not_226 (not_226_out, OP5);
  not not_227 (not_227_out, OP4);
  not not_228 (not_228_out, OP3);
  not not_229 (not_229_out, OP2);
  not not_230 (not_230_out, OP1);
  not not_231 (not_231_out, OP0);
  not not_232 (not_232_out, F4);
  not not_233 (not_233_out, F2);
  not not_234 (not_234_out, F0);
  not not_235 (not_235_out, OP5);
  not not_236 (not_236_out, OP4);
  not not_237 (not_237_out, OP3);
  not not_238 (not_238_out, OP2);
  not not_239 (not_239_out, OP1);
  not not_240 (not_240_out, OP0);
  not not_241 (not_241_out, F4);
  not not_242 (not_242_out, F2);
  not not_243 (not_243_out, OP5);
  not not_244 (not_244_out, OP4);
  not not_245 (not_245_out, OP2);
  not not_246 (not_246_out, OP0);
  not not_247 (not_247_out, OP5);
  not not_248 (not_248_out, OP4);
  not not_249 (not_249_out, OP1);
  not not_250 (not_250_out, OP5);
  not not_251 (not_251_out, OP4);
  not not_252 (not_252_out, OP0);
  and and_1 (and_1_out, not_1_out, not_2_out, not_3_out, not_4_out, not_5_out, not_6_out, not_7_out, not_8_out, not_9_out, not_10_out, F1, F0);
  and and_2 (and_2_out, not_11_out, not_12_out, not_13_out, not_14_out, not_15_out, not_16_out, F5, not_17_out, not_18_out, not_19_out, not_20_out, not_21_out);
  and and_3 (and_3_out, not_22_out, not_23_out, not_24_out, not_25_out, not_26_out, not_27_out, F5, not_28_out, not_29_out, not_30_out, not_31_out, F0);
  and and_4 (and_4_out, not_32_out, not_33_out, not_34_out, not_35_out, not_36_out, not_37_out, F5, not_38_out, not_39_out, F2, not_40_out, not_41_out);
  and and_5 (and_5_out, not_42_out, not_43_out, not_44_out, not_45_out, not_46_out, not_47_out, F5, not_48_out, F3, not_49_out, F1, not_50_out);
  and and_6 (and_6_out, not_51_out, not_52_out, OP3, not_53_out, not_54_out, not_55_out);
  and and_7 (and_7_out, not_56_out, not_57_out, OP3, OP2, not_58_out, not_59_out);
  and and_8 (and_8_out, not_60_out, not_61_out, OP3, not_62_out, not_63_out, OP0);
  and and_9 (and_9_out, not_64_out, not_65_out, OP3, not_66_out, OP1, not_67_out);
  and and_10 (and_10_out, OP5, not_68_out, not_69_out, not_70_out, OP1, OP0);
  and and_11 (and_11_out, OP5, not_71_out, OP3, not_72_out, OP1, OP0);
  and and_12 (and_12_out, not_73_out, not_74_out, OP3, OP2, OP1, not_75_out);
  and and_13 (and_13_out, OP5, not_76_out, not_77_out, not_78_out, not_79_out, not_80_out);
  and and_14 (and_14_out, not_81_out, not_82_out, not_83_out, not_84_out, not_85_out, not_86_out, not_87_out, not_88_out, not_89_out, not_90_out, F1, not_91_out);
  and and_15 (and_15_out, not_92_out, not_93_out, not_94_out, not_95_out, not_96_out, not_97_out, F5, not_98_out, not_99_out, not_100_out, F1, not_101_out);
  and and_16 (and_16_out, not_102_out, not_103_out, not_104_out, not_105_out, not_106_out, not_107_out, F5, not_108_out, not_109_out, F2, not_110_out, not_111_out);
  and and_17 (and_17_out, not_112_out, not_113_out, not_114_out, not_115_out, not_116_out, not_117_out, F5, not_118_out, not_119_out, F2, F1, F0);
  and and_18 (and_18_out, not_120_out, not_121_out, not_122_out, not_123_out, not_124_out, not_125_out, F5, not_126_out, F3, not_127_out, F1, not_128_out);
  and and_19 (and_19_out, not_129_out, not_130_out, OP3, OP2, not_131_out, not_132_out);
  and and_20 (and_20_out, not_133_out, not_134_out, OP3, not_135_out, OP1, not_136_out);
  and and_21 (and_21_out, not_137_out, not_138_out, not_139_out, not_140_out, not_141_out, not_142_out, F5, not_143_out, not_144_out, not_145_out, not_146_out, not_147_out);
  and and_22 (and_22_out, not_148_out, not_149_out, not_150_out, not_151_out, not_152_out, not_153_out, F5, not_154_out, not_155_out, not_156_out, not_157_out, F0);
  and and_23 (and_23_out, not_158_out, not_159_out, not_160_out, not_161_out, not_162_out, not_163_out, F5, not_164_out, not_165_out, not_166_out, F1, not_167_out);
  and and_24 (and_24_out, not_168_out, not_169_out, not_170_out, not_171_out, not_172_out, not_173_out, F5, not_174_out, not_175_out, F2, not_176_out, not_177_out);
  and and_25 (and_25_out, not_178_out, not_179_out, not_180_out, not_181_out, not_182_out, not_183_out, F5, not_184_out, F3, not_185_out, F1, F0);
  and and_26 (and_26_out, not_186_out, not_187_out, OP3, not_188_out, not_189_out, not_190_out);
  and and_27 (and_27_out, not_191_out, not_192_out, OP3, OP2, not_193_out, not_194_out);
  and and_28 (and_28_out, not_195_out, not_196_out, OP3, not_197_out, not_198_out, OP0);
  and and_29 (and_29_out, OP5, not_199_out, not_200_out, not_201_out, OP1, OP0);
  and and_30 (and_30_out, OP5, not_202_out, OP3, not_203_out, OP1, OP0);
  and and_31 (and_31_out, OP5, not_204_out, not_205_out, not_206_out, not_207_out, not_208_out);
  and and_32 (and_32_out, not_209_out, not_210_out, not_211_out, not_212_out, not_213_out, not_214_out, F5, not_215_out, not_216_out, F2, not_217_out, F0);
  and and_33 (and_33_out, not_218_out, not_219_out, not_220_out, not_221_out, not_222_out, not_223_out, F5, not_224_out, not_225_out, F2, F1, F0);
  and and_34 (and_34_out, not_226_out, not_227_out, not_228_out, not_229_out, not_230_out, not_231_out, F5, not_232_out, F3, not_233_out, F1, not_234_out);
  and and_35 (and_35_out, not_235_out, not_236_out, not_237_out, not_238_out, not_239_out, not_240_out, F5, not_241_out, F3, not_242_out, F1, F0);
  and and_36 (and_36_out, not_243_out, not_244_out, OP3, not_245_out, OP1, not_246_out);
  and and_37 (and_37_out, not_247_out, not_248_out, OP3, OP2, not_249_out, OP0);
  and and_38 (and_38_out, not_250_out, not_251_out, OP3, OP2, OP1, not_252_out);
  or or_1 (S1, and_14_out, and_15_out, and_16_out, and_17_out, and_18_out, and_19_out, and_20_out);
  or or_2 (S2, and_21_out, and_22_out, and_23_out, and_24_out, and_25_out, and_26_out, and_27_out, and_28_out, and_29_out, and_30_out, and_31_out);
  or or_3 (S3, and_32_out, and_33_out, and_34_out, and_35_out, and_36_out, and_37_out, and_38_out);
  or or_4 (S0, and_1_out, and_2_out, and_3_out, and_4_out, and_5_out, and_6_out, and_7_out, and_8_out, and_9_out, and_10_out, and_11_out, and_12_out, and_13_out);
endmodule

// 控制信号生成
module \控制信号自动生成  (
  input  OP0,
  input  OP1,
  input  OP2,
  input  OP3,
  input  OP4,
  input  OP5,
  input  F0,
  input  F1,
  input  F2,
  input  F3,
  input  F4,
  input  F5,
  output SLLV,
  output LB,
  output BGTZ,
  output MemToReg,
  output MemWrite,
  output ALU_SRC,
  output RegWrite,
  output SysCALL,
  output SignedExt,
  output RegDst,
  output BEQ,
  output BNE,
  output JR,
  output JUMP,
  output JAL
);

  wire and_4_out, and_5_out, and_7_out, and_8_out, and_9_out, and_10_out, and_11_out, and_12_out, and_13_out,
       and_14_out, and_15_out, and_16_out, and_17_out, and_18_out, and_19_out, and_20_out, and_22_out,
       and_23_out, and_24_out, and_25_out, and_26_out, and_27_out, and_28_out, and_29_out, and_30_out,
       and_31_out, and_32_out, and_36_out, and_37_out, not_1_out, not_2_out, not_3_out, not_4_out, not_5_out,
       not_6_out, not_7_out, not_8_out, not_9_out, not_10_out, not_11_out, not_12_out, not_13_out,
       not_14_out, not_15_out, not_16_out, not_17_out, not_18_out, not_19_out, not_20_out, not_21_out,
       not_22_out, not_23_out, not_24_out, not_25_out, not_26_out, not_27_out, not_28_out, not_29_out,
       not_30_out, not_31_out, not_32_out, not_33_out, not_34_out, not_35_out, not_36_out, not_37_out,
       not_38_out, not_39_out, not_40_out, not_41_out, not_42_out, not_43_out, not_44_out, not_45_out,
       not_46_out, not_47_out, not_48_out, not_49_out, not_50_out, not_51_out, not_52_out, not_53_out,
       not_54_out, not_55_out, not_56_out, not_57_out, not_58_out, not_59_out, not_60_out, not_61_out,
       not_62_out, not_63_out, not_64_out, not_65_out, not_66_out, not_67_out, not_68_out, not_69_out,
       not_70_out, not_71_out, not_72_out, not_73_out, not_74_out, not_75_out, not_76_out, not_77_out,
       not_78_out, not_79_out, not_80_out, not_81_out, not_82_out, not_83_out, not_84_out, not_85_out,
       not_86_out, not_87_out, not_88_out, not_89_out, not_90_out, not_91_out, not_92_out, not_93_out,
       not_94_out, not_95_out, not_96_out, not_97_out, not_98_out, not_99_out, not_100_out, not_101_out,
       not_102_out, not_103_out, not_104_out, not_105_out, not_106_out, not_107_out, not_108_out,
       not_109_out, not_110_out, not_111_out, not_112_out, not_113_out, not_114_out, not_115_out,
       not_116_out, not_117_out, not_118_out, not_119_out, not_120_out, not_121_out, not_122_out,
       not_123_out, not_124_out, not_125_out, not_126_out, not_127_out, not_128_out, not_129_out,
       not_130_out, not_131_out, not_132_out, not_133_out, not_134_out, not_135_out, not_136_out,
       not_137_out, not_138_out, not_139_out, not_140_out, not_141_out, not_142_out, not_143_out,
       not_144_out, not_145_out, not_146_out, not_147_out, not_148_out, not_149_out, not_150_out,
       not_151_out, not_152_out, not_153_out, not_154_out, not_155_out, not_156_out, not_157_out,
       not_158_out, not_159_out, not_160_out, not_161_out, not_162_out, not_163_out, not_164_out,
       not_165_out, not_166_out, not_167_out, not_168_out, not_169_out, not_170_out, not_171_out,
       not_172_out, not_173_out, not_174_out, not_175_out, not_176_out, not_177_out, not_178_out,
       not_179_out, not_180_out, not_181_out, not_182_out, not_183_out, not_184_out, not_185_out,
       not_186_out, not_187_out, not_188_out, not_189_out, not_190_out, not_191_out, not_192_out,
       not_193_out, not_194_out, not_195_out, not_196_out, not_197_out, not_198_out, not_199_out,
       not_200_out, not_201_out, not_202_out, not_203_out, not_204_out, not_205_out, not_206_out,
       not_207_out, not_208_out, not_209_out, not_210_out, not_211_out, not_212_out, not_213_out,
       not_214_out, not_215_out, not_216_out, not_217_out, not_218_out, not_219_out, not_220_out,
       not_221_out, not_222_out, not_223_out, not_224_out, not_225_out, not_226_out, not_227_out,
       not_228_out, not_229_out, not_230_out, not_231_out, not_232_out, not_233_out, not_234_out;

  not not_1 (not_1_out, OP5);
  not not_2 (not_2_out, OP4);
  not not_3 (not_3_out, OP3);
  not not_4 (not_4_out, OP2);
  not not_5 (not_5_out, OP1);
  not not_6 (not_6_out, OP0);
  not not_7 (not_7_out, F5);
  not not_8 (not_8_out, F4);
  not not_9 (not_9_out, F3);
  not not_10 (not_10_out, F1);
  not not_11 (not_11_out, F0);
  not not_12 (not_12_out, OP4);
  not not_13 (not_13_out, OP3);
  not not_14 (not_14_out, OP2);
  not not_15 (not_15_out, OP1);
  not not_16 (not_16_out, OP0);
  not not_17 (not_17_out, OP5);
  not not_18 (not_18_out, OP4);
  not not_19 (not_19_out, OP3);
  not not_20 (not_20_out, OP0);
  not not_21 (not_21_out, OP1);
  not not_22 (not_22_out, OP2);
  not not_23 (not_23_out, OP3);
  not not_24 (not_24_out, OP4);
  not not_25 (not_25_out, OP2);
  not not_26 (not_26_out, OP3);
  not not_27 (not_27_out, OP4);
  not not_28 (not_28_out, OP2);
  not not_29 (not_29_out, OP4);
  not not_30 (not_30_out, OP0);
  not not_31 (not_31_out, OP1);
  not not_32 (not_32_out, OP2);
  not not_33 (not_33_out, OP3);
  not not_34 (not_34_out, OP4);
  not not_35 (not_35_out, OP0);
  not not_36 (not_36_out, OP4);
  not not_37 (not_37_out, OP5);
  not not_38 (not_38_out, OP1);
  not not_39 (not_39_out, OP4);
  not not_40 (not_40_out, OP5);
  not not_41 (not_41_out, OP2);
  not not_42 (not_42_out, OP4);
  not not_43 (not_43_out, OP0);
  not not_44 (not_44_out, OP1);
  not not_45 (not_45_out, OP2);
  not not_46 (not_46_out, OP3);
  not not_47 (not_47_out, OP4);
  not not_48 (not_48_out, F0);
  not not_49 (not_49_out, F1);
  not not_50 (not_50_out, F3);
  not not_51 (not_51_out, F4);
  not not_52 (not_52_out, OP0);
  not not_53 (not_53_out, OP1);
  not not_54 (not_54_out, OP2);
  not not_55 (not_55_out, OP3);
  not not_56 (not_56_out, OP4);
  not not_57 (not_57_out, F0);
  not not_58 (not_58_out, F2);
  not not_59 (not_59_out, F3);
  not not_60 (not_60_out, F4);
  not not_61 (not_61_out, OP0);
  not not_62 (not_62_out, OP1);
  not not_63 (not_63_out, OP2);
  not not_64 (not_64_out, OP3);
  not not_65 (not_65_out, OP4);
  not not_66 (not_66_out, F1);
  not not_67 (not_67_out, F3);
  not not_68 (not_68_out, F4);
  not not_69 (not_69_out, OP0);
  not not_70 (not_70_out, OP1);
  not not_71 (not_71_out, OP2);
  not not_72 (not_72_out, OP3);
  not not_73 (not_73_out, OP4);
  not not_74 (not_74_out, F2);
  not not_75 (not_75_out, F3);
  not not_76 (not_76_out, F4);
  not not_77 (not_77_out, F5);
  not not_78 (not_78_out, OP0);
  not not_79 (not_79_out, OP1);
  not not_80 (not_80_out, OP2);
  not not_81 (not_81_out, OP3);
  not not_82 (not_82_out, OP4);
  not not_83 (not_83_out, F2);
  not not_84 (not_84_out, F4);
  not not_85 (not_85_out, OP0);
  not not_86 (not_86_out, OP1);
  not not_87 (not_87_out, OP2);
  not not_88 (not_88_out, OP3);
  not not_89 (not_89_out, OP4);
  not not_90 (not_90_out, F3);
  not not_91 (not_91_out, F4);
  not not_92 (not_92_out, OP0);
  not not_93 (not_93_out, OP1);
  not not_94 (not_94_out, OP2);
  not not_95 (not_95_out, OP3);
  not not_96 (not_96_out, OP4);
  not not_97 (not_97_out, OP0);
  not not_98 (not_98_out, OP4);
  not not_99 (not_99_out, OP5);
  not not_100 (not_100_out, OP1);
  not not_101 (not_101_out, OP4);
  not not_102 (not_102_out, OP5);
  not not_103 (not_103_out, OP2);
  not not_104 (not_104_out, OP3);
  not not_105 (not_105_out, OP4);
  not not_106 (not_106_out, OP0);
  not not_107 (not_107_out, OP1);
  not not_108 (not_108_out, OP2);
  not not_109 (not_109_out, OP3);
  not not_110 (not_110_out, OP4);
  not not_111 (not_111_out, OP5);
  not not_112 (not_112_out, F0);
  not not_113 (not_113_out, F1);
  not not_114 (not_114_out, F4);
  not not_115 (not_115_out, F5);
  not not_116 (not_116_out, OP0);
  not not_117 (not_117_out, OP1);
  not not_118 (not_118_out, OP2);
  not not_119 (not_119_out, OP3);
  not not_120 (not_120_out, OP4);
  not not_121 (not_121_out, OP0);
  not not_122 (not_122_out, OP2);
  not not_123 (not_123_out, OP4);
  not not_124 (not_124_out, OP5);
  not not_125 (not_125_out, OP1);
  not not_126 (not_126_out, OP2);
  not not_127 (not_127_out, OP4);
  not not_128 (not_128_out, OP5);
  not not_129 (not_129_out, OP2);
  not not_130 (not_130_out, OP4);
  not not_131 (not_131_out, OP0);
  not not_132 (not_132_out, OP1);
  not not_133 (not_133_out, OP2);
  not not_134 (not_134_out, OP3);
  not not_135 (not_135_out, OP4);
  not not_136 (not_136_out, OP5);
  not not_137 (not_137_out, F0);
  not not_138 (not_138_out, F1);
  not not_139 (not_139_out, F2);
  not not_140 (not_140_out, F4);
  not not_141 (not_141_out, F5);
  not not_142 (not_142_out, OP0);
  not not_143 (not_143_out, OP1);
  not not_144 (not_144_out, OP2);
  not not_145 (not_145_out, OP3);
  not not_146 (not_146_out, OP4);
  not not_147 (not_147_out, OP5);
  not not_148 (not_148_out, F0);
  not not_149 (not_149_out, F1);
  not not_150 (not_150_out, F3);
  not not_151 (not_151_out, F4);
  not not_152 (not_152_out, OP0);
  not not_153 (not_153_out, OP1);
  not not_154 (not_154_out, OP2);
  not not_155 (not_155_out, OP3);
  not not_156 (not_156_out, OP4);
  not not_157 (not_157_out, OP5);
  not not_158 (not_158_out, F0);
  not not_159 (not_159_out, F2);
  not not_160 (not_160_out, F3);
  not not_161 (not_161_out, F4);
  not not_162 (not_162_out, OP0);
  not not_163 (not_163_out, OP1);
  not not_164 (not_164_out, OP2);
  not not_165 (not_165_out, OP3);
  not not_166 (not_166_out, OP4);
  not not_167 (not_167_out, OP5);
  not not_168 (not_168_out, F1);
  not not_169 (not_169_out, F3);
  not not_170 (not_170_out, F4);
  not not_171 (not_171_out, OP0);
  not not_172 (not_172_out, OP1);
  not not_173 (not_173_out, OP2);
  not not_174 (not_174_out, OP3);
  not not_175 (not_175_out, OP4);
  not not_176 (not_176_out, OP5);
  not not_177 (not_177_out, F2);
  not not_178 (not_178_out, F3);
  not not_179 (not_179_out, F4);
  not not_180 (not_180_out, F5);
  not not_181 (not_181_out, OP0);
  not not_182 (not_182_out, OP1);
  not not_183 (not_183_out, OP2);
  not not_184 (not_184_out, OP3);
  not not_185 (not_185_out, OP4);
  not not_186 (not_186_out, OP5);
  not not_187 (not_187_out, F2);
  not not_188 (not_188_out, F4);
  not not_189 (not_189_out, OP0);
  not not_190 (not_190_out, OP1);
  not not_191 (not_191_out, OP2);
  not not_192 (not_192_out, OP3);
  not not_193 (not_193_out, OP4);
  not not_194 (not_194_out, OP5);
  not not_195 (not_195_out, F3);
  not not_196 (not_196_out, F4);
  not not_197 (not_197_out, OP0);
  not not_198 (not_198_out, OP1);
  not not_199 (not_199_out, OP3);
  not not_200 (not_200_out, OP4);
  not not_201 (not_201_out, OP5);
  not not_202 (not_202_out, OP1);
  not not_203 (not_203_out, OP3);
  not not_204 (not_204_out, OP4);
  not not_205 (not_205_out, OP5);
  not not_206 (not_206_out, OP0);
  not not_207 (not_207_out, OP1);
  not not_208 (not_208_out, OP2);
  not not_209 (not_209_out, OP3);
  not not_210 (not_210_out, OP4);
  not not_211 (not_211_out, OP5);
  not not_212 (not_212_out, F0);
  not not_213 (not_213_out, F1);
  not not_214 (not_214_out, F2);
  not not_215 (not_215_out, F4);
  not not_216 (not_216_out, F5);
  not not_217 (not_217_out, OP0);
  not not_218 (not_218_out, OP2);
  not not_219 (not_219_out, OP3);
  not not_220 (not_220_out, OP4);
  not not_221 (not_221_out, OP5);
  not not_222 (not_222_out, F0);
  not not_223 (not_223_out, F1);
  not not_224 (not_224_out, F2);
  not not_225 (not_225_out, F4);
  not not_226 (not_226_out, F5);
  not not_227 (not_227_out, OP2);
  not not_228 (not_228_out, OP3);
  not not_229 (not_229_out, OP4);
  not not_230 (not_230_out, OP5);
  not not_231 (not_231_out, OP2);
  not not_232 (not_232_out, OP3);
  not not_233 (not_233_out, OP4);
  not not_234 (not_234_out, OP5);
  and and_1 (SLLV, not_1_out, not_2_out, not_3_out, not_4_out, not_5_out, not_6_out, not_7_out, not_8_out, not_9_out, F2, not_10_out, not_11_out);
  and and_2 (LB, OP5, not_12_out, not_13_out, not_14_out, not_15_out, not_16_out);
  and and_3 (BGTZ, not_17_out, not_18_out, not_19_out, OP2, OP1, OP0);
  and and_4 (and_4_out, not_20_out, not_21_out, not_22_out, not_23_out, not_24_out, OP5);
  and and_5 (and_5_out, OP0, OP1, not_25_out, not_26_out, not_27_out, OP5);
  and and_6 (MemWrite, OP0, OP1, not_28_out, OP3, not_29_out, OP5);
  and and_7 (and_7_out, not_30_out, not_31_out, not_32_out, not_33_out, not_34_out, OP5);
  and and_8 (and_8_out, not_35_out, OP3, not_36_out, not_37_out);
  and and_9 (and_9_out, not_38_out, OP3, not_39_out, not_40_out);
  and and_10 (and_10_out, OP0, OP1, not_41_out, not_42_out, OP5);
  and and_11 (and_11_out, not_43_out, not_44_out, not_45_out, not_46_out, not_47_out, not_48_out, not_49_out, not_50_out, not_51_out);
  and and_12 (and_12_out, not_52_out, not_53_out, not_54_out, not_55_out, not_56_out, not_57_out, not_58_out, not_59_out, not_60_out);
  and and_13 (and_13_out, not_61_out, not_62_out, not_63_out, not_64_out, not_65_out, not_66_out, not_67_out, not_68_out, F5);
  and and_14 (and_14_out, not_69_out, not_70_out, not_71_out, not_72_out, not_73_out, F1, not_74_out, not_75_out, not_76_out, not_77_out);
  and and_15 (and_15_out, not_78_out, not_79_out, not_80_out, not_81_out, not_82_out, F1, not_83_out, F3, not_84_out, F5);
  and and_16 (and_16_out, not_85_out, not_86_out, not_87_out, not_88_out, not_89_out, F0, F2, not_90_out, not_91_out, F5);
  and and_17 (and_17_out, not_92_out, not_93_out, not_94_out, not_95_out, not_96_out, OP5);
  and and_18 (and_18_out, not_97_out, OP3, not_98_out, not_99_out);
  and and_19 (and_19_out, not_100_out, OP3, not_101_out, not_102_out);
  and and_20 (and_20_out, OP0, OP1, not_103_out, not_104_out, not_105_out);
  and and_21 (SysCALL, not_106_out, not_107_out, not_108_out, not_109_out, not_110_out, not_111_out, not_112_out, not_113_out, F2, F3, not_114_out, not_115_out);
  and and_22 (and_22_out, not_116_out, not_117_out, not_118_out, not_119_out, not_120_out, OP5);
  and and_23 (and_23_out, not_121_out, not_122_out, OP3, not_123_out, not_124_out);
  and and_24 (and_24_out, not_125_out, not_126_out, OP3, not_127_out, not_128_out);
  and and_25 (and_25_out, OP0, OP1, not_129_out, not_130_out, OP5);
  and and_26 (and_26_out, not_131_out, not_132_out, not_133_out, not_134_out, not_135_out, not_136_out, not_137_out, not_138_out, not_139_out, not_140_out, not_141_out);
  and and_27 (and_27_out, not_142_out, not_143_out, not_144_out, not_145_out, not_146_out, not_147_out, not_148_out, not_149_out, not_150_out, not_151_out);
  and and_28 (and_28_out, not_152_out, not_153_out, not_154_out, not_155_out, not_156_out, not_157_out, not_158_out, not_159_out, not_160_out, not_161_out);
  and and_29 (and_29_out, not_162_out, not_163_out, not_164_out, not_165_out, not_166_out, not_167_out, not_168_out, not_169_out, not_170_out, F5);
  and and_30 (and_30_out, not_171_out, not_172_out, not_173_out, not_174_out, not_175_out, not_176_out, F1, not_177_out, not_178_out, not_179_out, not_180_out);
  and and_31 (and_31_out, not_181_out, not_182_out, not_183_out, not_184_out, not_185_out, not_186_out, F1, not_187_out, F3, not_188_out, F5);
  and and_32 (and_32_out, not_189_out, not_190_out, not_191_out, not_192_out, not_193_out, not_194_out, F0, F2, not_195_out, not_196_out, F5);
  and and_33 (BEQ, not_197_out, not_198_out, OP2, not_199_out, not_200_out, not_201_out);
  and and_34 (BNE, OP0, not_202_out, OP2, not_203_out, not_204_out, not_205_out);
  and and_35 (JR, not_206_out, not_207_out, not_208_out, not_209_out, not_210_out, not_211_out, not_212_out, not_213_out, not_214_out, F3, not_215_out, not_216_out);
  and and_36 (and_36_out, not_217_out, not_218_out, not_219_out, not_220_out, not_221_out, not_222_out, not_223_out, not_224_out, F3, not_225_out, not_226_out);
  and and_37 (and_37_out, OP1, not_227_out, not_228_out, not_229_out, not_230_out);
  and and_38 (JAL, OP0, OP1, not_231_out, not_232_out, not_233_out, not_234_out);
  or or_1 (MemToReg, and_4_out, and_5_out);
  or or_2 (ALU_SRC, and_7_out, and_8_out, and_9_out, and_10_out);
  or or_3 (RegWrite, and_11_out, and_12_out, and_13_out, and_14_out, and_15_out, and_16_out, and_17_out, and_18_out, and_19_out, and_20_out);
  or or_4 (SignedExt, and_22_out, and_23_out, and_24_out, and_25_out);
  or or_5 (RegDst, and_26_out, and_27_out, and_28_out, and_29_out, and_30_out, and_31_out, and_32_out);
  or or_6 (JUMP, and_36_out, and_37_out);
endmodule

// ALU
module MIPS_ALU (
  input  [4:0] shamt,
  input  [31:0] X,
  input  [31:0] Y,
  input  [3:0] AluOP,
  output Equal,
  output [31:0] Result,
  output [31:0] Result_2
);

  wire [0:0] comparator_1_lt, comparator_2_lt;
  wire [31:0] adder_1_out, AND_out, divider_1_out, divider_1_rem, multiplier_1_cout, multiplier_1_out,
       NOR_out, OR_out, shifter_1_out, shifter_2_out, shifter_3_out, subtractor_1_out, XOR_out;

  assign AND_out = X & Y;  // AND_Gate AND, 32 bits wide
  assign OR_out = X | Y;  // OR_Gate OR, 32 bits wide
  Shifter #(.width(32), .shift("ll")) shifter_1 (.in(Y), .\dist (shamt), .out(shifter_1_out));
  Shifter #(.width(32), .shift("ar")) shifter_2 (.in(Y), .\dist (shamt), .out(shifter_2_out));
  Shifter #(.width(32), .shift("lr")) shifter_3 (.in(Y), .\dist (shamt), .out(shifter_3_out));
  Multiplier #(.width(32)) multiplier_1 (.a(X), .b(Y), .out(multiplier_1_out), .cout(multiplier_1_cout));  // open: cin
  Divider #(.width(32)) divider_1 (.a(X), .b(Y), .out(divider_1_out), .rem(divider_1_rem));  // open: upper
  Adder #(.width(32)) adder_1 (.a(X), .b(Y), .out(adder_1_out));  // open: cin, cout
  Subtractor #(.width(32)) subtractor_1 (.a(X), .b(Y), .out(subtractor_1_out));  // open: bin, bout
  assign XOR_out = X ^ Y;  // XOR_Gate XOR, 32 bits wide
  assign NOR_out = ~(X | Y);  // NOR_Gate NOR, 32 bits wide
  Comparator #(.width(32), .mode("twosComplement")) comparator_1 (
    .a(X), .b(Y), .eq(Equal), .lt(comparator_1_lt[0]));  // open: gt
  Comparator #(.width(32), .mode("unsigned")) comparator_2 (.a(X), .b(Y), .lt(comparator_2_lt[0]));  // open: gt, eq
  Multiplexer #(.select(4), .width(32), .disabled("Z"), .enable("false")) multiplexer_1 (
    .in0(shifter_1_out), .in1(shifter_2_out), .in2(shifter_3_out), .in3(multiplier_1_out),
    .in4(divider_1_out), .in5(adder_1_out), .in6(subtractor_1_out), .in7(AND_out), .in8(OR_out),
    .in9(XOR_out), .in10(NOR_out), .in11({{31{1'b0}}, comparator_1_lt[0]}),
    .in12({{31{1'b0}}, comparator_2_lt[0]}), .in13({32{1'b0}}), .in14({32{1'b0}}), .in15({32{1'b0}}),
    .out(Result), .sel(AluOP));
  Multiplexer #(.select(4), .width(32), .disabled("Z"), .enable("false")) multiplexer_2 (
    .in0({32{1'b0}}), .in1({32{1'b0}}), .in2({32{1'b0}}), .in3(multiplier_1_cout), .in4(divider_1_rem),
    .in5({32{1'b0}}), .in6({32{1'b0}}), .in7({32{1'b0}}), .in8({32{1'b0}}), .in9({32{1'b0}}),
    .in10({32{1'b0}}), .in11({32{1'b0}}), .in12({32{1'b0}}), .in13({32{1'b0}}), .in14({32{1'b0}}),
    .in15({32{1'b0}}), .out(Result_2), .sel(AluOP));

  // Other names for the same wires on the sheet: Result2[31:0] = Result_2; S[3:0] = AluOP

  // Notes on the sheet:
  //   不要改变此引脚区域内容，也不要改变ALU封装形式
  //   输入引脚
  //   输出引脚
endmodule

module MIPS_Regifile (
  input  [31:0] Din,
  input  Clk,
  input  WE,
  input  [4:0] R1_num,
  input  [4:0] W_num,
  input  [4:0] R2_num,
  output [31:0] R1,
  output [31:0] R2
);

  // RegisterFile registerfile_1: pin names not known; wires that end beside it: Din, Clk, WE, W_num, R1_num, R2_num, R1, R2
endmodule

module \理想流水线  (
  output RegWrite,
  output MemWrite,
  output [31:0] IF_PC,
  output [31:0] ID_PC,
  output [31:0] EX_PC,
  output [31:0] M_PC,
  output [31:0] WB_PC,
  output [31:0] RDin,
  output [31:0] MDin,
  output [31:0] LedData
);

  wire CLK, clock_1_out, clock_2_out, comparator_1_eq, comparator_1_lt, controlled_buffer_1_out, d_ff_1_q,
       Go, IR1, IR2, IR3, nand_1_out, RST, W1, W2, W3;
  wire [12:0] CNT_num;
  wire [15:0] \LoadUse次数 , \总周期数 , \插入气泡数 , \无条件分支数 , \条件分支成功数 ;
  wire [31:0] EX_IR, ID_IR, IF_IR, MEM_IR, WB_IR;

  Button \u_总复位  (.out(RST));
  Button _1 (.out(IR1));
  Button _2 (.out(IR2));
  Button _3 (.out(IR3));
  // Probe on \总周期数 
  // Probe on \总周期数 
  Button \u_继续运行  (.out(Go));
  LED #(.active("true")) led_1 (.in(W1));
  LED #(.active("true")) led_2 (.in(W2));
  LED #(.active("true")) led_3 (.in(W3));
  Hex_Digit_Display hex_digit_display_1 (.value(LedData[31:28]));  // open: dp
  // Probe on IF_PC[19:0]
  // Mips_Probe mips_probe_1: pin names not known; wires that end beside it: IF_IR
  Hex_Digit_Display hex_digit_display_2 (.value(LedData[27:24]));  // open: dp
  Hex_Digit_Display hex_digit_display_3 (.value(LedData[23:20]));  // open: dp
  // Probe on ID_PC[19:0]
  // Mips_Probe mips_probe_2: pin names not known; wires that end beside it: ID_IR
  Hex_Digit_Display hex_digit_display_4 (.value(LedData[15:12]));  // open: dp
  Hex_Digit_Display hex_digit_display_5 (.value(LedData[19:16]));  // open: dp
  Hex_Digit_Display hex_digit_display_6 (.value(LedData[7:4]));  // open: dp
  Hex_Digit_Display hex_digit_display_7 (.value(LedData[11:8]));  // open: dp
  Clock #(.highDuration(1), .lowDuration(1)) clock_1 (.out(clock_1_out));
  // Probe on EX_PC[19:0]
  // Mips_Probe mips_probe_3: pin names not known; wires that end beside it: clock_1_out, EX_IR, CLK
  Hex_Digit_Display hex_digit_display_8 (.value(LedData[3:0]));  // open: dp
  // Probe on \总周期数 
  // Probe on M_PC[19:0]
  // Mips_Probe mips_probe_4: pin names not known; wires that end beside it: MEM_IR
  // Probe on \总周期数 
  // Probe on \无条件分支数 
  // Probe on \条件分支成功数 
  // Probe on \插入气泡数 
  // Probe on \LoadUse次数 
  // Probe on IF_PC[11:0]
  // Probe on WB_PC[19:0]
  // Mips_Probe mips_probe_5: pin names not known; wires that end beside it: WB_IR
  // Probe on EX_PC[11:0]
  // Probe on ID_PC[11:0]
  // Probe on M_PC[11:0]
  D_Flip_Flop #(.trigger("high"), .Pre_Clr_Positions("LEGACY"), .NegatePresetClear("false"), .enable("true"), .NewFFLayout("false")) d_ff_1 (.Q(d_ff_1_q));  // open: clk, D, Qn, preset, en, reset
  // Probe on 13'hc
  // Probe on WB_PC[11:0]
  Comparator #(.width(13), .mode("twosComplement")) comparator_1 (
    .a(CNT_num), .b(13'hc), .eq(comparator_1_eq), .lt(comparator_1_lt));  // open: gt
  Clock #(.highDuration(1), .lowDuration(1)) clock_2 (.out(clock_2_out));
  nand nand_1 (nand_1_out, d_ff_1_q, comparator_1_eq);
  Counter #(.width(13), .max('h1fff), .ongoal("stay"), .trigger("rising"), .behavior("old")) counter_1 (
    .count(comparator_1_lt), .Q(CNT_num), .clk(clock_2_out));  // open: load, D, carry, clr, preset
  assign controlled_buffer_1_out = nand_1_out ? clock_2_out : 1'bz;  // Controlled_Buffer controlled_buffer_1
  Pull_Resistor #(.pull(1)) pull_resistor_1 (.node(controlled_buffer_1_out));

  // Other names for the same wires on the sheet: MEM_PC[31:0] = M_PC

  // Notes on the sheet:
  //   中断源
  //   时空图监测，可删除
  //   中断等待指示
  //   数码管输出
  //   控制位
  //   流水调试日志用
  //   暂停节拍，不能为0
  //   戳工具置1进入计数暂停模式，ctrl+k时钟自动运行到对应节拍暂停
  //   ctrl+k关闭时钟连续运行，将控制位置零，进入单步调试模式调试
  //   用这个时钟源需要去掉电路中的其他时钟源
  //   可计数暂停的时钟源
  //   断开防止影响气泡流水线
  //   为方便自动评测，需要输出流水线各段保存的PC值，注意是PC不是PC+4，另外ID段寄存器写入信息，Mem段内存写入信息也要输出
endmodule

module \气泡流水线  (
  output RegWrite,
  output MemWrite,
  output [31:0] IF_PC,
  output [31:0] ID_PC,
  output [31:0] EX_PC,
  output [31:0] M_PC,
  output [31:0] WB_PC,
  output [31:0] RDin,
  output [31:0] MDin,
  output [31:0] LedData
);

  wire CLK, clock_1_out, clock_2_out, comparator_1_eq, comparator_1_lt, controlled_buffer_1_out, d_ff_1_q,
       Go, IR1, IR2, IR3, nand_1_out, RST, W1, W2, W3;
  wire [12:0] CNT_num;
  wire [15:0] \LoadUse次数 , \总周期数 , \插入气泡数 , \无条件分支数 , \条件分支成功数 ;
  wire [31:0] EX_IR, ID_IR, IF_IR, MEM_IR, WB_IR;

  Button \u_总复位  (.out(RST));
  Button _1 (.out(IR1));
  Button _2 (.out(IR2));
  Button _3 (.out(IR3));
  // Probe on \总周期数 
  // Probe on \总周期数 
  Button \u_继续运行  (.out(Go));
  LED #(.active("true")) led_1 (.in(W1));
  LED #(.active("true")) led_2 (.in(W2));
  LED #(.active("true")) led_3 (.in(W3));
  Hex_Digit_Display hex_digit_display_1 (.value(LedData[31:28]));  // open: dp
  // Probe on IF_PC[19:0]
  // Mips_Probe mips_probe_1: pin names not known; wires that end beside it: IF_IR
  Hex_Digit_Display hex_digit_display_2 (.value(LedData[23:20]));  // open: dp
  Hex_Digit_Display hex_digit_display_3 (.value(LedData[27:24]));  // open: dp
  // Probe on ID_PC[19:0]
  // Mips_Probe mips_probe_2: pin names not known; wires that end beside it: ID_IR
  Hex_Digit_Display hex_digit_display_4 (.value(LedData[19:16]));  // open: dp
  Hex_Digit_Display hex_digit_display_5 (.value(LedData[15:12]));  // open: dp
  Hex_Digit_Display hex_digit_display_6 (.value(LedData[7:4]));  // open: dp
  Hex_Digit_Display hex_digit_display_7 (.value(LedData[11:8]));  // open: dp
  Clock #(.highDuration(1), .lowDuration(1)) clock_1 (.out(clock_1_out));
  // Probe on EX_PC[19:0]
  // Mips_Probe mips_probe_3: pin names not known; wires that end beside it: EX_IR, clock_1_out, CLK
  Hex_Digit_Display hex_digit_display_8 (.value(LedData[3:0]));  // open: dp
  // Probe on \总周期数 
  // Probe on M_PC[19:0]
  // Mips_Probe mips_probe_4: pin names not known; wires that end beside it: MEM_IR
  // Probe on \总周期数 
  // Probe on \无条件分支数 
  // Probe on \条件分支成功数 
  // Probe on \插入气泡数 
  // Probe on \LoadUse次数 
  // Probe on IF_PC[11:0]
  // Probe on WB_PC[19:0]
  // Mips_Probe mips_probe_5: pin names not known; wires that end beside it: WB_IR
  // Probe on EX_PC[11:0]
  // Probe on ID_PC[11:0]
  // Probe on M_PC[11:0]
  D_Flip_Flop #(.trigger("high"), .Pre_Clr_Positions("LEGACY"), .NegatePresetClear("false"), .enable("true"), .NewFFLayout("false")) d_ff_1 (.Q(d_ff_1_q));  // open: clk, D, Qn, preset, en, reset
  // Probe on 13'h611
  // Probe on WB_PC[11:0]
  Comparator #(.width(13), .mode("twosComplement")) comparator_1 (
    .a(CNT_num), .b(13'h611), .eq(comparator_1_eq), .lt(comparator_1_lt));  // open: gt
  Clock #(.highDuration(1), .lowDuration(1)) clock_2 (.out(clock_2_out));
  nand nand_1 (nand_1_out, d_ff_1_q, comparator_1_eq);
  Counter #(.width(13), .max('h1fff), .ongoal("stay"), .trigger("rising"), .behavior("old")) counter_1 (
    .count(comparator_1_lt), .Q(CNT_num), .clk(clock_2_out));  // open: load, D, carry, clr, preset
  assign controlled_buffer_1_out = nand_1_out ? clock_2_out : 1'bz;  // Controlled_Buffer controlled_buffer_1
  Pull_Resistor #(.pull(1)) pull_resistor_1 (.node(controlled_buffer_1_out));

  // Other names for the same wires on the sheet: MEM_PC[31:0] = M_PC

  // Notes on the sheet:
  //   中断源
  //   时空图监测，可删除
  //   中断等待指示
  //   数码管输出
  //   控制位
  //   流水调试日志用
  //   暂停节拍，不能为0
  //   戳工具置1进入计数暂停模式，ctrl+k时钟自动运行到对应节拍暂停
  //   ctrl+k关闭时钟连续运行，将控制位置零，进入单步调试模式调试
  //   可计数暂停的时钟源
  //   为方便自动评测，需要输出流水线各段保存的PC值，注意是PC不是PC+4，另外ID段寄存器写入信息，Mem段内存写入信息也要输出
endmodule

module \重定向流水线  (
  output RegWrite,
  output MemWrite,
  output [31:0] IF_PC,
  output [31:0] ID_PC,
  output [31:0] EX_PC,
  output [31:0] M_PC,
  output [31:0] WB_PC,
  output [31:0] RDin,
  output [31:0] MDin,
  output [31:0] LedData
);

  wire CLK, clock_1_out, clock_2_out, comparator_1_eq, comparator_1_lt, d_ff_1_q, Go, IR1, IR2, IR3,
       nand_1_out, RST, W1, W2, W3;
  wire [12:0] CNT_num;
  wire [15:0] \LoadUse次数 , \总周期数 , \插入气泡数 , \无条件分支数 , \条件分支成功数 ;
  wire [31:0] EX_IR, ID_IR, IF_IR, MEM_IR, WB_IR;

  Button \u_总复位  (.out(RST));
  Button _1 (.out(IR1));
  Button _2 (.out(IR2));
  Button _3 (.out(IR3));
  // Probe on \总周期数 
  // Probe on \总周期数 
  Button \u_继续运行  (.out(Go));
  LED #(.active("true")) led_1 (.in(W1));
  LED #(.active("true")) led_2 (.in(W2));
  LED #(.active("true")) led_3 (.in(W3));
  Hex_Digit_Display hex_digit_display_1 (.value(LedData[31:28]));  // open: dp
  // Probe on IF_PC[19:0]
  // Mips_Probe mips_probe_1: pin names not known; wires that end beside it: IF_IR
  Hex_Digit_Display hex_digit_display_2 (.value(LedData[27:24]));  // open: dp
  Hex_Digit_Display hex_digit_display_3 (.value(LedData[23:20]));  // open: dp
  // Probe on ID_PC[19:0]
  // Mips_Probe mips_probe_2: pin names not known; wires that end beside it: ID_IR
  Hex_Digit_Display hex_digit_display_4 (.value(LedData[15:12]));  // open: dp
  Hex_Digit_Display hex_digit_display_5 (.value(LedData[19:16]));  // open: dp
  Hex_Digit_Display hex_digit_display_6 (.value(LedData[7:4]));  // open: dp
  Hex_Digit_Display hex_digit_display_7 (.value(LedData[11:8]));  // open: dp
  Clock #(.highDuration(1), .lowDuration(1)) clock_1 (.out(clock_1_out));
  // Probe on EX_PC[19:0]
  // Mips_Probe mips_probe_3: pin names not known; wires that end beside it: clock_1_out, EX_IR, CLK
  Hex_Digit_Display hex_digit_display_8 (.value(LedData[3:0]));  // open: dp
  // Probe on \总周期数 
  // Probe on M_PC[19:0]
  // Mips_Probe mips_probe_4: pin names not known; wires that end beside it: MEM_IR
  // Probe on \总周期数 
  // Probe on \无条件分支数 
  // Probe on \条件分支成功数 
  // Probe on \插入气泡数 
  // Probe on \LoadUse次数 
  // Probe on IF_PC[11:0]
  // Probe on WB_PC[19:0]
  // Mips_Probe mips_probe_5: pin names not known; wires that end beside it: WB_IR
  // Probe on ID_PC[11:0]
  // Probe on EX_PC[11:0]
  // Probe on M_PC[11:0]
  D_Flip_Flop #(.trigger("high"), .Pre_Clr_Positions("LEGACY"), .NegatePresetClear("false"), .enable("true"), .NewFFLayout("false")) d_ff_1 (.Q(d_ff_1_q));  // open: clk, D, Qn, preset, en, reset
  // Probe on 13'h39d
  // Probe on WB_PC[11:0]
  Comparator #(.width(13), .mode("twosComplement")) comparator_1 (
    .a(CNT_num), .b(13'h39d), .eq(comparator_1_eq), .lt(comparator_1_lt));  // open: gt
  Clock #(.highDuration(1), .lowDuration(1)) clock_2 (.out(clock_2_out));
  nand nand_1 (nand_1_out, d_ff_1_q, comparator_1_eq);
  Counter #(.width(13), .max('h1fff), .ongoal("stay"), .trigger("rising"), .behavior("old")) counter_1 (
    .count(comparator_1_lt), .Q(CNT_num), .clk(clock_2_out));  // open: load, D, carry, clr, preset
  assign CLK = nand_1_out ? clock_2_out : 1'bz;  // Controlled_Buffer controlled_buffer_1
  Pull_Resistor #(.pull(1)) pull_resistor_1 (.node(CLK));

  // Other names for the same wires on the sheet: MEM_PC[31:0] = M_PC

  // Notes on the sheet:
  //   中断源
  //   时空图监测，可删除
  //   中断等待指示
  //   数码管输出
  //   控制位
  //   流水调试日志用
  //   暂停节拍，不能为0
  //   戳工具置1进入计数暂停模式，ctrl+k时钟自动运行到对应节拍暂停
  //   ctrl+k关闭时钟连续运行，将控制位置零，进入单步调试模式调试
  //   可计数暂停的时钟源
  //   为方便自动评测，需要输出流水线各段保存的PC值，注意是PC不是PC+4，另外ID段寄存器写入信息，Mem段内存写入信息也要输出
endmodule

module \中断按键参考电路  (
  input  \同步清零信号 ,
  output \与中断屏蔽位与 
);

  wire \_1号中断_out , and_1_out, clock_1_out, d_ff_1_q, or_1_out, or_2_out;

  Clock #(.highDuration(1), .lowDuration(1)) clock_1 (.out(clock_1_out));
  Button \_1号中断  (.out(\_1号中断_out ));
  LED #(.active("true")) \_1号中断等待指示灯  (.in(or_1_out));
  or or_1 (or_1_out, \与中断屏蔽位与 , d_ff_1_q);
  D_Flip_Flop #(.trigger("rising"), .Pre_Clr_Positions("LEGACY"), .NegatePresetClear("false"), .enable("true"), .NewFFLayout("false")) d_ff_1 (
    .clk(\_1号中断_out ), .D(1'b1), .Q(d_ff_1_q), .reset(\与中断屏蔽位与 ));  // open: Qn, preset, en
  or or_2 (or_2_out, d_ff_1_q, \与中断屏蔽位与 );
  and and_1 (and_1_out, or_2_out, ~\同步清零信号 );  // AND_Gate
  D_Flip_Flop #(.trigger("rising"), .Pre_Clr_Positions("LEGACY"), .NegatePresetClear("false"), .enable("true"), .NewFFLayout("false")) IR1 (
    .clk(clock_1_out), .D(and_1_out), .Q(\与中断屏蔽位与 ));  // open: Qn, preset, en, reset
  \单周期硬布线控制器  \u_单周期硬布线控制器_1  ();  // open: Func, OP, ALU_OP, MemToReg, MemWrite, ALU_SRC, RegWrite, SysCALL, SignedExt, RegDst, JR, JMP, Beq, JAL, Bne, sllv, bgtz, lb

  // Notes on the sheet:
  //   中断信号采样参考电路
  //   Reset 
endmodule

module \单周期MIPS_单级中断  (
  input  IR1,
  input  IR2,
  input  IR3,
  output RegWrite,
  output MemWrite,
  output [31:0] PC,
  output [31:0] IR,
  output [31:0] RDin,
  output [31:0] MDin,
  output [31:0] LedData
);

  wire _1_out, _2_out, _3_out, CLK, comparator_1_eq, comparator_2_eq, comparator_3_eq, comparator_4_eq, Go,
       IR1_t, IR2_t, IR3_t, IRA, IRB, IRC, or_1_out, W1, W2, W3;
  wire [15:0] \总周期数 ;

  Clock #(.highDuration(1), .lowDuration(1)) clock_1 (.out(CLK));
  Button _1 (.out(_1_out));
  Button _2 (.out(_2_out));
  Button _3 (.out(_3_out));
  Button \u_继续运行  (.out(Go));
  LED #(.active("true")) led_1 (.in(W1));
  LED #(.active("true")) led_2 (.in(W2));
  LED #(.active("true")) led_3 (.in(W3));
  Hex_Digit_Display hex_digit_display_1 (.value(LedData[31:28]));  // open: dp
  Comparator #(.width(16), .mode("twosComplement")) comparator_1 (
    .a(16'h23b), .b(\总周期数 ), .eq(comparator_1_eq));  // open: gt, lt
  Comparator #(.width(16), .mode("twosComplement")) comparator_2 (
    .a(\总周期数 ), .b(16'h1), .eq(comparator_2_eq));  // open: gt, lt
  Comparator #(.width(16), .mode("twosComplement")) comparator_3 (
    .a(\总周期数 ), .b(16'h4), .eq(comparator_3_eq));  // open: gt, lt
  Comparator #(.width(16), .mode("twosComplement")) comparator_4 (
    .a(\总周期数 ), .b(16'h7), .eq(comparator_4_eq));  // open: gt, lt
  Hex_Digit_Display hex_digit_display_2 (.value(LedData[23:20]));  // open: dp
  Hex_Digit_Display hex_digit_display_3 (.value(LedData[27:24]));  // open: dp
  or or_1 (or_1_out, comparator_1_eq, comparator_2_eq);
  assign IRA = or_1_out ? ~CLK : 1'bz;  // Controlled_Inverter controlled_inverter_1
  assign IRB = comparator_3_eq ? ~CLK : 1'bz;  // Controlled_Inverter controlled_inverter_2
  assign IRC = comparator_4_eq ? ~CLK : 1'bz;  // Controlled_Inverter controlled_inverter_3
  Hex_Digit_Display hex_digit_display_4 (.value(LedData[19:16]));  // open: dp
  Hex_Digit_Display hex_digit_display_5 (.value(LedData[15:12]));  // open: dp
  Pull_Resistor #(.pull(0)) pull_resistor_1 (.node(IRA));
  Pull_Resistor #(.pull(0)) pull_resistor_2 (.node(IRB));
  Pull_Resistor #(.pull(0)) pull_resistor_3 (.node(IRC));
  Hex_Digit_Display hex_digit_display_6 (.value(LedData[7:4]));  // open: dp
  Hex_Digit_Display hex_digit_display_7 (.value(LedData[11:8]));  // open: dp
  // Probe on \总周期数 
  Hex_Digit_Display hex_digit_display_8 (.value(LedData[3:0]));  // open: dp
  or or_2 (IR1_t, IR1, IRA);
  or or_3 (IR2_t, IR2, IRB);
  or or_4 (IR3_t, IR3, IRC);

  // Notes on the sheet:
  //   中断源
  //   中断等待指示
  //   总复位信号应将除ROM以外所有存储组件全部清零
  //   单级中断测试信号模拟器
  //   数码管输出
  //   数码管输出应该用寄存器锁存，否则显示数据只能一闪而过
  //   为方便自动评测，需要输出PC，IR，寄存器堆写如数据RDin
  //   RAM写使能MemWrite、RAM写入数据MDin等信号
endmodule

module \单周期MIPS_多级中断  (
  input  IR1,
  input  IR2,
  input  IR3,
  output RegWrite,
  output MemWrite,
  output [31:0] PC,
  output [31:0] IR,
  output [31:0] RDin,
  output [31:0] MDin,
  output [31:0] LedData
);

  wire CLK, comparator_1_eq, comparator_2_eq, comparator_3_eq, comparator_4_eq, comparator_5_eq, Go, IR1_t,
       IR2_t, IR3_t, IRA, IRB, IRC, or_1_out, or_2_out, W1, W2, W3;
  wire [15:0] \总周期数 ;

  Clock #(.highDuration(1), .lowDuration(1)) clock_1 (.out(CLK));
  Button _1 ();  // open: out
  Button _2 ();  // open: out
  Button _3 ();  // open: out
  Button \u_继续运行  (.out(Go));
  LED #(.active("true")) led_1 (.in(W1));
  LED #(.active("true")) led_2 (.in(W2));
  LED #(.active("true")) led_3 (.in(W3));
  Hex_Digit_Display hex_digit_display_1 (.value(LedData[31:28]));  // open: dp
  Comparator #(.width(16), .mode("twosComplement")) comparator_1 (
    .a(\总周期数 ), .b(16'h7), .eq(comparator_1_eq));  // open: gt, lt
  Comparator #(.width(16), .mode("twosComplement")) comparator_2 (
    .a(\总周期数 ), .b(16'h241), .eq(comparator_2_eq));  // open: gt, lt
  Hex_Digit_Display hex_digit_display_2 (.value(LedData[27:24]));  // open: dp
  Hex_Digit_Display hex_digit_display_3 (.value(LedData[23:20]));  // open: dp
  Comparator #(.width(16), .mode("twosComplement")) comparator_3 (
    .a(16'h258), .b(\总周期数 ), .eq(comparator_3_eq));  // open: gt, lt
  or or_1 (or_1_out, comparator_3_eq, comparator_4_eq);
  Comparator #(.width(16), .mode("twosComplement")) comparator_4 (
    .a(\总周期数 ), .b(16'h1), .eq(comparator_4_eq));  // open: gt, lt
  Comparator #(.width(16), .mode("twosComplement")) comparator_5 (
    .a(\总周期数 ), .b(16'h4), .eq(comparator_5_eq));  // open: gt, lt
  or or_2 (or_2_out, comparator_1_eq, comparator_2_eq);
  Hex_Digit_Display hex_digit_display_4 (.value(LedData[15:12]));  // open: dp
  Hex_Digit_Display hex_digit_display_5 (.value(LedData[19:16]));  // open: dp
  Pull_Resistor #(.pull(0)) pull_resistor_1 (.node(IRA));
  assign IRA = or_1_out ? ~CLK : 1'bz;  // Controlled_Inverter controlled_inverter_1
  Pull_Resistor #(.pull(0)) pull_resistor_2 (.node(IRB));
  assign IRB = comparator_5_eq ? ~CLK : 1'bz;  // Controlled_Inverter controlled_inverter_2
  Pull_Resistor #(.pull(0)) pull_resistor_3 (.node(IRC));
  assign IRC = or_2_out ? ~CLK : 1'bz;  // Controlled_Inverter controlled_inverter_3
  Hex_Digit_Display hex_digit_display_6 (.value(LedData[11:8]));  // open: dp
  Hex_Digit_Display hex_digit_display_7 (.value(LedData[7:4]));  // open: dp
  // Probe on \总周期数 
  Hex_Digit_Display hex_digit_display_8 (.value(LedData[3:0]));  // open: dp
  or or_3 (IR1_t, IR1, IRA);
  or or_4 (IR2_t, IR2, IRB);
  or or_5 (IR3_t, IR3, IRC);

  // Notes on the sheet:
  //   中断源
  //   中断等待指示
  //   总复位信号应将除ROM以外所有存储组件全部清零
  //   多级中断测试信号模拟器
  //   数码管输出
  //   数码管输出应该用寄存器锁存，否则显示数据只能一闪而过
  //   为方便自动评测，需要输出PC，IR，寄存器堆写如数据RDin
  //   RAM写使能MemWrite、RAM写入数据MDin等信号
endmodule

module \封装正确性测试  (
);

  wire IR1, IR2, IR3, MemW, RegW;
  wire [31:0] EX_PC, ID_PC, IF_PC, IR, LED, MDin, MDinr, MEM_PC, PC, RDin, RDinr, WB_PC;

  \单周期MIPS  \u_单周期mips_1  (
    .IR1(IR1), .IR2(IR2), .IR3(IR3), .RegWrite(RegW), .MemWrite(MemW), .PC(PC), .IR(IR), .RDin(RDin),
    .MDin(MDin), .LedData(LED));
  \气泡流水线  \u_气泡流水线_1  (
    .RegWrite(RegW), .MemWrite(MemW), .IF_PC(IF_PC), .ID_PC(ID_PC), .EX_PC(EX_PC), .M_PC(MEM_PC),
    .WB_PC(WB_PC), .RDin(RDinr), .MDin(MDinr), .LedData(LED));
  \单周期MIPS_单级中断  \u_单周期mips_单级中断_1  (
    .IR1(IR1), .IR2(IR2), .IR3(IR3), .RegWrite(RegW), .MemWrite(MemW), .PC(PC), .IR(IR), .RDin(RDin),
    .MDin(MDin), .LedData(LED));
  \理想流水线  \u_理想流水线_1  (
    .RegWrite(RegW), .MemWrite(MemW), .IF_PC(IF_PC), .ID_PC(ID_PC), .EX_PC(EX_PC), .M_PC(MEM_PC),
    .WB_PC(WB_PC), .RDin(RDinr), .MDin(MDinr), .LedData(LED));
  \重定向流水线  \u_重定向流水线_1  (
    .RegWrite(RegW), .MemWrite(MemW), .IF_PC(IF_PC), .ID_PC(ID_PC), .EX_PC(EX_PC), .M_PC(MEM_PC),
    .WB_PC(WB_PC), .RDin(RDinr), .MDin(MDinr), .LedData(LED));
  \单周期MIPS_多级中断  \u_单周期mips_多级中断_1  (
    .IR1(IR1), .IR2(IR2), .IR3(IR3), .RegWrite(RegW), .MemWrite(MemW), .PC(PC), .IR(IR), .RDin(RDin),
    .MDin(MDin), .LedData(LED));

  // Notes on the sheet:
  //   单周期封装测试
  //   气泡流水封装测试
  //   单周期+单级中断封装测试
  //   请检查上面封装有无位宽不匹配，引脚标签是否和连接的标签相对应，否则无法在educoder平台上正确测试
  //   理想流水封装测试
  //   重定向流水封装测试
  //   单周期+多级中断封装测试
endmodule

module IF__ID (
  input  CLK,
  input  \同步清零_高 ,
  input  \使能端_低 ,
  input  [31:0] PC,
  input  [31:0] IR,
  input  [31:0] PC_4,
  input  PredictJump,
  output [31:0] PC_2,
  output [31:0] IR_2,
  output [31:0] PC_4_2,
  output PredictJump_2
);

  wire multiplexer_4_out, not_1_out;
  wire [31:0] multiplexer_1_out, multiplexer_2_out, multiplexer_3_out;

  not not_1 (not_1_out, \使能端_低 );
  Multiplexer #(.select(1), .width(32), .disabled("Z"), .enable("false")) multiplexer_1 (
    .in0(PC), .in1({32{1'b0}}), .out(multiplexer_1_out), .sel(\同步清零_高 ));
  Multiplexer #(.select(1), .width(32), .disabled("Z"), .enable("false")) multiplexer_2 (
    .in0(IR), .in1({32{1'b0}}), .out(multiplexer_2_out), .sel(\同步清零_高 ));
  Multiplexer #(.select(1), .width(32), .disabled("Z"), .enable("false")) multiplexer_3 (
    .in0(PC_4), .in1({32{1'b0}}), .out(multiplexer_3_out), .sel(\同步清零_高 ));
  Multiplexer #(.select(1), .width(1), .disabled("Z"), .enable("false")) multiplexer_4 (
    .in0(PredictJump), .in1(1'b0), .out(multiplexer_4_out), .sel(\同步清零_高 ));
  Register #(.width(32), .trigger("rising"), .Select("low")) register_1 (
    .D(multiplexer_1_out), .en(not_1_out), .Q(PC_2), .clk(CLK));  // open: clr
  Register #(.width(32), .trigger("rising"), .Select("low")) register_2 (
    .D(multiplexer_2_out), .en(not_1_out), .Q(IR_2), .clk(CLK));  // open: clr
  Register #(.width(32), .trigger("rising"), .Select("low")) register_3 (
    .D(multiplexer_3_out), .en(not_1_out), .Q(PC_4_2), .clk(CLK));  // open: clr
  Register #(.width(1), .trigger("rising"), .Select("low")) register_4 (
    .D(multiplexer_4_out), .en(not_1_out), .Q(PredictJump_2), .clk(CLK));  // open: clr
  Pull_Resistor #(.pull(0)) pull_resistor_1 (.node(\同步清零_高 ));
  Pull_Resistor #(.pull(0)) pull_resistor_2 (.node(not_1_out));
endmodule

module ID__EX (
  input  CLK,
  input  \同步清零_高 ,
  input  \使能端_低 ,
  input  JMP,
  input  [31:0] IR,
  input  JR,
  input  signedext,
  input  [31:0] PC,
  input  beq,
  input  bne,
  input  [31:0] R1,
  input  memtoreg,
  input  [31:0] R2,
  input  memwrite,
  input  [3:0] aluop,
  input  sllv,
  input  [25:0] imm26,
  input  alu_src,
  input  [31:0] PC_4,
  input  bgtz,
  input  regwrite,
  input  [1:0] IF_Rs_F,
  input  [1:0] IF_Rt_F,
  input  lb,
  input  jal,
  input  regdst,
  input  syscall,
  input  PredictJump,
  output JMP_2,
  output [31:0] IR_2,
  output JR_2,
  output signedext_2,
  output [31:0] PC_2,
  output beq_2,
  output bne_2,
  output [31:0] R1_2,
  output memtoreg_2,
  output [31:0] R2_2,
  output memwrite_2,
  output [3:0] aluop_2,
  output sllv_2,
  output [25:0] imm26_2,
  output alu_src_2,
  output [31:0] PC_4_2,
  output bgtz_2,
  output regwrite_2,
  output [1:0] EX_Rs_F,
  output [1:0] EX_Rt_F,
  output lb_2,
  output jal_2,
  output regdst_2,
  output syscall_2,
  output PredictJump_2
);

  wire multiplexer_1_out, multiplexer_2_out, multiplexer_3_out, multiplexer_4_out, multiplexer_5_out,
       multiplexer_6_out, multiplexer_7_out, multiplexer_9_out, multiplexer_10_out, multiplexer_11_out,
       multiplexer_12_out, multiplexer_13_out, multiplexer_14_out, multiplexer_15_out, multiplexer_16_out,
       multiplexer_17_out, not_1_out;
  wire [1:0] multiplexer_24_out, multiplexer_25_out;
  wire [3:0] multiplexer_8_out;
  wire [25:0] multiplexer_22_out;
  wire [31:0] multiplexer_18_out, multiplexer_19_out, multiplexer_20_out, multiplexer_21_out,
       multiplexer_23_out;

  not not_1 (not_1_out, \使能端_低 );
  Multiplexer #(.select(1), .width(1), .disabled("Z"), .enable("false")) multiplexer_1 (
    .in0(JMP), .in1(1'b0), .out(multiplexer_1_out), .sel(\同步清零_高 ));
  Multiplexer #(.select(1), .width(1), .disabled("Z"), .enable("false")) multiplexer_2 (
    .in0(JR), .in1(1'b0), .out(multiplexer_2_out), .sel(\同步清零_高 ));
  Multiplexer #(.select(1), .width(1), .disabled("Z"), .enable("false")) multiplexer_3 (
    .in0(signedext), .in1(1'b0), .out(multiplexer_3_out), .sel(\同步清零_高 ));
  Multiplexer #(.select(1), .width(1), .disabled("Z"), .enable("false")) multiplexer_4 (
    .in0(beq), .in1(1'b0), .out(multiplexer_4_out), .sel(\同步清零_高 ));
  Multiplexer #(.select(1), .width(1), .disabled("Z"), .enable("false")) multiplexer_5 (
    .in0(bne), .in1(1'b0), .out(multiplexer_5_out), .sel(\同步清零_高 ));
  Multiplexer #(.select(1), .width(1), .disabled("Z"), .enable("false")) multiplexer_6 (
    .in0(memtoreg), .in1(1'b0), .out(multiplexer_6_out), .sel(\同步清零_高 ));
  Multiplexer #(.select(1), .width(1), .disabled("Z"), .enable("false")) multiplexer_7 (
    .in0(memwrite), .in1(1'b0), .out(multiplexer_7_out), .sel(\同步清零_高 ));
  Multiplexer #(.select(1), .width(4), .disabled("Z"), .enable("false")) multiplexer_8 (
    .in0(aluop), .in1(4'b0000), .out(multiplexer_8_out), .sel(\同步清零_高 ));
  Multiplexer #(.select(1), .width(1), .disabled("Z"), .enable("false")) multiplexer_9 (
    .in0(sllv), .in1(1'b0), .out(multiplexer_9_out), .sel(\同步清零_高 ));
  Multiplexer #(.select(1), .width(1), .disabled("Z"), .enable("false")) multiplexer_10 (
    .in0(alu_src), .in1(1'b0), .out(multiplexer_10_out), .sel(\同步清零_高 ));
  Multiplexer #(.select(1), .width(1), .disabled("Z"), .enable("false")) multiplexer_11 (
    .in0(bgtz), .in1(1'b0), .out(multiplexer_11_out), .sel(\同步清零_高 ));
  Multiplexer #(.select(1), .width(1), .disabled("Z"), .enable("false")) multiplexer_12 (
    .in0(regwrite), .in1(1'b0), .out(multiplexer_12_out), .sel(\同步清零_高 ));
  Multiplexer #(.select(1), .width(1), .disabled("Z"), .enable("false")) multiplexer_13 (
    .in0(lb), .in1(1'b0), .out(multiplexer_13_out), .sel(\同步清零_高 ));
  Multiplexer #(.select(1), .width(1), .disabled("Z"), .enable("false")) multiplexer_14 (
    .in0(jal), .in1(1'b0), .out(multiplexer_14_out), .sel(\同步清零_高 ));
  Multiplexer #(.select(1), .width(1), .disabled("Z"), .enable("false")) multiplexer_15 (
    .in0(regdst), .in1(1'b0), .out(multiplexer_15_out), .sel(\同步清零_高 ));
  Multiplexer #(.select(1), .width(1), .disabled("Z"), .enable("false")) multiplexer_16 (
    .in0(syscall), .in1(1'b0), .out(multiplexer_16_out), .sel(\同步清零_高 ));
  Multiplexer #(.select(1), .width(1), .disabled("Z"), .enable("false")) multiplexer_17 (
    .in0(PredictJump), .in1(1'b0), .out(multiplexer_17_out), .sel(\同步清零_高 ));
  Register #(.width(1), .trigger("rising"), .Select("low")) register_1 (
    .D(multiplexer_1_out), .en(not_1_out), .Q(JMP_2), .clk(CLK));  // open: clr
  Register #(.width(1), .trigger("rising"), .Select("low")) register_2 (
    .D(multiplexer_2_out), .en(not_1_out), .Q(JR_2), .clk(CLK));  // open: clr
  Register #(.width(1), .trigger("rising"), .Select("low")) register_3 (
    .D(multiplexer_3_out), .en(not_1_out), .Q(signedext_2), .clk(CLK));  // open: clr
  Register #(.width(1), .trigger("rising"), .Select("low")) register_4 (
    .D(multiplexer_4_out), .en(not_1_out), .Q(beq_2), .clk(CLK));  // open: clr
  Register #(.width(1), .trigger("rising"), .Select("low")) register_5 (
    .D(multiplexer_5_out), .en(not_1_out), .Q(bne_2), .clk(CLK));  // open: clr
  Register #(.width(1), .trigger("rising"), .Select("low")) register_6 (
    .D(multiplexer_6_out), .en(not_1_out), .Q(memtoreg_2), .clk(CLK));  // open: clr
  Register #(.width(1), .trigger("rising"), .Select("low")) register_7 (
    .D(multiplexer_7_out), .en(not_1_out), .Q(memwrite_2), .clk(CLK));  // open: clr
  Register #(.width(4), .trigger("rising"), .Select("low")) register_8 (
    .D(multiplexer_8_out), .en(not_1_out), .Q(aluop_2), .clk(CLK));  // open: clr
  Register #(.width(1), .trigger("rising"), .Select("low")) register_9 (
    .D(multiplexer_9_out), .en(not_1_out), .Q(sllv_2), .clk(CLK));  // open: clr
  Register #(.width(1), .trigger("rising"), .Select("low")) register_10 (
    .D(multiplexer_10_out), .en(not_1_out), .Q(alu_src_2), .clk(CLK));  // open: clr
  Register #(.width(1), .trigger("rising"), .Select("low")) register_11 (
    .D(multiplexer_11_out), .en(not_1_out), .Q(bgtz_2), .clk(CLK));  // open: clr
  Register #(.width(1), .trigger("rising"), .Select("low")) register_12 (
    .D(multiplexer_12_out), .en(not_1_out), .Q(regwrite_2), .clk(CLK));  // open: clr
  Register #(.width(1), .trigger("rising"), .Select("low")) register_13 (
    .D(multiplexer_13_out), .en(not_1_out), .Q(lb_2), .clk(CLK));  // open: clr
  Register #(.width(1), .trigger("rising"), .Select("low")) register_14 (
    .D(multiplexer_14_out), .en(not_1_out), .Q(jal_2), .clk(CLK));  // open: clr
  Register #(.width(1), .trigger("rising"), .Select("low")) register_15 (
    .D(multiplexer_15_out), .en(not_1_out), .Q(regdst_2), .clk(CLK));  // open: clr
  Register #(.width(1), .trigger("rising"), .Select("low")) register_16 (
    .D(multiplexer_16_out), .en(not_1_out), .Q(syscall_2), .clk(CLK));  // open: clr
  Register #(.width(1), .trigger("rising"), .Select("low")) register_17 (
    .D(multiplexer_17_out), .en(not_1_out), .Q(PredictJump_2), .clk(CLK));  // open: clr
  Pull_Resistor #(.pull(0)) pull_resistor_1 (.node(\同步清零_高 ));
  Pull_Resistor #(.pull(0)) pull_resistor_2 (.node(not_1_out));
  Multiplexer #(.select(1), .width(32), .disabled("Z"), .enable("false")) multiplexer_18 (
    .in0(IR), .in1({32{1'b0}}), .out(multiplexer_18_out), .sel(\同步清零_高 ));
  Multiplexer #(.select(1), .width(32), .disabled("Z"), .enable("false")) multiplexer_19 (
    .in0(PC), .in1({32{1'b0}}), .out(multiplexer_19_out), .sel(\同步清零_高 ));
  Multiplexer #(.select(1), .width(32), .disabled("Z"), .enable("false")) multiplexer_20 (
    .in0(R1), .in1({32{1'b0}}), .out(multiplexer_20_out), .sel(\同步清零_高 ));
  Multiplexer #(.select(1), .width(32), .disabled("Z"), .enable("false")) multiplexer_21 (
    .in0(R2), .in1({32{1'b0}}), .out(multiplexer_21_out), .sel(\同步清零_高 ));
  Multiplexer #(.select(1), .width(26), .disabled("Z"), .enable("false")) multiplexer_22 (
    .in0(imm26), .in1({26{1'b0}}), .out(multiplexer_22_out), .sel(\同步清零_高 ));
  Multiplexer #(.select(1), .width(32), .disabled("Z"), .enable("false")) multiplexer_23 (
    .in0(PC_4), .in1({32{1'b0}}), .out(multiplexer_23_out), .sel(\同步清零_高 ));
  Multiplexer #(.select(1), .width(2), .disabled("Z"), .enable("false")) multiplexer_24 (
    .in0(IF_Rs_F), .in1(2'b00), .out(multiplexer_24_out), .sel(\同步清零_高 ));
  Multiplexer #(.select(1), .width(2), .disabled("Z"), .enable("false")) multiplexer_25 (
    .in0(IF_Rt_F), .in1(2'b00), .out(multiplexer_25_out), .sel(\同步清零_高 ));
  Register #(.width(32), .trigger("rising"), .Select("low")) register_18 (
    .D(multiplexer_18_out), .en(not_1_out), .Q(IR_2), .clk(CLK));  // open: clr
  Register #(.width(32), .trigger("rising"), .Select("low")) register_19 (
    .D(multiplexer_19_out), .en(not_1_out), .Q(PC_2), .clk(CLK));  // open: clr
  Register #(.width(32), .trigger("rising"), .Select("low")) register_20 (
    .D(multiplexer_20_out), .en(not_1_out), .Q(R1_2), .clk(CLK));  // open: clr
  Register #(.width(32), .trigger("rising"), .Select("low")) register_21 (
    .D(multiplexer_21_out), .en(not_1_out), .Q(R2_2), .clk(CLK));  // open: clr
  Register #(.width(26), .trigger("rising"), .Select("low")) register_22 (
    .D(multiplexer_22_out), .en(not_1_out), .Q(imm26_2), .clk(CLK));  // open: clr
  Register #(.width(32), .trigger("rising"), .Select("low")) register_23 (
    .D(multiplexer_23_out), .en(not_1_out), .Q(PC_4_2), .clk(CLK));  // open: clr
  Register #(.width(2), .trigger("rising"), .Select("low")) register_24 (
    .D(multiplexer_24_out), .en(not_1_out), .Q(EX_Rs_F), .clk(CLK));  // open: clr
  Register #(.width(2), .trigger("rising"), .Select("low")) register_25 (
    .D(multiplexer_25_out), .en(not_1_out), .Q(EX_Rt_F), .clk(CLK));  // open: clr
endmodule

module EX__MEM (
  input  CLK,
  input  \同步清零_高 ,
  input  \使能端_低 ,
  input  [31:0] IR,
  input  [31:0] PC,
  input  [31:0] ALUdata,
  input  memtoreg,
  input  [31:0] R1,
  input  memwrite,
  input  [31:0] R2,
  input  [31:0] PC_4,
  input  regwrite,
  input  lb,
  input  jal,
  input  regdst,
  input  sys,
  output [31:0] IR_2,
  output [31:0] PC_2,
  output [31:0] ALUdata_2,
  output memtoreg_2,
  output [31:0] R1_2,
  output memwrite_2,
  output [31:0] R2_2,
  output [31:0] PC_4_2,
  output regwrite_2,
  output lb_2,
  output jal_2,
  output regdst_2,
  output sys_2
);

  wire multiplexer_1_out, multiplexer_2_out, multiplexer_3_out, multiplexer_4_out, multiplexer_5_out,
       multiplexer_6_out, multiplexer_7_out, not_1_out;
  wire [31:0] multiplexer_8_out, multiplexer_9_out, multiplexer_10_out, multiplexer_11_out,
       multiplexer_12_out, multiplexer_13_out;

  not not_1 (not_1_out, \使能端_低 );
  Multiplexer #(.select(1), .width(1), .disabled("Z"), .enable("false")) multiplexer_1 (
    .in0(memtoreg), .in1(1'b0), .out(multiplexer_1_out), .sel(\同步清零_高 ));
  Multiplexer #(.select(1), .width(1), .disabled("Z"), .enable("false")) multiplexer_2 (
    .in0(memwrite), .in1(1'b0), .out(multiplexer_2_out), .sel(\同步清零_高 ));
  Multiplexer #(.select(1), .width(1), .disabled("Z"), .enable("false")) multiplexer_3 (
    .in0(regwrite), .in1(1'b0), .out(multiplexer_3_out), .sel(\同步清零_高 ));
  Multiplexer #(.select(1), .width(1), .disabled("Z"), .enable("false")) multiplexer_4 (
    .in0(lb), .in1(1'b0), .out(multiplexer_4_out), .sel(\同步清零_高 ));
  Multiplexer #(.select(1), .width(1), .disabled("Z"), .enable("false")) multiplexer_5 (
    .in0(jal), .in1(1'b0), .out(multiplexer_5_out), .sel(\同步清零_高 ));
  Multiplexer #(.select(1), .width(1), .disabled("Z"), .enable("false")) multiplexer_6 (
    .in0(regdst), .in1(1'b0), .out(multiplexer_6_out), .sel(\同步清零_高 ));
  Multiplexer #(.select(1), .width(1), .disabled("Z"), .enable("false")) multiplexer_7 (
    .in0(sys), .in1(1'b0), .out(multiplexer_7_out), .sel(\同步清零_高 ));
  Register #(.width(1), .trigger("rising"), .Select("low")) register_1 (
    .D(multiplexer_1_out), .en(not_1_out), .Q(memtoreg_2), .clk(CLK));  // open: clr
  Register #(.width(1), .trigger("rising"), .Select("low")) register_2 (
    .D(multiplexer_2_out), .en(not_1_out), .Q(memwrite_2), .clk(CLK));  // open: clr
  Register #(.width(1), .trigger("rising"), .Select("low")) register_3 (
    .D(multiplexer_3_out), .en(not_1_out), .Q(regwrite_2), .clk(CLK));  // open: clr
  Register #(.width(1), .trigger("rising"), .Select("low")) register_4 (
    .D(multiplexer_4_out), .en(not_1_out), .Q(lb_2), .clk(CLK));  // open: clr
  Register #(.width(1), .trigger("rising"), .Select("low")) register_5 (
    .D(multiplexer_5_out), .en(not_1_out), .Q(jal_2), .clk(CLK));  // open: clr
  Register #(.width(1), .trigger("rising"), .Select("low")) register_6 (
    .D(multiplexer_6_out), .en(not_1_out), .Q(regdst_2), .clk(CLK));  // open: clr
  Register #(.width(1), .trigger("rising"), .Select("low")) register_7 (
    .D(multiplexer_7_out), .en(not_1_out), .Q(sys_2), .clk(CLK));  // open: clr
  Pull_Resistor #(.pull(0)) pull_resistor_1 (.node(\同步清零_高 ));
  Pull_Resistor #(.pull(0)) pull_resistor_2 (.node(not_1_out));
  Multiplexer #(.select(1), .width(32), .disabled("Z"), .enable("false")) multiplexer_8 (
    .in0(IR), .in1({32{1'b0}}), .out(multiplexer_8_out), .sel(\同步清零_高 ));
  Multiplexer #(.select(1), .width(32), .disabled("Z"), .enable("false")) multiplexer_9 (
    .in0(PC), .in1({32{1'b0}}), .out(multiplexer_9_out), .sel(\同步清零_高 ));
  Multiplexer #(.select(1), .width(32), .disabled("Z"), .enable("false")) multiplexer_10 (
    .in0(ALUdata), .in1({32{1'b0}}), .out(multiplexer_10_out), .sel(\同步清零_高 ));
  Multiplexer #(.select(1), .width(32), .disabled("Z"), .enable("false")) multiplexer_11 (
    .in0(R1), .in1({32{1'b0}}), .out(multiplexer_11_out), .sel(\同步清零_高 ));
  Multiplexer #(.select(1), .width(32), .disabled("Z"), .enable("false")) multiplexer_12 (
    .in0(R2), .in1({32{1'b0}}), .out(multiplexer_12_out), .sel(\同步清零_高 ));
  Multiplexer #(.select(1), .width(32), .disabled("Z"), .enable("false")) multiplexer_13 (
    .in0(PC_4), .in1({32{1'b0}}), .out(multiplexer_13_out), .sel(\同步清零_高 ));
  Register #(.width(32), .trigger("rising"), .Select("low")) register_8 (
    .D(multiplexer_8_out), .en(not_1_out), .Q(IR_2), .clk(CLK));  // open: clr
  Register #(.width(32), .trigger("rising"), .Select("low")) register_9 (
    .D(multiplexer_9_out), .en(not_1_out), .Q(PC_2), .clk(CLK));  // open: clr
  Register #(.width(32), .trigger("rising"), .Select("low")) register_10 (
    .D(multiplexer_10_out), .en(not_1_out), .Q(ALUdata_2), .clk(CLK));  // open: clr
  Register #(.width(32), .trigger("rising"), .Select("low")) register_11 (
    .D(multiplexer_11_out), .en(not_1_out), .Q(R1_2), .clk(CLK));  // open: clr
  Register #(.width(32), .trigger("rising"), .Select("low")) register_12 (
    .D(multiplexer_12_out), .en(not_1_out), .Q(R2_2), .clk(CLK));  // open: clr
  Register #(.width(32), .trigger("rising"), .Select("low")) register_13 (
    .D(multiplexer_13_out), .en(not_1_out), .Q(PC_4_2), .clk(CLK));  // open: clr
endmodule

module MEM__WB (
  input  CLK,
  input  \同步清零_高 ,
  input  \使能端_低 ,
  input  [31:0] IR,
  input  [31:0] PC,
  input  memtoreg,
  input  [31:0] ALUdata,
  input  [31:0] memdata,
  input  [1:0] Addr10,
  input  [31:0] R1,
  input  regwrite,
  input  lb,
  input  [31:0] R2,
  input  jal,
  input  regdst,
  input  [31:0] PC_4,
  input  syscall,
  output [31:0] IR_2,
  output [31:0] PC_2,
  output memtoreg_2,
  output [31:0] ALUdata_2,
  output [31:0] memdata_2,
  output [1:0] Addr,
  output [31:0] R1_2,
  output regwrite_2,
  output lb_2,
  output [31:0] R2_2,
  output jal_2,
  output regdst_2,
  output [31:0] PC_4_2,
  output syscall_2
);

  wire multiplexer_1_out, multiplexer_2_out, multiplexer_3_out, multiplexer_4_out, multiplexer_5_out,
       multiplexer_6_out, not_1_out;
  wire [1:0] multiplexer_11_out;
  wire [31:0] multiplexer_7_out, multiplexer_8_out, multiplexer_9_out, multiplexer_10_out,
       multiplexer_12_out, multiplexer_13_out, multiplexer_14_out;

  not not_1 (not_1_out, \使能端_低 );
  Multiplexer #(.select(1), .width(1), .disabled("Z"), .enable("false")) multiplexer_1 (
    .in0(memtoreg), .in1(1'b0), .out(multiplexer_1_out), .sel(\同步清零_高 ));
  Multiplexer #(.select(1), .width(1), .disabled("Z"), .enable("false")) multiplexer_2 (
    .in0(regwrite), .in1(1'b0), .out(multiplexer_2_out), .sel(\同步清零_高 ));
  Multiplexer #(.select(1), .width(1), .disabled("Z"), .enable("false")) multiplexer_3 (
    .in0(lb), .in1(1'b0), .out(multiplexer_3_out), .sel(\同步清零_高 ));
  Multiplexer #(.select(1), .width(1), .disabled("Z"), .enable("false")) multiplexer_4 (
    .in0(jal), .in1(1'b0), .out(multiplexer_4_out), .sel(\同步清零_高 ));
  Multiplexer #(.select(1), .width(1), .disabled("Z"), .enable("false")) multiplexer_5 (
    .in0(regdst), .in1(1'b0), .out(multiplexer_5_out), .sel(\同步清零_高 ));
  Multiplexer #(.select(1), .width(1), .disabled("Z"), .enable("false")) multiplexer_6 (
    .in0(syscall), .in1(1'b0), .out(multiplexer_6_out), .sel(\同步清零_高 ));
  Register #(.width(1), .trigger("rising"), .Select("low")) register_1 (
    .D(multiplexer_1_out), .en(not_1_out), .Q(memtoreg_2), .clk(CLK));  // open: clr
  Register #(.width(1), .trigger("rising"), .Select("low")) register_2 (
    .D(multiplexer_2_out), .en(not_1_out), .Q(regwrite_2), .clk(CLK));  // open: clr
  Register #(.width(1), .trigger("rising"), .Select("low")) register_3 (
    .D(multiplexer_3_out), .en(not_1_out), .Q(lb_2), .clk(CLK));  // open: clr
  Register #(.width(1), .trigger("rising"), .Select("low")) register_4 (
    .D(multiplexer_4_out), .en(not_1_out), .Q(jal_2), .clk(CLK));  // open: clr
  Register #(.width(1), .trigger("rising"), .Select("low")) register_5 (
    .D(multiplexer_5_out), .en(not_1_out), .Q(regdst_2), .clk(CLK));  // open: clr
  Register #(.width(1), .trigger("rising"), .Select("low")) register_6 (
    .D(multiplexer_6_out), .en(not_1_out), .Q(syscall_2), .clk(CLK));  // open: clr
  Pull_Resistor #(.pull(0)) pull_resistor_1 (.node(\同步清零_高 ));
  Pull_Resistor #(.pull(0)) pull_resistor_2 (.node(not_1_out));
  Multiplexer #(.select(1), .width(32), .disabled("Z"), .enable("false")) multiplexer_7 (
    .in0(IR), .in1({32{1'b0}}), .out(multiplexer_7_out), .sel(\同步清零_高 ));
  Multiplexer #(.select(1), .width(32), .disabled("Z"), .enable("false")) multiplexer_8 (
    .in0(PC), .in1({32{1'b0}}), .out(multiplexer_8_out), .sel(\同步清零_高 ));
  Multiplexer #(.select(1), .width(32), .disabled("Z"), .enable("false")) multiplexer_9 (
    .in0(ALUdata), .in1({32{1'b0}}), .out(multiplexer_9_out), .sel(\同步清零_高 ));
  Multiplexer #(.select(1), .width(32), .disabled("Z"), .enable("false")) multiplexer_10 (
    .in0(memdata), .in1({32{1'b0}}), .out(multiplexer_10_out), .sel(\同步清零_高 ));
  Multiplexer #(.select(1), .width(2), .disabled("Z"), .enable("false")) multiplexer_11 (
    .in0(Addr10), .in1(2'b00), .out(multiplexer_11_out), .sel(\同步清零_高 ));
  Multiplexer #(.select(1), .width(32), .disabled("Z"), .enable("false")) multiplexer_12 (
    .in0(R1), .in1({32{1'b0}}), .out(multiplexer_12_out), .sel(\同步清零_高 ));
  Multiplexer #(.select(1), .width(32), .disabled("Z"), .enable("false")) multiplexer_13 (
    .in0(R2), .in1({32{1'b0}}), .out(multiplexer_13_out), .sel(\同步清零_高 ));
  Multiplexer #(.select(1), .width(32), .disabled("Z"), .enable("false")) multiplexer_14 (
    .in0(PC_4), .in1({32{1'b0}}), .out(multiplexer_14_out), .sel(\同步清零_高 ));
  Register #(.width(32), .trigger("rising"), .Select("low")) register_7 (
    .D(multiplexer_7_out), .en(not_1_out), .Q(IR_2), .clk(CLK));  // open: clr
  Register #(.width(32), .trigger("rising"), .Select("low")) register_8 (
    .D(multiplexer_8_out), .en(not_1_out), .Q(PC_2), .clk(CLK));  // open: clr
  Register #(.width(32), .trigger("rising"), .Select("low")) register_9 (
    .D(multiplexer_9_out), .en(not_1_out), .Q(ALUdata_2), .clk(CLK));  // open: clr
  Register #(.width(32), .trigger("rising"), .Select("low")) register_10 (
    .D(multiplexer_10_out), .en(not_1_out), .Q(memdata_2), .clk(CLK));  // open: clr
  Register #(.width(2), .trigger("rising"), .Select("low")) register_11 (
    .D(multiplexer_11_out), .en(not_1_out), .Q(Addr), .clk(CLK));  // open: clr
  Register #(.width(32), .trigger("rising"), .Select("low")) register_12 (
    .D(multiplexer_12_out), .en(not_1_out), .Q(R1_2), .clk(CLK));  // open: clr
  Register #(.width(32), .trigger("rising"), .Select("low")) register_13 (
    .D(multiplexer_13_out), .en(not_1_out), .Q(R2_2), .clk(CLK));  // open: clr
  Register #(.width(32), .trigger("rising"), .Select("low")) register_14 (
    .D(multiplexer_14_out), .en(not_1_out), .Q(PC_4_2), .clk(CLK));  // open: clr
endmodule
module \R1R2检测  (
  input  OP0,
  input  OP1,
  input  OP2,
  input  OP3,
  input  OP4,
  input  OP5,
  input  F0,
  input  F1,
  input  F2,
  input  F3,
  input  F4,
  input  F5,
  output R1_used,
  output R2_used
);

  wire and_1_out, and_2_out, and_3_out, and_4_out, and_5_out, and_6_out, and_7_out, and_8_out, and_9_out,
       and_10_out, and_11_out, and_12_out, and_13_out, and_14_out, and_15_out, and_16_out, and_17_out,
       and_18_out, and_19_out, and_20_out, and_21_out, and_22_out, and_23_out, and_24_out, and_25_out,
       and_26_out, and_27_out, and_28_out, and_29_out, and_30_out, and_31_out, and_32_out, and_33_out,
       and_34_out, and_35_out, and_36_out, and_37_out, and_38_out, and_39_out, and_40_out, and_41_out,
       and_42_out, not_1_out, not_2_out, not_3_out, not_4_out, not_5_out, not_6_out, not_7_out, not_8_out,
       not_9_out, not_10_out, not_11_out, not_12_out, not_13_out, not_14_out, not_15_out, not_16_out,
       not_17_out, not_18_out, not_19_out, not_20_out, not_21_out, not_22_out, not_23_out, not_24_out,
       not_25_out, not_26_out, not_27_out, not_28_out, not_29_out, not_30_out, not_31_out, not_32_out,
       not_33_out, not_34_out, not_35_out, not_36_out, not_37_out, not_38_out, not_39_out, not_40_out,
       not_41_out, not_42_out, not_43_out, not_44_out, not_45_out, not_46_out, not_47_out, not_48_out,
       not_49_out, not_50_out, not_51_out, not_52_out, not_53_out, not_54_out, not_55_out, not_56_out,
       not_57_out, not_58_out, not_59_out, not_60_out, not_61_out, not_62_out, not_63_out, not_64_out,
       not_65_out, not_66_out, not_67_out, not_68_out, not_69_out, not_70_out, not_71_out, not_72_out,
       not_73_out, not_74_out, not_75_out, not_76_out, not_77_out, not_78_out, not_79_out, not_80_out,
       not_81_out, not_82_out, not_83_out, not_84_out, not_85_out, not_86_out, not_87_out, not_88_out,
       not_89_out, not_90_out, not_91_out, not_92_out, not_93_out, not_94_out, not_95_out, not_96_out,
       not_97_out, not_98_out, not_99_out, not_100_out, not_101_out, not_102_out, not_103_out, not_104_out,
       not_105_out, not_106_out, not_107_out, not_108_out, not_109_out, not_110_out, not_111_out,
       not_112_out, not_113_out, not_114_out, not_115_out, not_116_out, not_117_out, not_118_out,
       not_119_out, not_120_out, not_121_out, not_122_out, not_123_out, not_124_out, not_125_out,
       not_126_out, not_127_out, not_128_out, not_129_out, not_130_out, not_131_out, not_132_out,
       not_133_out, not_134_out, not_135_out, not_136_out, not_137_out, not_138_out, not_139_out,
       not_140_out, not_141_out, not_142_out, not_143_out, not_144_out, not_145_out, not_146_out,
       not_147_out, not_148_out, not_149_out, not_150_out, not_151_out, not_152_out, not_153_out,
       not_154_out, not_155_out, not_156_out, not_157_out, not_158_out, not_159_out, not_160_out,
       not_161_out, not_162_out, not_163_out, not_164_out, not_165_out, not_166_out, not_167_out,
       not_168_out, not_169_out, not_170_out, not_171_out, not_172_out, not_173_out, not_174_out,
       not_175_out, not_176_out, not_177_out, not_178_out, not_179_out, not_180_out, not_181_out,
       not_182_out, not_183_out, not_184_out, not_185_out, not_186_out, not_187_out, not_188_out,
       not_189_out, not_190_out, not_191_out, not_192_out, not_193_out, not_194_out, not_195_out,
       not_196_out, not_197_out, not_198_out, not_199_out, not_200_out, not_201_out, not_202_out,
       not_203_out, not_204_out, not_205_out, not_206_out, not_207_out, not_208_out, not_209_out,
       not_210_out, not_211_out, not_212_out, not_213_out, not_214_out, not_215_out, not_216_out,
       not_217_out, not_218_out, not_219_out, not_220_out, not_221_out, not_222_out, not_223_out,
       not_224_out, not_225_out, not_226_out, not_227_out, not_228_out, not_229_out, not_230_out,
       not_231_out, not_232_out, not_233_out, not_234_out, not_235_out, not_236_out, not_237_out,
       not_238_out, not_239_out, not_240_out, not_241_out, not_242_out, not_243_out, not_244_out,
       not_245_out, not_246_out, not_247_out, not_248_out, not_249_out, not_250_out, not_251_out,
       not_252_out, not_253_out, not_254_out, not_255_out, not_256_out, not_257_out, not_258_out,
       not_259_out, not_260_out, not_261_out, not_262_out, not_263_out, not_264_out, not_265_out,
       not_266_out, not_267_out, not_268_out, not_269_out, not_270_out, not_271_out, not_272_out,
       not_273_out, not_274_out, not_275_out, not_276_out, not_277_out, not_278_out, not_279_out,
       not_280_out, not_281_out, not_282_out, not_283_out, not_284_out, not_285_out, not_286_out,
       not_287_out, not_288_out, not_289_out, not_290_out, not_291_out, not_292_out, not_293_out,
       not_294_out, not_295_out, not_296_out, not_297_out, not_298_out, not_299_out, not_300_out,
       not_301_out, not_302_out, not_303_out, not_304_out, not_305_out, not_306_out, not_307_out,
       not_308_out, not_309_out, not_310_out, not_311_out, not_312_out, not_313_out, not_314_out,
       not_315_out, not_316_out, not_317_out, not_318_out, not_319_out, not_320_out, not_321_out,
       not_322_out, not_323_out, not_324_out, not_325_out;

  not not_1 (not_1_out, OP5);
  not not_2 (not_2_out, OP4);
  not not_3 (not_3_out, OP3);
  not not_4 (not_4_out, OP2);
  not not_5 (not_5_out, OP1);
  not not_6 (not_6_out, OP0);
  not not_7 (not_7_out, F5);
  not not_8 (not_8_out, F4);
  not not_9 (not_9_out, F3);
  not not_10 (not_10_out, F2);
  not not_11 (not_11_out, F1);
  not not_12 (not_12_out, F0);
  not not_13 (not_13_out, OP5);
  not not_14 (not_14_out, OP4);
  not not_15 (not_15_out, OP3);
  not not_16 (not_16_out, OP2);
  not not_17 (not_17_out, OP1);
  not not_18 (not_18_out, OP0);
  not not_19 (not_19_out, F5);
  not not_20 (not_20_out, F4);
  not not_21 (not_21_out, F3);
  not not_22 (not_22_out, F2);
  not not_23 (not_23_out, OP5);
  not not_24 (not_24_out, OP4);
  not not_25 (not_25_out, OP3);
  not not_26 (not_26_out, OP2);
  not not_27 (not_27_out, OP1);
  not not_28 (not_28_out, OP0);
  not not_29 (not_29_out, F5);
  not not_30 (not_30_out, F4);
  not not_31 (not_31_out, F3);
  not not_32 (not_32_out, F2);
  not not_33 (not_33_out, F0);
  not not_34 (not_34_out, OP5);
  not not_35 (not_35_out, OP4);
  not not_36 (not_36_out, OP3);
  not not_37 (not_37_out, OP2);
  not not_38 (not_38_out, OP1);
  not not_39 (not_39_out, OP0);
  not not_40 (not_40_out, F4);
  not not_41 (not_41_out, F3);
  not not_42 (not_42_out, F2);
  not not_43 (not_43_out, F1);
  not not_44 (not_44_out, F0);
  not not_45 (not_45_out, OP5);
  not not_46 (not_46_out, OP4);
  not not_47 (not_47_out, OP3);
  not not_48 (not_48_out, OP2);
  not not_49 (not_49_out, OP1);
  not not_50 (not_50_out, OP0);
  not not_51 (not_51_out, F4);
  not not_52 (not_52_out, F3);
  not not_53 (not_53_out, F2);
  not not_54 (not_54_out, F1);
  not not_55 (not_55_out, OP5);
  not not_56 (not_56_out, OP4);
  not not_57 (not_57_out, OP3);
  not not_58 (not_58_out, OP2);
  not not_59 (not_59_out, OP1);
  not not_60 (not_60_out, OP0);
  not not_61 (not_61_out, F4);
  not not_62 (not_62_out, F3);
  not not_63 (not_63_out, F2);
  not not_64 (not_64_out, F0);
  not not_65 (not_65_out, OP5);
  not not_66 (not_66_out, OP4);
  not not_67 (not_67_out, OP3);
  not not_68 (not_68_out, OP2);
  not not_69 (not_69_out, OP1);
  not not_70 (not_70_out, OP0);
  not not_71 (not_71_out, F4);
  not not_72 (not_72_out, F3);
  not not_73 (not_73_out, F1);
  not not_74 (not_74_out, F0);
  not not_75 (not_75_out, OP5);
  not not_76 (not_76_out, OP4);
  not not_77 (not_77_out, OP3);
  not not_78 (not_78_out, OP2);
  not not_79 (not_79_out, OP1);
  not not_80 (not_80_out, OP0);
  not not_81 (not_81_out, F4);
  not not_82 (not_82_out, F3);
  not not_83 (not_83_out, F1);
  not not_84 (not_84_out, OP5);
  not not_85 (not_85_out, OP4);
  not not_86 (not_86_out, OP3);
  not not_87 (not_87_out, OP2);
  not not_88 (not_88_out, OP1);
  not not_89 (not_89_out, OP0);
  not not_90 (not_90_out, F4);
  not not_91 (not_91_out, F3);
  not not_92 (not_92_out, OP5);
  not not_93 (not_93_out, OP4);
  not not_94 (not_94_out, OP3);
  not not_95 (not_95_out, OP2);
  not not_96 (not_96_out, OP1);
  not not_97 (not_97_out, OP0);
  not not_98 (not_98_out, F4);
  not not_99 (not_99_out, F2);
  not not_100 (not_100_out, F0);
  not not_101 (not_101_out, OP5);
  not not_102 (not_102_out, OP4);
  not not_103 (not_103_out, OP3);
  not not_104 (not_104_out, OP2);
  not not_105 (not_105_out, OP1);
  not not_106 (not_106_out, OP0);
  not not_107 (not_107_out, F4);
  not not_108 (not_108_out, F2);
  not not_109 (not_109_out, OP5);
  not not_110 (not_110_out, OP4);
  not not_111 (not_111_out, OP3);
  not not_112 (not_112_out, OP2);
  not not_113 (not_113_out, OP1);
  not not_114 (not_114_out, OP0);
  not not_115 (not_115_out, F5);
  not not_116 (not_116_out, F4);
  not not_117 (not_117_out, F2);
  not not_118 (not_118_out, F1);
  not not_119 (not_119_out, F0);
  not not_120 (not_120_out, OP5);
  not not_121 (not_121_out, OP4);
  not not_122 (not_122_out, OP3);
  not not_123 (not_123_out, OP2);
  not not_124 (not_124_out, OP1);
  not not_125 (not_125_out, OP0);
  not not_126 (not_126_out, F5);
  not not_127 (not_127_out, F4);
  not not_128 (not_128_out, F1);
  not not_129 (not_129_out, F0);
  not not_130 (not_130_out, OP5);
  not not_131 (not_131_out, OP4);
  not not_132 (not_132_out, OP3);
  not not_133 (not_133_out, OP1);
  not not_134 (not_134_out, OP0);
  not not_135 (not_135_out, OP5);
  not not_136 (not_136_out, OP4);
  not not_137 (not_137_out, OP3);
  not not_138 (not_138_out, OP1);
  not not_139 (not_139_out, OP5);
  not not_140 (not_140_out, OP4);
  not not_141 (not_141_out, OP2);
  not not_142 (not_142_out, OP1);
  not not_143 (not_143_out, OP0);
  not not_144 (not_144_out, OP5);
  not not_145 (not_145_out, OP4);
  not not_146 (not_146_out, OP1);
  not not_147 (not_147_out, OP0);
  not not_148 (not_148_out, OP5);
  not not_149 (not_149_out, OP4);
  not not_150 (not_150_out, OP2);
  not not_151 (not_151_out, OP1);
  not not_152 (not_152_out, OP5);
  not not_153 (not_153_out, OP4);
  not not_154 (not_154_out, OP2);
  not not_155 (not_155_out, OP0);
  not not_156 (not_156_out, OP5);
  not not_157 (not_157_out, OP4);
  not not_158 (not_158_out, OP1);
  not not_159 (not_159_out, OP4);
  not not_160 (not_160_out, OP3);
  not not_161 (not_161_out, OP2);
  not not_162 (not_162_out, OP4);
  not not_163 (not_163_out, OP2);
  not not_164 (not_164_out, OP5);
  not not_165 (not_165_out, OP4);
  not not_166 (not_166_out, OP3);
  not not_167 (not_167_out, OP2);
  not not_168 (not_168_out, OP1);
  not not_169 (not_169_out, OP0);
  not not_170 (not_170_out, F5);
  not not_171 (not_171_out, F4);
  not not_172 (not_172_out, F3);
  not not_173 (not_173_out, F1);
  not not_174 (not_174_out, F0);
  not not_175 (not_175_out, OP5);
  not not_176 (not_176_out, OP4);
  not not_177 (not_177_out, OP0);
  not not_178 (not_178_out, OP4);
  not not_179 (not_179_out, OP3);
  not not_180 (not_180_out, OP2);
  not not_181 (not_181_out, OP1);
  not not_182 (not_182_out, OP0);
  not not_183 (not_183_out, OP5);
  not not_184 (not_184_out, OP4);
  not not_185 (not_185_out, OP3);
  not not_186 (not_186_out, OP5);
  not not_187 (not_187_out, OP4);
  not not_188 (not_188_out, OP3);
  not not_189 (not_189_out, OP2);
  not not_190 (not_190_out, OP1);
  not not_191 (not_191_out, OP0);
  not not_192 (not_192_out, F5);
  not not_193 (not_193_out, F4);
  not not_194 (not_194_out, F3);
  not not_195 (not_195_out, F2);
  not not_196 (not_196_out, F1);
  not not_197 (not_197_out, F0);
  not not_198 (not_198_out, OP5);
  not not_199 (not_199_out, OP4);
  not not_200 (not_200_out, OP3);
  not not_201 (not_201_out, OP2);
  not not_202 (not_202_out, OP1);
  not not_203 (not_203_out, OP0);
  not not_204 (not_204_out, F5);
  not not_205 (not_205_out, F4);
  not not_206 (not_206_out, F3);
  not not_207 (not_207_out, F2);
  not not_208 (not_208_out, OP5);
  not not_209 (not_209_out, OP4);
  not not_210 (not_210_out, OP3);
  not not_211 (not_211_out, OP2);
  not not_212 (not_212_out, OP1);
  not not_213 (not_213_out, OP0);
  not not_214 (not_214_out, F5);
  not not_215 (not_215_out, F4);
  not not_216 (not_216_out, F3);
  not not_217 (not_217_out, F2);
  not not_218 (not_218_out, F0);
  not not_219 (not_219_out, OP5);
  not not_220 (not_220_out, OP4);
  not not_221 (not_221_out, OP3);
  not not_222 (not_222_out, OP2);
  not not_223 (not_223_out, OP1);
  not not_224 (not_224_out, OP0);
  not not_225 (not_225_out, F4);
  not not_226 (not_226_out, F3);
  not not_227 (not_227_out, F2);
  not not_228 (not_228_out, F1);
  not not_229 (not_229_out, F0);
  not not_230 (not_230_out, OP5);
  not not_231 (not_231_out, OP4);
  not not_232 (not_232_out, OP3);
  not not_233 (not_233_out, OP2);
  not not_234 (not_234_out, OP1);
  not not_235 (not_235_out, OP0);
  not not_236 (not_236_out, F4);
  not not_237 (not_237_out, F3);
  not not_238 (not_238_out, F2);
  not not_239 (not_239_out, F1);
  not not_240 (not_240_out, OP5);
  not not_241 (not_241_out, OP4);
  not not_242 (not_242_out, OP3);
  not not_243 (not_243_out, OP2);
  not not_244 (not_244_out, OP1);
  not not_245 (not_245_out, OP0);
  not not_246 (not_246_out, F4);
  not not_247 (not_247_out, F3);
  not not_248 (not_248_out, F2);
  not not_249 (not_249_out, F0);
  not not_250 (not_250_out, OP5);
  not not_251 (not_251_out, OP4);
  not not_252 (not_252_out, OP3);
  not not_253 (not_253_out, OP2);
  not not_254 (not_254_out, OP1);
  not not_255 (not_255_out, OP0);
  not not_256 (not_256_out, F4);
  not not_257 (not_257_out, F3);
  not not_258 (not_258_out, F1);
  not not_259 (not_259_out, F0);
  not not_260 (not_260_out, OP5);
  not not_261 (not_261_out, OP4);
  not not_262 (not_262_out, OP3);
  not not_263 (not_263_out, OP2);
  not not_264 (not_264_out, OP1);
  not not_265 (not_265_out, OP0);
  not not_266 (not_266_out, F4);
  not not_267 (not_267_out, F3);
  not not_268 (not_268_out, F1);
  not not_269 (not_269_out, OP5);
  not not_270 (not_270_out, OP4);
  not not_271 (not_271_out, OP3);
  not not_272 (not_272_out, OP2);
  not not_273 (not_273_out, OP1);
  not not_274 (not_274_out, OP0);
  not not_275 (not_275_out, F4);
  not not_276 (not_276_out, F3);
  not not_277 (not_277_out, OP5);
  not not_278 (not_278_out, OP4);
  not not_279 (not_279_out, OP3);
  not not_280 (not_280_out, OP2);
  not not_281 (not_281_out, OP1);
  not not_282 (not_282_out, OP0);
  not not_283 (not_283_out, F4);
  not not_284 (not_284_out, F2);
  not not_285 (not_285_out, F0);
  not not_286 (not_286_out, OP5);
  not not_287 (not_287_out, OP4);
  not not_288 (not_288_out, OP3);
  not not_289 (not_289_out, OP2);
  not not_290 (not_290_out, OP1);
  not not_291 (not_291_out, OP0);
  not not_292 (not_292_out, F4);
  not not_293 (not_293_out, F2);
  not not_294 (not_294_out, OP5);
  not not_295 (not_295_out, OP4);
  not not_296 (not_296_out, OP3);
  not not_297 (not_297_out, OP2);
  not not_298 (not_298_out, OP1);
  not not_299 (not_299_out, OP0);
  not not_300 (not_300_out, F5);
  not not_301 (not_301_out, F4);
  not not_302 (not_302_out, F1);
  not not_303 (not_303_out, F0);
  not not_304 (not_304_out, OP5);
  not not_305 (not_305_out, OP4);
  not not_306 (not_306_out, OP3);
  not not_307 (not_307_out, OP1);
  not not_308 (not_308_out, OP0);
  not not_309 (not_309_out, OP5);
  not not_310 (not_310_out, OP4);
  not not_311 (not_311_out, OP3);
  not not_312 (not_312_out, OP1);
  not not_313 (not_313_out, OP4);
  not not_314 (not_314_out, OP2);
  not not_315 (not_315_out, OP5);
  not not_316 (not_316_out, OP4);
  not not_317 (not_317_out, OP3);
  not not_318 (not_318_out, OP2);
  not not_319 (not_319_out, OP1);
  not not_320 (not_320_out, OP0);
  not not_321 (not_321_out, F5);
  not not_322 (not_322_out, F4);
  not not_323 (not_323_out, F3);
  not not_324 (not_324_out, F1);
  not not_325 (not_325_out, F0);
  and and_1 (and_1_out, not_1_out, not_2_out, not_3_out, not_4_out, not_5_out, not_6_out, not_7_out, not_8_out, not_9_out, not_10_out, not_11_out, not_12_out);
  and and_2 (and_2_out, not_13_out, not_14_out, not_15_out, not_16_out, not_17_out, not_18_out, not_19_out, not_20_out, not_21_out, not_22_out, F1, F0);
  and and_3 (and_3_out, not_23_out, not_24_out, not_25_out, not_26_out, not_27_out, not_28_out, not_29_out, not_30_out, not_31_out, not_32_out, F1, not_33_out);
  and and_4 (and_4_out, not_34_out, not_35_out, not_36_out, not_37_out, not_38_out, not_39_out, F5, not_40_out, not_41_out, not_42_out, not_43_out, not_44_out);
  and and_5 (and_5_out, not_45_out, not_46_out, not_47_out, not_48_out, not_49_out, not_50_out, F5, not_51_out, not_52_out, not_53_out, not_54_out, F0);
  and and_6 (and_6_out, not_55_out, not_56_out, not_57_out, not_58_out, not_59_out, not_60_out, F5, not_61_out, not_62_out, not_63_out, F1, not_64_out);
  and and_7 (and_7_out, not_65_out, not_66_out, not_67_out, not_68_out, not_69_out, not_70_out, F5, not_71_out, not_72_out, F2, not_73_out, not_74_out);
  and and_8 (and_8_out, not_75_out, not_76_out, not_77_out, not_78_out, not_79_out, not_80_out, F5, not_81_out, not_82_out, F2, not_83_out, F0);
  and and_9 (and_9_out, not_84_out, not_85_out, not_86_out, not_87_out, not_88_out, not_89_out, F5, not_90_out, not_91_out, F2, F1, F0);
  and and_10 (and_10_out, not_92_out, not_93_out, not_94_out, not_95_out, not_96_out, not_97_out, F5, not_98_out, F3, not_99_out, F1, not_100_out);
  and and_11 (and_11_out, not_101_out, not_102_out, not_103_out, not_104_out, not_105_out, not_106_out, F5, not_107_out, F3, not_108_out, F1, F0);
  and and_12 (and_12_out, not_109_out, not_110_out, not_111_out, not_112_out, not_113_out, not_114_out, not_115_out, not_116_out, F3, not_117_out, not_118_out, not_119_out);
  and and_13 (and_13_out, not_120_out, not_121_out, not_122_out, not_123_out, not_124_out, not_125_out, not_126_out, not_127_out, F3, F2, not_128_out, not_129_out);
  and and_14 (and_14_out, not_130_out, not_131_out, not_132_out, OP2, not_133_out, not_134_out);
  and and_15 (and_15_out, not_135_out, not_136_out, not_137_out, OP2, not_138_out, OP0);
  and and_16 (and_16_out, not_139_out, not_140_out, OP3, not_141_out, not_142_out, not_143_out);
  and and_17 (and_17_out, not_144_out, not_145_out, OP3, OP2, not_146_out, not_147_out);
  and and_18 (and_18_out, not_148_out, not_149_out, OP3, not_150_out, not_151_out, OP0);
  and and_19 (and_19_out, not_152_out, not_153_out, OP3, not_154_out, OP1, not_155_out);
  and and_20 (and_20_out, not_156_out, not_157_out, OP3, OP2, not_158_out, OP0);
  and and_21 (and_21_out, OP5, not_159_out, not_160_out, not_161_out, OP1, OP0);
  and and_22 (and_22_out, OP5, not_162_out, OP3, not_163_out, OP1, OP0);
  and and_23 (and_23_out, not_164_out, not_165_out, not_166_out, not_167_out, not_168_out, not_169_out, not_170_out, not_171_out, not_172_out, F2, not_173_out, not_174_out);
  and and_24 (and_24_out, not_175_out, not_176_out, OP3, OP2, OP1, not_177_out);
  and and_25 (and_25_out, OP5, not_178_out, not_179_out, not_180_out, not_181_out, not_182_out);
  and and_26 (and_26_out, not_183_out, not_184_out, not_185_out, OP2, OP1, OP0);
  and and_27 (and_27_out, not_186_out, not_187_out, not_188_out, not_189_out, not_190_out, not_191_out, not_192_out, not_193_out, not_194_out, not_195_out, not_196_out, not_197_out);
  and and_28 (and_28_out, not_198_out, not_199_out, not_200_out, not_201_out, not_202_out, not_203_out, not_204_out, not_205_out, not_206_out, not_207_out, F1, F0);
  and and_29 (and_29_out, not_208_out, not_209_out, not_210_out, not_211_out, not_212_out, not_213_out, not_214_out, not_215_out, not_216_out, not_217_out, F1, not_218_out);
  and and_30 (and_30_out, not_219_out, not_220_out, not_221_out, not_222_out, not_223_out, not_224_out, F5, not_225_out, not_226_out, not_227_out, not_228_out, not_229_out);
  and and_31 (and_31_out, not_230_out, not_231_out, not_232_out, not_233_out, not_234_out, not_235_out, F5, not_236_out, not_237_out, not_238_out, not_239_out, F0);
  and and_32 (and_32_out, not_240_out, not_241_out, not_242_out, not_243_out, not_244_out, not_245_out, F5, not_246_out, not_247_out, not_248_out, F1, not_249_out);
  and and_33 (and_33_out, not_250_out, not_251_out, not_252_out, not_253_out, not_254_out, not_255_out, F5, not_256_out, not_257_out, F2, not_258_out, not_259_out);
  and and_34 (and_34_out, not_260_out, not_261_out, not_262_out, not_263_out, not_264_out, not_265_out, F5, not_266_out, not_267_out, F2, not_268_out, F0);
  and and_35 (and_35_out, not_269_out, not_270_out, not_271_out, not_272_out, not_273_out, not_274_out, F5, not_275_out, not_276_out, F2, F1, F0);
  and and_36 (and_36_out, not_277_out, not_278_out, not_279_out, not_280_out, not_281_out, not_282_out, F5, not_283_out, F3, not_284_out, F1, not_285_out);
  and and_37 (and_37_out, not_286_out, not_287_out, not_288_out, not_289_out, not_290_out, not_291_out, F5, not_292_out, F3, not_293_out, F1, F0);
  and and_38 (and_38_out, not_294_out, not_295_out, not_296_out, not_297_out, not_298_out, not_299_out, not_300_out, not_301_out, F3, F2, not_302_out, not_303_out);
  and and_39 (and_39_out, not_304_out, not_305_out, not_306_out, OP2, not_307_out, not_308_out);
  and and_40 (and_40_out, not_309_out, not_310_out, not_311_out, OP2, not_312_out, OP0);
  and and_41 (and_41_out, OP5, not_313_out, OP3, not_314_out, OP1, OP0);
  and and_42 (and_42_out, not_315_out, not_316_out, not_317_out, not_318_out, not_319_out, not_320_out, not_321_out, not_322_out, not_323_out, F2, not_324_out, not_325_out);
  or or_1 (R1_used, and_1_out, and_2_out, and_3_out, and_4_out, and_5_out, and_6_out, and_7_out, and_8_out, and_9_out, and_10_out, and_11_out, and_12_out, and_13_out, and_14_out, and_15_out, and_16_out, and_17_out, and_18_out, and_19_out, and_20_out, and_21_out, and_22_out, and_23_out, and_24_out, and_25_out, and_26_out);
  or or_2 (R2_used, and_27_out, and_28_out, and_29_out, and_30_out, and_31_out, and_32_out, and_33_out, and_34_out, and_35_out, and_36_out, and_37_out, and_38_out, and_39_out, and_40_out, and_41_out, and_42_out);
endmodule

module \DataHazarrd检测  (
  input  Rs_used,
  input  Rt_used,
  input  [4:0] Rs_num,
  input  [4:0] Rt_num,
  input  [4:0] EX_WriteReg,
  input  EX_RegWrite,
  input  [4:0] MEM_WriteReg,
  input  MEM_RegWrite,
  output DataHazzard
);

  wire and_1_out, and_2_out, and_3_out, and_4_out, comparator_1_eq, comparator_2_eq, comparator_3_eq,
       comparator_4_eq, comparator_5_eq, comparator_6_eq, not_1_out, not_2_out, or_1_out, or_2_out, or_3_out;

  not not_1 (not_1_out, comparator_1_eq);
  Comparator #(.width(5), .mode("twosComplement")) comparator_1 (
    .a(Rs_num), .b({5{1'b0}}), .eq(comparator_1_eq));  // open: gt, lt
  Comparator #(.width(5), .mode("twosComplement")) comparator_2 (
    .a(Rt_num), .b({5{1'b0}}), .eq(comparator_2_eq));  // open: gt, lt
  not not_2 (not_2_out, comparator_2_eq);
  Comparator #(.width(5), .mode("twosComplement")) comparator_3 (
    .a(Rs_num), .b(EX_WriteReg), .eq(comparator_3_eq));  // open: gt, lt
  Comparator #(.width(5), .mode("twosComplement")) comparator_4 (
    .a(EX_WriteReg), .b(Rt_num), .eq(comparator_4_eq));  // open: gt, lt
  Comparator #(.width(5), .mode("twosComplement")) comparator_5 (
    .a(Rs_num), .b(MEM_WriteReg), .eq(comparator_5_eq));  // open: gt, lt
  Comparator #(.width(5), .mode("twosComplement")) comparator_6 (
    .a(MEM_WriteReg), .b(Rt_num), .eq(comparator_6_eq));  // open: gt, lt
  and and_1 (and_1_out, not_1_out, comparator_3_eq, EX_RegWrite);
  and and_2 (and_2_out, EX_RegWrite, not_2_out, comparator_4_eq);
  and and_3 (and_3_out, not_1_out, comparator_5_eq, MEM_RegWrite);
  and and_4 (and_4_out, MEM_RegWrite, not_2_out, comparator_6_eq);
  or or_1 (or_1_out, and_1_out, and_3_out);
  or or_2 (or_2_out, and_2_out, and_4_out);
  or or_3 (or_3_out, or_2_out, or_1_out);
  Multiplexer #(.select(2), .width(1), .disabled("Z"), .enable("false")) multiplexer_1 (
    .in0(1'b0), .in1(or_1_out), .in2(or_2_out), .in3(or_3_out), .out(DataHazzard), .sel({Rt_used, Rs_used}));
endmodule

// LoadUse检测
module \load_used检测  (
  input  Rs_used,
  input  Rt_used,
  input  [4:0] Rs_num,
  input  [4:0] Rt_num,
  input  [4:0] EX_WriteReg_num,
  input  EX_memtoreg,
  output load_used
);

  wire and_1_out, and_2_out, comparator_1_eq, comparator_2_eq, comparator_3_eq, comparator_4_eq, not_1_out,
       not_2_out;

  Comparator #(.width(5), .mode("twosComplement")) comparator_1 (
    .a(Rs_num), .b({5{1'b0}}), .eq(comparator_1_eq));  // open: gt, lt
  not not_1 (not_1_out, comparator_1_eq);
  not not_2 (not_2_out, comparator_2_eq);
  Comparator #(.width(5), .mode("twosComplement")) comparator_2 (
    .a(Rt_num), .b({5{1'b0}}), .eq(comparator_2_eq));  // open: gt, lt
  Comparator #(.width(5), .mode("twosComplement")) comparator_3 (
    .a(Rs_num), .b(EX_WriteReg_num), .eq(comparator_3_eq));  // open: gt, lt
  Comparator #(.width(5), .mode("twosComplement")) comparator_4 (
    .a(Rt_num), .b(EX_WriteReg_num), .eq(comparator_4_eq));  // open: gt, lt
  and and_1 (and_1_out, Rs_used, not_1_out, comparator_3_eq, EX_memtoreg);
  and and_2 (and_2_out, Rt_used, not_2_out, EX_memtoreg, comparator_4_eq);
  or or_1 (load_used, and_1_out, and_2_out);
endmodule

// RsRt控制端
module \RSRT控制端  (
  input  Rs_used,
  input  [4:0] Rs_num,
  input  EX_RegWrite,
  input  [4:0] EX_WriteReg_num,
  input  MEM_RegWrite,
  input  [4:0] MEM_WriteReg,
  input  Rt_used,
  input  [4:0] Rt_num,
  output [1:0] RsUsed,
  output [1:0] RtUsed
);

  wire comparator_1_eq, comparator_2_eq, comparator_3_eq, comparator_4_eq, comparator_5_eq, comparator_6_eq,
       not_1_out, not_2_out;
  wire [1:0] and_1_out, and_3_out;

  Comparator #(.width(5), .mode("twosComplement")) comparator_1 (
    .a(Rs_num), .b({5{1'b0}}), .eq(comparator_1_eq));  // open: gt, lt
  Comparator #(.width(5), .mode("twosComplement")) comparator_2 (
    .a(Rs_num), .b(EX_WriteReg_num), .eq(comparator_2_eq));  // open: gt, lt
  Comparator #(.width(5), .mode("twosComplement")) comparator_3 (
    .a(Rs_num), .b(MEM_WriteReg), .eq(comparator_3_eq));  // open: gt, lt
  Comparator #(.width(5), .mode("twosComplement")) comparator_4 (
    .a(Rt_num), .b({5{1'b0}}), .eq(comparator_4_eq));  // open: gt, lt
  Comparator #(.width(5), .mode("twosComplement")) comparator_5 (
    .a(Rt_num), .b(EX_WriteReg_num), .eq(comparator_5_eq));  // open: gt, lt
  not not_1 (not_1_out, comparator_1_eq);
  not not_2 (not_2_out, comparator_4_eq);
  Comparator #(.width(5), .mode("twosComplement")) comparator_6 (
    .a(Rt_num), .b(MEM_WriteReg), .eq(comparator_6_eq));  // open: gt, lt
  and and_1 (and_1_out[0], Rs_used, not_1_out, EX_RegWrite, comparator_2_eq);
  and and_2 (and_1_out[1], not_1_out, Rs_used, MEM_RegWrite, comparator_3_eq);
  and and_3 (and_3_out[0], Rt_used, not_2_out, EX_RegWrite, comparator_5_eq);
  and and_4 (and_3_out[1], not_2_out, Rt_used, MEM_RegWrite, comparator_6_eq);
  Multiplexer #(.select(2), .width(2), .disabled("Z"), .enable("false")) multiplexer_1 (
    .in0(2'b00), .in1(2'b10), .in2(2'b01), .in3(2'b10), .out(RsUsed), .sel(and_1_out));
  Multiplexer #(.select(2), .width(2), .disabled("Z"), .enable("false")) multiplexer_2 (
    .in0(2'b00), .in1(2'b10), .in2(2'b01), .in3(2'b10), .out(RtUsed), .sel(and_3_out));
endmodule

module MAX (
  input  [15:0] Y,
  input  [15:0] X,
  input  [2:0] Y_num,
  input  [2:0] X_num,
  output [15:0] MAX,
  output [2:0] Max_num
);

  wire comparator_1_eq, comparator_1_gt, or_1_out;

  Comparator #(.width(16), .mode("unsigned")) comparator_1 (
    .a(X), .b(Y), .gt(comparator_1_gt), .eq(comparator_1_eq));  // open: lt
  Multiplexer #(.select(1), .width(16), .disabled("Z"), .enable("false")) multiplexer_1 (
    .in0(Y), .in1(X), .out(MAX), .sel(or_1_out));
  or or_1 (or_1_out, comparator_1_gt, comparator_1_eq);
  Multiplexer #(.select(1), .width(3), .disabled("Z"), .enable("false")) multiplexer_2 (
    .in0(Y_num), .in1(X_num), .out(Max_num), .sel(or_1_out));

  // Notes on the sheet:
  //   输出两个输入中的较大值，并输出较大值的3位编号
endmodule

module BTB (
  input  [31:0] PC,
  input  [31:0] EX_PC,
  input  [31:0] EX_BranchAddr,
  input  EX_Branch,
  input  EX_Branched,
  input  in_6,
  output ID_PredictJump,
  output [31:0] BTB_JumpAddr
);

  wire and_17_out, and_26_out, and_27_out, and_28_out, and_29_out, and_30_out, and_31_out, and_32_out,
       and_33_out, comparator_1_eq, comparator_2_eq, comparator_3_eq, comparator_4_eq, comparator_5_eq,
       comparator_6_eq, comparator_7_eq, comparator_8_eq, comparator_9_eq, comparator_10_eq,
       comparator_11_eq, comparator_12_eq, comparator_13_eq, comparator_14_eq, comparator_15_eq,
       comparator_16_eq, d_ff_1_q, d_ff_2_q, d_ff_3_q, d_ff_4_q, d_ff_5_q, d_ff_6_q, d_ff_7_q, d_ff_8_q,
       decoder_1_out0, decoder_1_out1, decoder_1_out2, decoder_1_out3, decoder_1_out4, decoder_1_out5,
       decoder_1_out6, decoder_1_out7, decoder_2_out0, decoder_2_out1, decoder_2_out2, decoder_2_out3,
       decoder_2_out4, decoder_2_out5, decoder_2_out6, decoder_2_out7, EX_Hit, EX_Miss, L0, L1, L2, L3, L4,
       L5, L6, L7, M0, M1, M2, M3, M4, M5, M6, M7, not_1_out, not_2_out, not_3_out, not_4_out, not_5_out,
       not_6_out, not_7_out, not_8_out, or_1_out, or_2_out, or_3_out, or_4_out, or_5_out, or_6_out, or_7_out,
       or_8_out, or_10_out, or_11_out, or_12_out, or_13_out, or_14_out, or_15_out, or_16_out, or_17_out,
       priority_encoder_1_gs, v0, v1, v2, v3, v4, v5, v6, v7, write0, write1, write2, write3, write4, write5,
       write6, write7;
  wire [0:0] controlled_buffer_9_out, controlled_buffer_10_out, controlled_buffer_11_out,
       controlled_buffer_12_out, controlled_buffer_13_out, controlled_buffer_14_out,
       controlled_buffer_15_out, controlled_buffer_16_out;
  wire [1:0] fsm_1_nextlow, fsm_2_nextlow, fsm_3_nextlow, fsm_4_nextlow, fsm_5_nextlow, fsm_6_nextlow,
       fsm_7_nextlow, fsm_8_nextlow, predict0, predict1, predict2, predict3, predict4, predict5, predict6,
       predict7;
  wire [2:0] max_1_max_num, max_2_max_num, max_3_max_num, max_4_max_num, max_5_max_num, max_6_max_num,
       max_7_max_num, priority_encoder_1_out;
  wire [15:0] c0, c1, c2, c3, c4, c5, c6, c7, max_1_max, max_2_max, max_3_max, max_4_max, max_5_max,
       max_6_max;
  wire [31:0] register_17_q, register_18_q, register_19_q, register_20_q, register_21_q, register_22_q,
       register_23_q, register_24_q, tag0, tag1, tag2, tag3, tag4, tag5, tag6, tag7;

  LED #(.active("true")) led_1 (.in(v0));
  Register #(.width(1), .trigger("rising"), .Select("low")) register_1 (
    .D(1'b1), .en(write0), .Q(v0), .clk(in_6));  // open: clr
  LED #(.active("true")) led_2 (.in(v1));
  Register #(.width(1), .trigger("rising"), .Select("low")) register_2 (
    .D(1'b1), .en(write1), .Q(v1), .clk(in_6));  // open: clr
  LED #(.active("true")) led_3 (.in(v2));
  Register #(.width(1), .trigger("rising"), .Select("low")) register_3 (
    .D(1'b1), .en(write2), .Q(v2), .clk(in_6));  // open: clr
  LED #(.active("true")) led_4 (.in(v3));
  Register #(.width(1), .trigger("rising"), .Select("low")) register_4 (
    .D(1'b1), .en(write3), .Q(v3), .clk(in_6));  // open: clr
  LED #(.active("true")) led_5 (.in(v4));
  Register #(.width(1), .trigger("rising"), .Select("low")) register_5 (
    .D(1'b1), .en(write4), .Q(v4), .clk(in_6));  // open: clr
  LED #(.active("true")) led_6 (.in(v5));
  Register #(.width(1), .trigger("rising"), .Select("low")) register_6 (
    .D(1'b1), .en(write5), .Q(v5), .clk(in_6));  // open: clr
  LED #(.active("true")) led_7 (.in(v6));
  Register #(.width(1), .trigger("rising"), .Select("low")) register_7 (
    .D(1'b1), .en(write6), .Q(v6), .clk(in_6));  // open: clr
  Register #(.width(1), .trigger("rising"), .Select("low")) register_8 (
    .D(1'b1), .en(write7), .Q(v7), .clk(in_6));  // open: clr
  LED #(.active("true")) led_8 (.in(v7));
  // Probe on tag0
  Register #(.width(32), .trigger("rising"), .Select("low")) register_9 (
    .D(EX_PC), .en(write0), .Q(tag0), .clk(in_6));  // open: clr
  // Probe on tag1
  Register #(.width(32), .trigger("rising"), .Select("low")) register_10 (
    .D(EX_PC), .en(write1), .Q(tag1), .clk(in_6));  // open: clr
  // Probe on tag2
  Register #(.width(32), .trigger("rising"), .Select("low")) register_11 (
    .D(EX_PC), .en(write2), .Q(tag2), .clk(in_6));  // open: clr
  // Probe on tag3
  Register #(.width(32), .trigger("rising"), .Select("low")) register_12 (
    .D(EX_PC), .en(write3), .Q(tag3), .clk(in_6));  // open: clr
  // Probe on tag4
  Register #(.width(32), .trigger("rising"), .Select("low")) register_13 (
    .D(EX_PC), .en(write4), .Q(tag4), .clk(in_6));  // open: clr
  // Probe on tag5
  Register #(.width(32), .trigger("rising"), .Select("low")) register_14 (
    .D(EX_PC), .en(write5), .Q(tag5), .clk(in_6));  // open: clr
  Register #(.width(32), .trigger("rising"), .Select("low")) register_15 (
    .D(EX_PC), .en(write6), .Q(tag6), .clk(in_6));  // open: clr
  // Probe on tag7
  Register #(.width(32), .trigger("rising"), .Select("low")) register_16 (
    .D(EX_PC), .en(write7), .Q(tag7), .clk(in_6));  // open: clr
  // Probe on tag6
  Counter #(.width(16), .max('hffff), .ongoal("wrap"), .trigger("rising"), .behavior("new")) counter_1 (
    .Q(c0), .clk(in_6), .clr(d_ff_3_q));  // open: load, D, count, carry, preset, down
  or or_1 (or_1_out, write0, L0);
  Counter #(.width(16), .max('hffff), .ongoal("wrap"), .trigger("rising"), .behavior("new")) counter_2 (
    .Q(c1), .clk(in_6), .clr(d_ff_4_q));  // open: load, D, count, carry, preset, down
  or or_2 (or_2_out, write1, L1);
  Counter #(.width(16), .max('hffff), .ongoal("wrap"), .trigger("rising"), .behavior("new")) counter_3 (
    .Q(c2), .clk(in_6), .clr(d_ff_5_q));  // open: load, D, count, carry, preset, down
  or or_3 (or_3_out, write2, L2);
  Counter #(.width(16), .max('hffff), .ongoal("wrap"), .trigger("rising"), .behavior("new")) counter_4 (
    .Q(c3), .clk(in_6), .clr(d_ff_6_q));  // open: load, D, count, carry, preset, down
  or or_4 (or_4_out, write3, L3);
  Counter #(.width(16), .max('hffff), .ongoal("wrap"), .trigger("rising"), .behavior("new")) counter_5 (
    .Q(c4), .clk(in_6), .clr(d_ff_1_q));  // open: load, D, count, carry, preset, down
  D_Flip_Flop #(.trigger("rising"), .Pre_Clr_Positions("ABOVE_BELOW"), .NegatePresetClear("false"), .enable("false"), .NewFFLayout("false")) d_ff_1 (
    .clk(in_6), .D(or_5_out), .Q(d_ff_1_q));  // open: Qn, preset, reset
  or or_5 (or_5_out, write4, L4);
  Counter #(.width(16), .max('hffff), .ongoal("wrap"), .trigger("rising"), .behavior("new")) counter_6 (
    .Q(c5), .clk(in_6), .clr(d_ff_7_q));  // open: load, D, count, carry, preset, down
  or or_6 (or_6_out, write5, L5);
  Counter #(.width(16), .max('hffff), .ongoal("wrap"), .trigger("rising"), .behavior("new")) counter_7 (
    .Q(c6), .clk(in_6), .clr(d_ff_8_q));  // open: load, D, count, carry, preset, down
  or or_7 (or_7_out, write6, L6);
  Counter #(.width(16), .max('hffff), .ongoal("wrap"), .trigger("rising"), .behavior("new")) counter_8 (
    .Q(c7), .clk(in_6), .clr(d_ff_2_q));  // open: load, D, count, carry, preset, down
  D_Flip_Flop #(.trigger("rising"), .Pre_Clr_Positions("LEGACY"), .NegatePresetClear("false"), .enable("true"), .NewFFLayout("false")) d_ff_2 (
    .clk(in_6), .D(or_8_out), .Q(d_ff_2_q));  // open: Qn, preset, en, reset
  or or_8 (or_8_out, write7, L7);
  D_Flip_Flop #(.trigger("rising"), .Pre_Clr_Positions("ABOVE_BELOW"), .NegatePresetClear("false"), .enable("false"), .NewFFLayout("false")) d_ff_3 (
    .clk(in_6), .D(or_1_out), .Q(d_ff_3_q));  // open: Qn, preset, reset
  D_Flip_Flop #(.trigger("rising"), .Pre_Clr_Positions("ABOVE_BELOW"), .NegatePresetClear("false"), .enable("false"), .NewFFLayout("false")) d_ff_4 (
    .clk(in_6), .D(or_2_out), .Q(d_ff_4_q));  // open: Qn, preset, reset
  D_Flip_Flop #(.trigger("rising"), .Pre_Clr_Positions("ABOVE_BELOW"), .NegatePresetClear("false"), .enable("false"), .NewFFLayout("false")) d_ff_5 (
    .clk(in_6), .D(or_3_out), .Q(d_ff_5_q));  // open: Qn, preset, reset
  D_Flip_Flop #(.trigger("rising"), .Pre_Clr_Positions("ABOVE_BELOW"), .NegatePresetClear("false"), .enable("false"), .NewFFLayout("false")) d_ff_6 (
    .clk(in_6), .D(or_4_out), .Q(d_ff_6_q));  // open: Qn, preset, reset
  D_Flip_Flop #(.trigger("rising"), .Pre_Clr_Positions("ABOVE_BELOW"), .NegatePresetClear("false"), .enable("false"), .NewFFLayout("false")) d_ff_7 (
    .clk(in_6), .D(or_6_out), .Q(d_ff_7_q));  // open: Qn, preset, reset
  D_Flip_Flop #(.trigger("rising"), .Pre_Clr_Positions("LEGACY"), .NegatePresetClear("false"), .enable("true"), .NewFFLayout("false")) d_ff_8 (
    .clk(in_6), .D(or_7_out), .Q(d_ff_8_q));  // open: Qn, preset, en, reset
  Register #(.width(32), .trigger("rising"), .Select("low")) register_17 (
    .D(EX_BranchAddr), .en(write0), .Q(register_17_q), .clk(in_6));  // open: clr
  Register #(.width(32), .trigger("rising"), .Select("low")) register_18 (
    .D(EX_BranchAddr), .en(write1), .Q(register_18_q), .clk(in_6));  // open: clr
  Register #(.width(32), .trigger("rising"), .Select("low")) register_19 (
    .D(EX_BranchAddr), .en(write2), .Q(register_19_q), .clk(in_6));  // open: clr
  Register #(.width(32), .trigger("rising"), .Select("low")) register_20 (
    .D(EX_BranchAddr), .en(write3), .Q(register_20_q), .clk(in_6));  // open: clr
  Register #(.width(32), .trigger("rising"), .Select("low")) register_21 (
    .D(EX_BranchAddr), .en(write4), .Q(register_21_q), .clk(in_6));  // open: clr
  Register #(.width(32), .trigger("rising"), .Select("low")) register_22 (
    .D(EX_BranchAddr), .en(write5), .Q(register_22_q), .clk(in_6));  // open: clr
  Register #(.width(32), .trigger("rising"), .Select("low")) register_23 (
    .D(EX_BranchAddr), .en(write6), .Q(register_23_q), .clk(in_6));  // open: clr
  Register #(.width(32), .trigger("rising"), .Select("low")) register_24 (
    .D(EX_BranchAddr), .en(write7), .Q(register_24_q), .clk(in_6));  // open: clr
  assign BTB_JumpAddr = L0 ? register_17_q : 32'bz;  // Controlled_Buffer controlled_buffer_1
  assign BTB_JumpAddr = L1 ? register_18_q : 32'bz;  // Controlled_Buffer controlled_buffer_2
  assign BTB_JumpAddr = L2 ? register_19_q : 32'bz;  // Controlled_Buffer controlled_buffer_3
  assign BTB_JumpAddr = L3 ? register_20_q : 32'bz;  // Controlled_Buffer controlled_buffer_4
  assign BTB_JumpAddr = L4 ? register_21_q : 32'bz;  // Controlled_Buffer controlled_buffer_5
  assign BTB_JumpAddr = L5 ? register_22_q : 32'bz;  // Controlled_Buffer controlled_buffer_6
  assign BTB_JumpAddr = L6 ? register_23_q : 32'bz;  // Controlled_Buffer controlled_buffer_7
  assign BTB_JumpAddr = L7 ? register_24_q : 32'bz;  // Controlled_Buffer controlled_buffer_8
  Comparator #(.width(32), .mode("twosComplement")) comparator_1 (
    .a(tag0), .b(PC), .eq(comparator_1_eq));  // open: gt, lt
  Comparator #(.width(32), .mode("twosComplement")) comparator_2 (
    .a(tag1), .b(PC), .eq(comparator_2_eq));  // open: gt, lt
  Comparator #(.width(32), .mode("twosComplement")) comparator_3 (
    .a(tag2), .b(PC), .eq(comparator_3_eq));  // open: gt, lt
  Comparator #(.width(32), .mode("twosComplement")) comparator_4 (
    .a(tag3), .b(PC), .eq(comparator_4_eq));  // open: gt, lt
  Comparator #(.width(32), .mode("twosComplement")) comparator_5 (
    .a(tag4), .b(PC), .eq(comparator_5_eq));  // open: gt, lt
  Comparator #(.width(32), .mode("twosComplement")) comparator_6 (
    .a(tag5), .b(PC), .eq(comparator_6_eq));  // open: gt, lt
  Comparator #(.width(32), .mode("twosComplement")) comparator_7 (
    .a(tag6), .b(PC), .eq(comparator_7_eq));  // open: gt, lt
  Comparator #(.width(32), .mode("twosComplement")) comparator_8 (
    .a(tag7), .b(PC), .eq(comparator_8_eq));  // open: gt, lt
  and and_1 (L0, v0, comparator_1_eq);
  and and_2 (L1, v1, comparator_2_eq);
  and and_3 (L2, v2, comparator_3_eq);
  and and_4 (L3, v3, comparator_4_eq);
  and and_5 (L4, v4, comparator_5_eq);
  and and_6 (L5, v5, comparator_6_eq);
  and and_7 (L6, v6, comparator_7_eq);
  and and_8 (L7, v7, comparator_8_eq);
  Comparator #(.width(32), .mode("twosComplement")) comparator_9 (
    .a(tag0), .b(EX_PC), .eq(comparator_9_eq));  // open: gt, lt
  Comparator #(.width(32), .mode("twosComplement")) comparator_10 (
    .a(tag1), .b(EX_PC), .eq(comparator_10_eq));  // open: gt, lt
  Comparator #(.width(32), .mode("twosComplement")) comparator_11 (
    .a(tag2), .b(EX_PC), .eq(comparator_11_eq));  // open: gt, lt
  Comparator #(.width(32), .mode("twosComplement")) comparator_12 (
    .a(tag3), .b(EX_PC), .eq(comparator_12_eq));  // open: gt, lt
  Comparator #(.width(32), .mode("twosComplement")) comparator_13 (
    .a(tag4), .b(EX_PC), .eq(comparator_13_eq));  // open: gt, lt
  Comparator #(.width(32), .mode("twosComplement")) comparator_14 (
    .a(tag5), .b(EX_PC), .eq(comparator_14_eq));  // open: gt, lt
  Comparator #(.width(32), .mode("twosComplement")) comparator_15 (
    .a(tag6), .b(EX_PC), .eq(comparator_15_eq));  // open: gt, lt
  Comparator #(.width(32), .mode("twosComplement")) comparator_16 (
    .a(tag7), .b(EX_PC), .eq(comparator_16_eq));  // open: gt, lt
  and and_9 (M0, v0, comparator_9_eq);
  and and_10 (M1, v1, comparator_10_eq);
  and and_11 (M2, v2, comparator_11_eq);
  and and_12 (M3, v3, comparator_12_eq);
  and and_13 (M4, v4, comparator_13_eq);
  and and_14 (M5, v5, comparator_14_eq);
  and and_15 (M6, v6, comparator_15_eq);
  and and_16 (M7, v7, comparator_16_eq);
  not not_1 (not_1_out, v0);
  not not_2 (not_2_out, v1);
  not not_3 (not_3_out, v2);
  not not_4 (not_4_out, v3);
  not not_5 (not_5_out, v4);
  not not_6 (not_6_out, v5);
  not not_7 (not_7_out, v6);
  not not_8 (not_8_out, v7);
  MAX max_1 (.Y(c1), .X(c0), .Y_num(3'b001), .X_num(3'b000), .MAX(max_1_max), .Max_num(max_1_max_num));
  MAX max_2 (.Y(c3), .X(c2), .Y_num(3'b011), .X_num(3'b010), .MAX(max_2_max), .Max_num(max_2_max_num));
  MAX max_3 (.Y(c5), .X(c4), .Y_num(3'b101), .X_num(3'b100), .MAX(max_3_max), .Max_num(max_3_max_num));
  MAX max_4 (.Y(c7), .X(c6), .Y_num(3'b111), .X_num(3'b110), .MAX(max_4_max), .Max_num(max_4_max_num));
  or or_9 (EX_Hit, M0, M1, M2, M3, M4, M5, M6, M7);
  not not_9 (EX_Miss, EX_Hit);
  Priority_Encoder #(.select(3), .disabled("Z")) priority_encoder_1 (
    .in0(not_1_out), .in1(not_2_out), .in2(not_3_out), .in3(not_4_out), .in4(not_5_out), .in5(not_6_out),
    .in6(not_7_out), .in7(not_8_out), .out(priority_encoder_1_out), .gs(priority_encoder_1_gs));  // open: en_out, en_in
  MAX max_5 (
    .Y(max_2_max), .X(max_1_max), .Y_num(max_2_max_num), .X_num(max_1_max_num), .MAX(max_5_max),
    .Max_num(max_5_max_num));
  MAX max_6 (
    .Y(max_4_max), .X(max_3_max), .Y_num(max_4_max_num), .X_num(max_3_max_num), .MAX(max_6_max),
    .Max_num(max_6_max_num));
  and and_17 (and_17_out, v0, v1, v2, v3, v4, v5, v6, v7);
  Decoder #(.select(3), .tristate("false"), .disabled(0), .enable("true")) decoder_1 (
    .out0(decoder_1_out0), .out1(decoder_1_out1), .out2(decoder_1_out2), .out3(decoder_1_out3),
    .out4(decoder_1_out4), .out5(decoder_1_out5), .out6(decoder_1_out6), .out7(decoder_1_out7),
    .sel(priority_encoder_1_out), .en(priority_encoder_1_gs));
  Decoder #(.select(3), .tristate("false"), .disabled(0), .enable("true")) decoder_2 (
    .out0(decoder_2_out0), .out1(decoder_2_out1), .out2(decoder_2_out2), .out3(decoder_2_out3),
    .out4(decoder_2_out4), .out5(decoder_2_out5), .out6(decoder_2_out6), .out7(decoder_2_out7),
    .sel(max_7_max_num), .en(and_17_out));
  MAX max_7 (
    .Y(max_6_max), .X(max_5_max), .Y_num(max_6_max_num), .X_num(max_5_max_num), .Max_num(max_7_max_num));  // open: MAX
  or or_10 (or_10_out, decoder_1_out0, decoder_2_out0);
  or or_11 (or_11_out, decoder_1_out1, decoder_2_out1);
  or or_12 (or_12_out, decoder_1_out2, decoder_2_out2);
  or or_13 (or_13_out, decoder_1_out3, decoder_2_out3);
  or or_14 (or_14_out, decoder_1_out4, decoder_2_out4);
  or or_15 (or_15_out, decoder_1_out5, decoder_2_out5);
  or or_16 (or_16_out, decoder_1_out6, decoder_2_out6);
  or or_17 (or_17_out, decoder_1_out7, decoder_2_out7);
  and and_18 (write0, or_10_out, EX_Miss, EX_Branch);
  and and_19 (write1, or_11_out, EX_Miss, EX_Branch);
  and and_20 (write2, or_12_out, EX_Miss, EX_Branch);
  and and_21 (write3, or_13_out, EX_Miss, EX_Branch);
  and and_22 (write4, or_14_out, EX_Miss, EX_Branch);
  and and_23 (write5, or_15_out, EX_Miss, EX_Branch);
  and and_24 (write6, or_16_out, EX_Miss, EX_Branch);
  and and_25 (write7, or_17_out, EX_Miss, EX_Branch);
  assign {ID_PredictJump, controlled_buffer_9_out[0]} = L0 ? predict0 : 2'bz;  // Controlled_Buffer controlled_buffer_9
  assign {ID_PredictJump, controlled_buffer_10_out[0]} = L1 ? predict1 : 2'bz;  // Controlled_Buffer controlled_buffer_10
  assign {ID_PredictJump, controlled_buffer_11_out[0]} = L2 ? predict2 : 2'bz;  // Controlled_Buffer controlled_buffer_11
  assign {ID_PredictJump, controlled_buffer_12_out[0]} = L3 ? predict3 : 2'bz;  // Controlled_Buffer controlled_buffer_12
  assign {ID_PredictJump, controlled_buffer_13_out[0]} = L4 ? predict4 : 2'bz;  // Controlled_Buffer controlled_buffer_13
  assign {ID_PredictJump, controlled_buffer_14_out[0]} = L5 ? predict5 : 2'bz;  // Controlled_Buffer controlled_buffer_14
  assign {ID_PredictJump, controlled_buffer_15_out[0]} = L6 ? predict6 : 2'bz;  // Controlled_Buffer controlled_buffer_15
  assign {ID_PredictJump, controlled_buffer_16_out[0]} = L7 ? predict7 : 2'bz;  // Controlled_Buffer controlled_buffer_16
  Pull_Resistor #(.pull(0)) pull_resistor_1 (.node(ID_PredictJump));
  FSM fsm_1 (
    .high(predict0[1]), .low(predict0[0]), .jump(EX_Branched), .NextHigh(fsm_1_nextlow[1]),
    .NextLow(fsm_1_nextlow[0]));
  FSM fsm_2 (
    .high(predict1[1]), .low(predict1[0]), .jump(EX_Branched), .NextHigh(fsm_2_nextlow[1]),
    .NextLow(fsm_2_nextlow[0]));
  FSM fsm_3 (
    .high(predict2[1]), .low(predict2[0]), .jump(EX_Branched), .NextHigh(fsm_3_nextlow[1]),
    .NextLow(fsm_3_nextlow[0]));
  FSM fsm_4 (
    .high(predict3[1]), .low(predict3[0]), .jump(EX_Branched), .NextHigh(fsm_4_nextlow[1]),
    .NextLow(fsm_4_nextlow[0]));
  FSM fsm_5 (
    .high(predict4[1]), .low(predict4[0]), .jump(EX_Branched), .NextHigh(fsm_5_nextlow[1]),
    .NextLow(fsm_5_nextlow[0]));
  FSM fsm_6 (
    .high(predict5[1]), .low(predict5[0]), .jump(EX_Branched), .NextHigh(fsm_6_nextlow[1]),
    .NextLow(fsm_6_nextlow[0]));
  FSM fsm_7 (
    .high(predict6[1]), .low(predict6[0]), .jump(EX_Branched), .NextHigh(fsm_7_nextlow[1]),
    .NextLow(fsm_7_nextlow[0]));
  FSM fsm_8 (
    .high(predict7[1]), .low(predict7[0]), .jump(EX_Branched), .NextHigh(fsm_8_nextlow[1]),
    .NextLow(fsm_8_nextlow[0]));
  and and_26 (and_26_out, EX_Branch, M0);
  Register #(.width(2), .trigger("rising"), .Select("low")) register_25 (
    .D(fsm_1_nextlow), .en(and_26_out), .Q(predict0), .clk(in_6));  // open: clr
  and and_27 (and_27_out, EX_Branch, M1);
  Register #(.width(2), .trigger("rising"), .Select("low")) register_26 (
    .D(fsm_2_nextlow), .en(and_27_out), .Q(predict1), .clk(in_6));  // open: clr
  and and_28 (and_28_out, EX_Branch, M2);
  Register #(.width(2), .trigger("rising"), .Select("low")) register_27 (
    .D(fsm_3_nextlow), .en(and_28_out), .Q(predict2), .clk(in_6));  // open: clr
  and and_29 (and_29_out, EX_Branch, M3);
  Register #(.width(2), .trigger("rising"), .Select("low")) register_28 (
    .D(fsm_4_nextlow), .en(and_29_out), .Q(predict3), .clk(in_6));  // open: clr
  and and_30 (and_30_out, EX_Branch, M4);
  Register #(.width(2), .trigger("rising"), .Select("low")) register_29 (
    .D(fsm_5_nextlow), .en(and_30_out), .Q(predict4), .clk(in_6));  // open: clr
  and and_31 (and_31_out, EX_Branch, M5);
  Register #(.width(2), .trigger("rising"), .Select("low")) register_30 (
    .D(fsm_6_nextlow), .en(and_31_out), .Q(predict5), .clk(in_6));  // open: clr
  and and_32 (and_32_out, EX_Branch, M6);
  Register #(.width(2), .trigger("rising"), .Select("low")) register_31 (
    .D(fsm_7_nextlow), .en(and_32_out), .Q(predict6), .clk(in_6));  // open: clr
  and and_33 (and_33_out, EX_Branch, M7);
  Register #(.width(2), .trigger("rising"), .Select("low")) register_32 (
    .D(fsm_8_nextlow), .en(and_33_out), .Q(predict7), .clk(in_6));  // open: clr

  // Other names for the same wires on the sheet: CLK = in_6; Tag[31:0] = EX_PC

  // Notes on the sheet:
  //   EX写入逻辑
  //   历史预测位
  //   与PC比较数据命中  选择L而不是M
  //   EX.PC如果数据命中，需要根据EX.Branched的值依据预测位状态机更新分支预测历史位的值
endmodule

module FSM (
  input  high,
  input  low,
  input  jump,
  output NextHigh,
  output NextLow
);

  wire and_1_out, and_2_out, and_3_out, and_4_out, not_1_out, not_2_out, not_3_out, not_4_out, not_5_out;

  not not_1 (not_1_out, low);
  not not_2 (not_2_out, high);
  not not_3 (not_3_out, low);
  not not_4 (not_4_out, low);
  not not_5 (not_5_out, jump);
  and and_1 (and_1_out, low, jump);
  and and_2 (and_2_out, high, not_1_out);
  and and_3 (and_3_out, not_2_out, not_3_out, jump);
  and and_4 (and_4_out, high, not_4_out, not_5_out);
  or or_1 (NextHigh, and_1_out, and_2_out);
  or or_2 (NextLow, and_3_out, and_4_out);
endmodule

module \重定向分支预测  (
  output RegWrite,
  output MemWrite,
  output [31:0] IF_PC,
  output [31:0] ID_PC,
  output [31:0] EX_PC,
  output [31:0] M_PC,
  output [31:0] WB_PC,
  output [31:0] RDin,
  output [31:0] MDin,
  output [31:0] LedData
);

  wire and_1_out, and_2_out, and_3_out, and_4_out, and_5_out, and_6_out, and_7_out, and_8_out, and_9_out,
       and_10_out, and_11_out, and_12_out, and_13_out, bgtz, BranchTaken, CLK, clock_1_out, clock_2_out,
       comparator_1_eq, comparator_1_lt, comparator_2_gt, comparator_3_eq, comparator_4_eq, d_ff_1_q, EX_beg,
       EX_bne, EX_Branch, EX_jal, EX_JMP, EX_JR, ex_mem_1_lb_2, ex_mem_1_memtoreg_2, ex_mem_1_sys_2,
       EX_memtoreg, EX_PredictJump, EX_regdst, EX_RegWrite, Go, halt, id_ex_1_alu_src_2, id_ex_1_lb_2,
       id_ex_1_memwrite_2, id_ex_1_syscall_2, ID_PredictJump, IF_PredictJump, IR1, IR2, IR3, lb, Ledout,
       loaduse, MEM_jal, MEM_regdst, MEM_RegWrite, memtoreg, mips_alu_1_equal, multiplexer_10_out,
       multiplexer_12_out, multiplexer_14_out, multiplexer_17_out, nand_1_out, not_1_out, not_2_out,
       not_3_out, not_4_out, not_5_out, not_6_out, not_7_out, not_8_out, not_9_out, not_10_out, not_12_out,
       or_2_out, or_3_out, or_4_out, or_6_out, or_7_out, Predicterror, RST, RsUsed, RtUsed, SignedExt, sllv,
       Syscall, W1, W2, W3, WB_jal, WB_regdst, WB_syscall, \单周期硬布线控制器_1_alu_src , \单周期硬布线控制器_1_beq ,
       \单周期硬布线控制器_1_bgtz , \单周期硬布线控制器_1_bne , \单周期硬布线控制器_1_jal , \单周期硬布线控制器_1_jmp , \单周期硬布线控制器_1_jr ,
       \单周期硬布线控制器_1_lb , \单周期硬布线控制器_1_memtoreg , \单周期硬布线控制器_1_memwrite , \单周期硬布线控制器_1_regdst ,
       \单周期硬布线控制器_1_regwrite , \单周期硬布线控制器_1_signedext , \单周期硬布线控制器_1_sllv , \条件分支 , \条件分支出现 ;
  wire [1:0] Addr10, EX_Rs_F, EX_Rt_F, IF_Rs_F, IF_Rt_F;
  wire [3:0] id_ex_1_aluop_2, \单周期硬布线控制器_1_alu_op ;
  wire [4:0] EX_WriteReg_num, MEM_WriteReg_num, multiplexer_8_out, multiplexer_9_out, multiplexer_16_out,
       multiplexer_18_out, multiplexer_22_out, Rs_num, Rt_num;
  wire [5:0] Func;
  wire [12:0] CNT_num;
  wire [15:0] \LoadUse次数 , \总周期数 , \插入气泡数 , \无条件分支数 , \条件分支成功数 ;
  wire [25:0] id_ex_1_imm26_2;
  wire [31:0] bit_extender_1_out, bit_extender_2_out, bit_extender_3_out, bit_extender_4_out,
       bit_extender_5_out, bit_extender_6_out, bit_extender_7_out, btb_1_btb_jumpaddr, EX_BranchAddr, EX_IR,
       ex_mem_1_pc_4_2, EX_PC_4, EX_R1Data, EX_R2Data, EX_redirctR1Data, EX_redirctR2Data, ID_R1Data,
       if_id_1_pc_4_2, IF_IR, IF_PC_4, JMPAddr, MEM_IR, MEM_R1data, MEM_redirect, mem_wb_1_aludata_2,
       mem_wb_1_memdata_2, memoword, mips_alu_1_result, mips_regifile_1_r2, multiplexer_1_out,
       multiplexer_2_out, multiplexer_3_out, multiplexer_4_out, multiplexer_13_out, multiplexer_15_out,
       multiplexer_24_out, PredictAddr, ram_1_data, shifter_2_out, signmemo, WB_IR, WB_PC_4, WB_R1Data,
       WB_R2Data, \条件分支Addr ;
  wire [31:6] ID_IR;

  Button \u_总复位  (.out(RST));
  Button _1 (.out(IR1));
  Button _2 (.out(IR2));
  Button _3 (.out(IR3));
  // Probe on \总周期数 
  // Probe on \总周期数 
  Button \u_继续运行  (.out(Go));
  LED #(.active("true")) led_1 (.in(W1));
  LED #(.active("true")) led_2 (.in(W2));
  LED #(.active("true")) led_3 (.in(W3));
  Hex_Digit_Display hex_digit_display_1 (.value(LedData[31:28]));  // open: dp
  // Probe on IF_PC[19:0]
  // Mips_Probe mips_probe_1: pin names not known; wires that end beside it: IF_IR
  Multiplexer #(.select(1), .width(32), .disabled("Z"), .enable("false")) multiplexer_1 (
    .in0(EX_PC_4), .in1(\条件分支Addr ), .out(multiplexer_1_out), .sel(\条件分支 ));
  Hex_Digit_Display hex_digit_display_2 (.value(LedData[23:20]));  // open: dp
  Hex_Digit_Display hex_digit_display_3 (.value(LedData[27:24]));  // open: dp
  // Probe on ID_PC[19:0]
  // Mips_Probe mips_probe_2: pin names not known; wires that end beside it: {ID_IR, Func}
  Multiplexer #(.select(1), .width(32), .disabled("Z"), .enable("false")) multiplexer_2 (
    .in0(multiplexer_1_out), .in1(JMPAddr), .out(multiplexer_2_out), .sel(EX_JMP));
  Multiplexer #(.select(1), .width(32), .disabled("Z"), .enable("false")) multiplexer_3 (
    .in0(multiplexer_2_out), .in1(EX_redirctR1Data), .out(multiplexer_3_out), .sel(EX_JR));
  or or_1 (\条件分支出现 , EX_beg, EX_bne, bgtz);
  Hex_Digit_Display hex_digit_display_4 (.value(LedData[19:16]));  // open: dp
  Hex_Digit_Display hex_digit_display_5 (.value(LedData[15:12]));  // open: dp
  Hex_Digit_Display hex_digit_display_6 (.value(LedData[7:4]));  // open: dp
  Hex_Digit_Display hex_digit_display_7 (.value(LedData[11:8]));  // open: dp
  Clock #(.highDuration(1), .lowDuration(1)) clock_1 (.out(clock_1_out));
  // Probe on EX_PC[19:0]
  // Mips_Probe mips_probe_3: pin names not known; wires that end beside it: clock_1_out, EX_IR, CLK
  Multiplexer #(.select(1), .width(32), .disabled("Z"), .enable("false")) multiplexer_4 (
    .in0(PredictAddr), .in1(multiplexer_3_out), .out(multiplexer_4_out), .sel(Predicterror));
  Hex_Digit_Display hex_digit_display_8 (.value(LedData[3:0]));  // open: dp
  or or_2 (or_2_out, and_1_out, Go);
  and and_1 (and_1_out, not_1_out, not_2_out);
  not not_1 (not_1_out, loaduse);
  not not_2 (not_2_out, halt);
  // Probe on \总周期数 
  // Probe on M_PC[19:0]
  // Mips_Probe mips_probe_4: pin names not known; wires that end beside it: MEM_IR
  Register #(.width(32), .trigger("rising"), .Select("low")) PC (
    .D(multiplexer_4_out), .en(or_2_out), .Q(IF_PC), .clk(CLK), .clr(RST));
  Multiplexer #(.select(3), .width(32), .disabled("Z"), .enable("false")) multiplexer_5 (
    .in0(IF_PC), .in1(EX_redirctR1Data), .in2(JMPAddr), .in4(\条件分支Addr ), .out(EX_BranchAddr),
    .sel({\条件分支出现 , EX_JMP, EX_JR}));  // open: in3, in5, in6, in7
  // Probe on {\条件分支出现 , EX_JMP, EX_JR}
  // Probe on \总周期数 
  // Probe on \无条件分支数 
  // Probe on \条件分支成功数 
  // Probe on \插入气泡数 
  // Probe on \LoadUse次数 
  Adder #(.width(32)) adder_1 (.a(IF_PC), .b(32'h4), .out(IF_PC_4));  // open: cin, cout
  // Probe on IF_PC[11:0]
  // Probe on WB_PC[19:0]
  // Mips_Probe mips_probe_5: pin names not known; wires that end beside it: WB_IR
  // Probe on EX_PC[11:0]
  // Probe on ID_PC[11:0]
  // Mips_Probe mips_probe_6: pin names not known; wires that end beside it: IF_PC, IF_IR
  ROM #(.addrWidth(10), .dataWidth(32), .Select("high")) rom_1 (.addr(IF_PC[11:2]), .data(IF_IR));
  // Probe on M_PC[11:0]
  D_Flip_Flop #(.trigger("high"), .Pre_Clr_Positions("LEGACY"), .NegatePresetClear("false"), .enable("true"), .NewFFLayout("false")) d_ff_1 (.Q(d_ff_1_q));  // open: clk, D, Qn, preset, en, reset
  // Probe on 13'h39d
  or or_3 (or_3_out, Predicterror, RST);
  // Probe on WB_PC[11:0]
  Comparator #(.width(13), .mode("twosComplement")) comparator_1 (
    .a(CNT_num), .b(13'h39d), .eq(comparator_1_eq), .lt(comparator_1_lt));  // open: gt
  Clock #(.highDuration(1), .lowDuration(1)) clock_2 (.out(clock_2_out));
  or or_4 (or_4_out, loaduse, and_2_out);
  IF__ID if_id_1 (
    .CLK(CLK), .\同步清零_高 (or_3_out), .\使能端_低 (or_4_out), .PC(IF_PC), .IR(IF_IR), .PC_4(IF_PC_4), .PC_2(ID_PC),
    .IR_2({ID_IR, Func}), .PC_4_2(if_id_1_pc_4_2), .PredictJump(IF_PredictJump),
    .PredictJump_2(ID_PredictJump));
  nand nand_1 (nand_1_out, d_ff_1_q, comparator_1_eq);
  Counter #(.width(13), .max('h1fff), .ongoal("stay"), .trigger("rising"), .behavior("old")) counter_1 (
    .count(comparator_1_lt), .Q(CNT_num), .clk(clock_2_out));  // open: load, D, carry, clr, preset
  and and_2 (and_2_out, halt, ~Go);  // AND_Gate
  assign CLK = nand_1_out ? clock_2_out : 1'bz;  // Controlled_Buffer controlled_buffer_1
  or or_5 (EX_Branch, EX_beg, EX_bne, bgtz, EX_JMP, EX_JR);
  Pull_Resistor #(.pull(1)) pull_resistor_1 (.node(CLK));
  \R1R2检测  \r1r2检测_1  (
    .OP0(ID_IR[26]), .OP1(ID_IR[27]), .OP2(ID_IR[28]), .OP3(ID_IR[29]), .OP4(ID_IR[30]), .OP5(ID_IR[31]),
    .F0(Func[0]), .F1(Func[1]), .F2(Func[2]), .F3(Func[3]), .F4(Func[4]), .F5(Func[5]), .R1_used(RsUsed),
    .R2_used(RtUsed));
  \load_used检测  \load_used检测_1  (
    .Rs_used(RsUsed), .Rt_used(RtUsed), .Rs_num(Rs_num), .Rt_num(Rt_num), .EX_WriteReg_num(EX_WriteReg_num),
    .EX_memtoreg(EX_memtoreg), .load_used(loaduse));
  \单周期硬布线控制器  \u_单周期硬布线控制器_1  (
    .Func(Func), .OP(ID_IR[31:26]), .ALU_OP(\单周期硬布线控制器_1_alu_op ), .MemToReg(\单周期硬布线控制器_1_memtoreg ),
    .MemWrite(\单周期硬布线控制器_1_memwrite ), .ALU_SRC(\单周期硬布线控制器_1_alu_src ), .RegWrite(\单周期硬布线控制器_1_regwrite ),
    .SysCALL(Syscall), .SignedExt(\单周期硬布线控制器_1_signedext ), .RegDst(\单周期硬布线控制器_1_regdst ),
    .JR(\单周期硬布线控制器_1_jr ), .JMP(\单周期硬布线控制器_1_jmp ), .Beq(\单周期硬布线控制器_1_beq ), .JAL(\单周期硬布线控制器_1_jal ),
    .Bne(\单周期硬布线控制器_1_bne ), .sllv(\单周期硬布线控制器_1_sllv ), .bgtz(\单周期硬布线控制器_1_bgtz ), .lb(\单周期硬布线控制器_1_lb ));
  Multiplexer #(.select(1), .width(5), .disabled("Z"), .enable("false")) multiplexer_6 (
    .in0(ID_IR[25:21]), .in1(5'b00010), .out(Rs_num), .sel(Syscall));
  Multiplexer #(.select(1), .width(5), .disabled("Z"), .enable("false")) multiplexer_7 (
    .in0(ID_IR[20:16]), .in1(5'b00100), .out(Rt_num), .sel(Syscall));
  Multiplexer #(.select(1), .width(5), .disabled("Z"), .enable("false")) multiplexer_8 (
    .in0(WB_IR[20:16]), .in1(WB_IR[15:11]), .out(multiplexer_8_out), .sel(WB_regdst));
  Multiplexer #(.select(1), .width(5), .disabled("Z"), .enable("false")) multiplexer_9 (
    .in0(multiplexer_8_out), .in1({5{1'b1}}), .out(multiplexer_9_out), .sel(WB_jal));
  Counter #(.width(16), .max('hffff), .ongoal("wrap"), .trigger("rising"), .behavior("old")) counter_2 (
    .count(1'b1), .Q(\无条件分支数 ), .clk(multiplexer_10_out), .clr(RST));  // open: load, D, carry, preset
  Multiplexer #(.select(1), .width(1), .disabled("Z"), .enable("false")) multiplexer_10 (
    .in0(and_3_out), .in1(1'b0), .out(multiplexer_10_out), .sel(not_3_out));
  not not_3 (not_3_out, not_4_out);
  not not_4 (not_4_out, CLK);
  and and_3 (and_3_out, EX_JMP, CLK);
  MIPS_Regifile mips_regifile_1 (
    .Din(RDin), .Clk(CLK), .R1(ID_R1Data), .R2(mips_regifile_1_r2), .WE(RegWrite), .W_num(multiplexer_9_out),
    .R1_num(Rs_num), .R2_num(Rt_num));
  \RSRT控制端  \rsrt控制端_1  (
    .Rs_used(RsUsed), .Rs_num(Rs_num), .EX_RegWrite(EX_RegWrite), .EX_WriteReg_num(EX_WriteReg_num),
    .MEM_RegWrite(MEM_RegWrite), .MEM_WriteReg(MEM_WriteReg_num), .Rt_used(RtUsed), .Rt_num(Rt_num),
    .RsUsed(IF_Rs_F), .RtUsed(IF_Rt_F));
  BTB btb_1 (
    .PC(IF_PC), .EX_PC(EX_PC), .EX_BranchAddr(EX_BranchAddr), .EX_Branch(EX_Branch),
    .EX_Branched(BranchTaken), .in_6(CLK), .ID_PredictJump(IF_PredictJump), .BTB_JumpAddr(btb_1_btb_jumpaddr));
  or or_6 (or_6_out, loaduse, Predicterror, RST);
  and and_4 (and_4_out, halt, ~Go);  // AND_Gate
  Multiplexer #(.select(1), .width(32), .disabled("Z"), .enable("false")) multiplexer_11 (
    .in0(IF_PC_4), .in1(btb_1_btb_jumpaddr), .out(PredictAddr), .sel(IF_PredictJump));
  Counter #(.width(16), .max('hffff), .ongoal("wrap"), .trigger("rising"), .behavior("old")) counter_3 (
    .count(1'b1), .Q(\条件分支成功数 ), .clk(multiplexer_12_out), .clr(RST));  // open: load, D, carry, preset
  Multiplexer #(.select(1), .width(1), .disabled("Z"), .enable("false")) multiplexer_12 (
    .in0(and_5_out), .in1(1'b0), .out(multiplexer_12_out), .sel(not_5_out));
  not not_5 (not_5_out, not_6_out);
  not not_6 (not_6_out, CLK);
  and and_5 (and_5_out, \条件分支 , CLK);
  ID__EX id_ex_1 (
    .CLK(CLK), .\同步清零_高 (or_6_out), .\使能端_低 (and_4_out), .JMP(\单周期硬布线控制器_1_jmp ), .IR({ID_IR, Func}),
    .JR(\单周期硬布线控制器_1_jr ), .signedext(\单周期硬布线控制器_1_signedext ), .PC(ID_PC), .beq(\单周期硬布线控制器_1_beq ),
    .bne(\单周期硬布线控制器_1_bne ), .R1(ID_R1Data), .memtoreg(\单周期硬布线控制器_1_memtoreg ), .R2(mips_regifile_1_r2),
    .memwrite(\单周期硬布线控制器_1_memwrite ), .aluop(\单周期硬布线控制器_1_alu_op ), .sllv(\单周期硬布线控制器_1_sllv ),
    .imm26({ID_IR[25:6], Func}), .alu_src(\单周期硬布线控制器_1_alu_src ), .bgtz(\单周期硬布线控制器_1_bgtz ),
    .regwrite(\单周期硬布线控制器_1_regwrite ), .lb(\单周期硬布线控制器_1_lb ), .jal(\单周期硬布线控制器_1_jal ),
    .regdst(\单周期硬布线控制器_1_regdst ), .syscall(Syscall), .JMP_2(EX_JMP), .IR_2(EX_IR), .JR_2(EX_JR),
    .signedext_2(SignedExt), .PC_2(EX_PC), .beq_2(EX_beg), .bne_2(EX_bne), .R1_2(EX_R1Data),
    .memtoreg_2(EX_memtoreg), .R2_2(EX_R2Data), .memwrite_2(id_ex_1_memwrite_2), .aluop_2(id_ex_1_aluop_2),
    .sllv_2(sllv), .imm26_2(id_ex_1_imm26_2), .alu_src_2(id_ex_1_alu_src_2), .bgtz_2(bgtz),
    .regwrite_2(EX_RegWrite), .lb_2(id_ex_1_lb_2), .jal_2(EX_jal), .regdst_2(EX_regdst),
    .syscall_2(id_ex_1_syscall_2), .PC_4(if_id_1_pc_4_2), .PC_4_2(EX_PC_4), .IF_Rs_F(IF_Rs_F),
    .EX_Rs_F(EX_Rs_F), .IF_Rt_F(IF_Rt_F), .EX_Rt_F(EX_Rt_F), .PredictJump(ID_PredictJump),
    .PredictJump_2(EX_PredictJump));
  assign bit_extender_1_out = {{6{id_ex_1_imm26_2[25]}}, id_ex_1_imm26_2};  // Bit_Extender bit_extender_1
  Shifter #(.width(32), .shift("ll")) shifter_1 (.in(bit_extender_1_out), .\dist (5'b00010), .out(JMPAddr));
  assign bit_extender_2_out = {{16{1'b0}}, id_ex_1_imm26_2[15:0]};  // Bit_Extender bit_extender_2
  assign bit_extender_3_out = {{16{id_ex_1_imm26_2[15]}}, id_ex_1_imm26_2[15:0]};  // Bit_Extender bit_extender_3
  or or_7 (or_7_out, loaduse, Predicterror);
  Multiplexer #(.select(1), .width(32), .disabled("Z"), .enable("false")) multiplexer_13 (
    .in0(bit_extender_2_out), .in1(bit_extender_3_out), .out(multiplexer_13_out), .sel(SignedExt));
  Shifter #(.width(32), .shift("ll")) shifter_2 (.in(bit_extender_3_out), .\dist (5'b00010), .out(shifter_2_out));
  Counter #(.width(16), .max('hffff), .ongoal("wrap"), .trigger("rising"), .behavior("old")) counter_4 (
    .count(1'b1), .Q(\插入气泡数 ), .clk(multiplexer_14_out), .clr(RST));  // open: load, D, carry, preset
  Multiplexer #(.select(1), .width(1), .disabled("Z"), .enable("false")) multiplexer_14 (
    .in0(and_6_out), .in1(1'b0), .out(multiplexer_14_out), .sel(not_7_out));
  not not_7 (not_7_out, not_8_out);
  not not_8 (not_8_out, CLK);
  and and_6 (and_6_out, and_7_out, CLK);
  and and_7 (and_7_out, ~halt, or_7_out);  // AND_Gate
  Multiplexer #(.select(1), .width(32), .disabled("Z"), .enable("false")) multiplexer_15 (
    .in0(EX_redirctR2Data), .in1(multiplexer_13_out), .out(multiplexer_15_out), .sel(id_ex_1_alu_src_2));
  Adder #(.width(32)) adder_2 (.a(shifter_2_out), .b(EX_PC_4), .out(\条件分支Addr ));  // open: cin, cout
  Comparator #(.width(32), .mode("unsigned")) comparator_2 (
    .a(EX_redirctR1Data), .b({32{1'b0}}), .gt(comparator_2_gt));  // open: eq, lt
  MIPS_ALU mips_alu_1 (
    .X(EX_redirctR1Data), .Y(multiplexer_15_out), .AluOP(id_ex_1_aluop_2), .Equal(mips_alu_1_equal),
    .Result(mips_alu_1_result), .shamt(multiplexer_16_out));  // open: Result_2
  Multiplexer #(.select(1), .width(5), .disabled("Z"), .enable("false")) multiplexer_16 (
    .in0(id_ex_1_imm26_2[10:6]), .in1(EX_redirctR1Data[4:0]), .out(multiplexer_16_out), .sel(sllv));
  and and_8 (and_8_out, comparator_2_gt, bgtz);
  and and_9 (and_9_out, mips_alu_1_equal, EX_beg);
  and and_10 (and_10_out, ~mips_alu_1_equal, EX_bne);  // AND_Gate
  Counter #(.width(16), .max('hffff), .ongoal("wrap"), .trigger("rising"), .behavior("old")) counter_5 (
    .count(1'b1), .Q(\LoadUse次数 ), .clk(multiplexer_17_out), .clr(RST));  // open: load, D, carry, preset
  Multiplexer #(.select(1), .width(1), .disabled("Z"), .enable("false")) multiplexer_17 (
    .in0(and_11_out), .in1(1'b0), .out(multiplexer_17_out), .sel(not_10_out));
  not not_9 (not_9_out, CLK);
  not not_10 (not_10_out, not_9_out);
  and and_11 (and_11_out, loaduse, CLK);
  or or_8 (\条件分支 , and_8_out, and_9_out, and_10_out);
  Multiplexer #(.select(1), .width(5), .disabled("Z"), .enable("false")) multiplexer_18 (
    .in0(EX_IR[20:16]), .in1(EX_IR[15:11]), .out(multiplexer_18_out), .sel(EX_regdst));
  or or_9 (BranchTaken, \条件分支 , EX_JR, EX_JMP);
  Multiplexer #(.select(1), .width(5), .disabled("Z"), .enable("false")) multiplexer_19 (
    .in0(multiplexer_18_out), .in1({5{1'b1}}), .out(EX_WriteReg_num), .sel(EX_jal));
  Multiplexer #(.select(2), .width(32), .disabled("Z"), .enable("false")) multiplexer_20 (
    .in0(EX_R1Data), .in1(RDin), .in2(MEM_redirect), .out(EX_redirctR1Data), .sel(EX_Rs_F));  // open: in3
  Comparator #(.width(1), .mode("twosComplement")) comparator_3 (
    .a(BranchTaken), .b(EX_PredictJump), .eq(comparator_3_eq));  // open: gt, lt
  Multiplexer #(.select(2), .width(32), .disabled("Z"), .enable("false")) multiplexer_21 (
    .in0(EX_R2Data), .in1(RDin), .in2(MEM_redirect), .out(EX_redirctR2Data), .sel(EX_Rt_F));  // open: in3
  not not_11 (Predicterror, comparator_3_eq);
  and and_12 (and_12_out, halt, ~Go);  // AND_Gate
  EX__MEM ex_mem_1 (
    .CLK(CLK), .\同步清零_高 (RST), .\使能端_低 (and_12_out), .IR(EX_IR), .PC(EX_PC), .memtoreg(EX_memtoreg),
    .memwrite(id_ex_1_memwrite_2), .PC_4(EX_PC_4), .regwrite(EX_RegWrite), .lb(id_ex_1_lb_2), .jal(EX_jal),
    .regdst(EX_regdst), .IR_2(MEM_IR), .PC_2(M_PC), .memtoreg_2(ex_mem_1_memtoreg_2), .memwrite_2(MemWrite),
    .PC_4_2(ex_mem_1_pc_4_2), .regwrite_2(MEM_RegWrite), .lb_2(ex_mem_1_lb_2), .jal_2(MEM_jal),
    .regdst_2(MEM_regdst), .ALUdata(mips_alu_1_result), .ALUdata_2(MEM_redirect), .R1(EX_redirctR1Data),
    .R1_2(MEM_R1data), .R2(EX_redirctR2Data), .R2_2(MDin), .sys(id_ex_1_syscall_2), .sys_2(ex_mem_1_sys_2));
  Multiplexer #(.select(1), .width(5), .disabled("Z"), .enable("false")) multiplexer_22 (
    .in0(MEM_IR[20:16]), .in1(MEM_IR[15:11]), .out(multiplexer_22_out), .sel(MEM_regdst));
  Multiplexer #(.select(1), .width(5), .disabled("Z"), .enable("false")) multiplexer_23 (
    .in0(multiplexer_22_out), .in1({5{1'b1}}), .out(MEM_WriteReg_num), .sel(MEM_jal));
  RAM #(.addrWidth(10), .dataWidth(32), .bus("separate"), .Select("high")) ram_1 (
    .addr(MEM_redirect[11:2]), .din(MDin), .data(ram_1_data), .str(MemWrite), .clk(CLK), .clr(RST));  // open: sel, ld
  and and_13 (and_13_out, halt, ~Go);  // AND_Gate
  MEM__WB mem_wb_1 (
    .CLK(CLK), .\同步清零_高 (RST), .\使能端_低 (and_13_out), .IR(MEM_IR), .PC(M_PC), .memdata(ram_1_data),
    .memtoreg(ex_mem_1_memtoreg_2), .Addr10(MEM_redirect[1:0]), .R1(MEM_R1data), .R2(MDin),
    .regwrite(MEM_RegWrite), .PC_4(ex_mem_1_pc_4_2), .lb(ex_mem_1_lb_2), .jal(MEM_jal), .regdst(MEM_regdst),
    .syscall(ex_mem_1_sys_2), .IR_2(WB_IR), .PC_2(WB_PC), .memdata_2(mem_wb_1_memdata_2),
    .memtoreg_2(memtoreg), .Addr(Addr10), .R1_2(WB_R1Data), .R2_2(WB_R2Data), .regwrite_2(RegWrite),
    .PC_4_2(WB_PC_4), .lb_2(lb), .jal_2(WB_jal), .regdst_2(WB_regdst), .syscall_2(WB_syscall),
    .ALUdata(MEM_redirect), .ALUdata_2(mem_wb_1_aludata_2));
  Multiplexer #(.select(1), .width(32), .disabled("Z"), .enable("false")) multiplexer_24 (
    .in0(mem_wb_1_aludata_2), .in1(mem_wb_1_memdata_2), .out(multiplexer_24_out), .sel(memtoreg));
  Multiplexer #(.select(1), .width(32), .disabled("Z"), .enable("false")) multiplexer_25 (
    .in0(multiplexer_24_out), .in1(WB_PC_4), .out(memoword), .sel(WB_jal));
  Comparator #(.width(32), .mode("twosComplement")) comparator_4 (
    .a(WB_R1Data), .b(32'h22), .eq(comparator_4_eq));  // open: gt, lt
  and and_14 (Ledout, WB_syscall, comparator_4_eq);
  and and_15 (halt, WB_syscall, ~comparator_4_eq);  // AND_Gate
  Multiplexer #(.select(1), .width(32), .disabled("Z"), .enable("false")) multiplexer_26 (
    .in0(memoword), .in1(signmemo), .out(RDin), .sel(lb));
  not not_12 (not_12_out, halt);
  assign bit_extender_4_out = {{24{memoword[7]}}, memoword[7:0]};  // Bit_Extender bit_extender_4
  assign bit_extender_5_out = {{24{memoword[15]}}, memoword[15:8]};  // Bit_Extender bit_extender_5
  assign bit_extender_6_out = {{24{memoword[23]}}, memoword[23:16]};  // Bit_Extender bit_extender_6
  assign bit_extender_7_out = {{24{memoword[31]}}, memoword[31:24]};  // Bit_Extender bit_extender_7
  Register #(.width(32), .trigger("rising"), .Select("low")) register_1 (
    .D(WB_R2Data), .en(Ledout), .Q(LedData), .clk(CLK), .clr(RST));
  Counter #(.width(16), .max('hffff), .ongoal("stay"), .trigger("rising"), .behavior("old")) counter_6 (
    .count(not_12_out), .Q(\总周期数 ), .clk(CLK));  // open: load, D, carry, clr, preset
  Multiplexer #(.select(2), .width(32), .disabled("Z"), .enable("false")) multiplexer_27 (
    .in0(bit_extender_4_out), .in1(bit_extender_5_out), .in2(bit_extender_6_out), .in3(bit_extender_7_out),
    .out(signmemo), .sel(Addr10));

  // Other names for the same wires on the sheet: 无条件分支 = EX_JMP; EX_rd[4:0] = EX_IR[15:11]; EX_rt[4:0] = EX_IR[20:16];
  //   ID_IR[5:0] = Func; OP[5:0] = ID_IR[31:26]; MEM_rd[4:0] = MEM_IR[15:11]; MEM_rt[4:0] = MEM_IR[20:16];
  //   MEM_PC[31:0] = M_PC; MEM_R2data[31:0] = MDin; WB_Din[31:0] = RDin; WB_rd[4:0] = WB_IR[15:11];
  //   WB_rt[4:0] = WB_IR[20:16]

  // Notes on the sheet:
  //   中断源
  //   时空图监测，可删除
  //   中断等待指示
  //   注意
  //   数码管输出
  //   分支预测选路
  //   分支信号类型，及对应跳转地址
  //   指令存储器
  //   控制位
  //   指令字
  //   contents of rom_1 (hex, n*v repeats v):
  //   20110001 8000c05 20110001 20120002 20130003 8000c09 20110001 20120002 20130003 8000c0d 20110001
  //   20120002 20130003 8000c11 20110001 20120002 20130003 c000d3f 20100001 20110001 118fc0 112020
  //   20020022 c 118882 12200001 8000c15 112020 20020022 c 20110001 118880 112020 20020022 c 12200001
  //   8000c1f 20110001 118fc0 112020 20020022 c 1188c3 112020 20020022 c 118903 112020 20020022 c 118903
  //   112020 20020022 c 118903 112020 20020022 c 118903 112020 20020022 c 118903 112020 20020022 c 118903
  //   112020 20020022 c 118903 112020 20020022 c 20100001 109fc0 139fc3 8021 2012000c 24160003 26100001
  //   3210000f 20080008 20090001 139900 2709825 132020 20020022 c 1094022 1500fff9 22100001 2018000f
  //   2188024 108700 20080008 20090001 139902 2709825 132021 20020022 c 1094022 1500fff9 108702 2c9b022
  //   12c00001 8000c50 4020 1084027 84400 3508ffff 82021 20020022 c 2010ffff 20110000 ae300000 22100001
  //   22310004 ae300000 22100001 22310004 ae300000 22100001 22310004 ae300000 22100001 22310004 ae300000
  //   22100001 22310004 ae300000 22100001 22310004 ae300000 22100001 22310004 ae300000 22100001 22310004
  //   ae300000 22100001 22310004 ae300000 22100001 22310004 ae300000 22100001 22310004 ae300000 22100001
  //   22310004 ae300000 22100001 22310004 ae300000 22100001 22310004 ae300000 22100001 22310004 ae300000
  //   22100001 22310004 22100001 8020 2011003c 8e130000 8e340000 274402a 11000002 ae330000 ae140000
  //   2231fffc 1611fff8 102020 20020022 c 22100004 2011003c 1611fff2 2002000a c 12*0 20020022 c 20080001
  //   20090003 20110876 112020 20020022 c 200b0008 1118804 1318804 112020 20020022 c 216bffff 1560fff9
  //   2002000a c 12*0 20020022 c 2008ffff 20117777 112020 20020022 c 200b0010 3a31ffff 112020 20020022 c
  //   216bffff 1560fffa 2002000a c 12*0 20020022 c 20090000 200b0010 34118483 20120404 118c00 129400
  //   36318281 22520404 ad310000 2328820 21290004 216bffff 1560fffb 200b0020 20090000 81310000 112020
  //   20020022 c 21290001 216bffff 1560fff9 2002000a c 12*0 20020022 c 2011000f 112020 20020022 c 2231ffff
  //   1e20fffb 2002000a c 20020022 2002000a c 12*0 20020022 c 20100000 22100001 102020 20020022 c 22100002
  //   102020 20020022 c 22100003 102020 20020022 c 22100004 102020 20020022 c 22100005 102020 20020022 c
  //   22100006 102020 20020022 c 22100007 102020 20020022 c 22100008 102020 20020022 20020022 c 3e00008
  //   流水调试日志用
  //   暂停节拍，不能为0
  //   戳工具置1进入计数暂停模式，ctrl+k时钟自动运行到对应节拍暂停
  //   ctrl+k关闭时钟连续运行，将控制位置零，进入单步调试模式调试
  //   用于暂停、插入气泡
  //   分支检测
  //   可计数暂停的时钟源
  //   OP
  //   Func
  //   rs
  //   rt
  //   rd
  //   JMP
  //   JR
  //   SignedExt
  //   OP
  //   Func
  //   R1R2使用检测
  //   Beq
  //   Bne
  //   MemToReg
  //   MemWrite
  //   AluOP
  //   sllv
  //   alu_src
  //   bgtz
  //   regwrite
  //   lb
  //   JAL
  //   RegDst
  //   Syscall
  //   为方便自动评测，需要输出流水线各段保存的PC值，注意是PC不是PC+4，另外ID段寄存器写入信息，Mem段内存写入信息也要输出
  //   用于重定向
  //   BTB表构建（具体功能见《指令流水线》）
  //   重定向---->>>
  //   重定向---->>>
  //   sllv扩展
  //   bgtz扩展
  //   rt
  //   rd
  //   重定向ALU
  //   预测结果比对
  //   本来的方法是用最高位置的0或1判断正负，但最后一步老有bug，发现是0的最高位也是0。。于是直接用比较器完美解决  
  //   WX.WriteReg#
  //   MDin是为了应付输出
  //   MEM.WriteReg#
  //   rt
  //   rd
  //   rt
  //   rd
  //   lb扩展
  //   输出或停机判断
  //   RDin是为了应付输出
endmodule
